// Digital circuit 4bit_ALU.dig as structural Verilog
module _4bit_ALU (
  input  D0,
  input  CLK,
  input  D1,
  input  D2,
  input  D3,
  input  I1,
  input  I0,
  input  NEG,
  input  Cin,
  input  SC,
  output Q0,
  output Q1,
  output Q2,
  output Q3
);

  wire nand_1_out, nand_2_out, nand_3_out, nand_4_out, nand_5_out, nand_6_out, nand_7_out, nand_8_out,
       nand_9_out, nand_10_out, nand_11_out, nand_12_out, nand_13_out, nand_14_out, nand_15_out, nand_16_out,
       nand_17_out, nand_18_out, nand_19_out, nand_20_out, nand_21_out, nand_22_out, nand_23_out,
       nand_24_out, nand_25_out, nand_26_out, nand_27_out, nand_28_out, nand_29_out, nand_30_out,
       nand_31_out, nand_32_out, nand_33_out, nand_34_out, nand_35_out, nand_36_out, nand_37_out,
       nand_38_out, nand_39_out, nand_40_out, nand_41_out, nand_42_out, nand_43_out, nand_44_out,
       nand_45_out, nand_46_out, nand_47_out, nand_48_out, nand_49_out, nand_50_out, nand_51_out,
       nand_52_out, nand_53_out, nand_54_out, nand_55_out, nand_56_out, nand_57_out, nand_58_out,
       nand_59_out, nand_60_out, nand_61_out, nand_62_out, nand_63_out, nand_64_out, nand_65_out,
       nand_66_out, nand_67_out, nand_68_out, nand_69_out, nand_70_out, nand_71_out, nand_72_out,
       nand_73_out, nand_74_out, nand_75_out, nand_76_out, nand_77_out, nand_78_out, nand_79_out,
       nand_80_out, nand_81_out, nand_82_out, nand_83_out, nand_84_out, nand_85_out, nand_86_out,
       nand_87_out, nand_88_out, nand_89_out, nand_90_out, nand_91_out, nand_92_out, nand_93_out,
       nand_94_out, nand_95_out, nand_96_out, nand_97_out, nand_98_out, nand_99_out, nand_100_out,
       nand_101_out, nand_103_out, nand_105_out, nand_107_out, nand_109_out;

  nand nand_1 (nand_1_out, D3, NEG);
  nand nand_2 (nand_2_out, D2, NEG);
  nand nand_3 (nand_3_out, D1, NEG);
  nand nand_4 (nand_4_out, D0, NEG);
  nand nand_5 (nand_5_out, D3, nand_1_out);
  nand nand_6 (nand_6_out, nand_1_out, NEG);
  nand nand_7 (nand_7_out, D2, nand_2_out);
  nand nand_8 (nand_8_out, nand_2_out, NEG);
  nand nand_9 (nand_9_out, D1, nand_3_out);
  nand nand_10 (nand_10_out, nand_3_out, NEG);
  nand nand_11 (nand_11_out, D0, nand_4_out);
  nand nand_12 (nand_12_out, nand_4_out, NEG);
  nand nand_13 (nand_13_out, nand_5_out, nand_6_out);
  nand nand_14 (nand_14_out, nand_7_out, nand_8_out);
  nand nand_15 (nand_15_out, nand_9_out, nand_10_out);
  nand nand_16 (nand_16_out, nand_11_out, nand_12_out);
  nand nand_17 (nand_17_out, Q3, nand_13_out);
  nand nand_18 (nand_18_out, Q2, nand_14_out);
  nand nand_19 (nand_19_out, Q1, nand_15_out);
  nand nand_20 (nand_20_out, Q0, nand_16_out);
  nand nand_21 (nand_21_out, Q3, nand_17_out);
  nand nand_22 (nand_22_out, nand_17_out, nand_17_out);
  nand nand_23 (nand_23_out, nand_17_out, nand_13_out);
  nand nand_24 (nand_24_out, Q2, nand_18_out);
  nand nand_25 (nand_25_out, nand_18_out, nand_18_out);
  nand nand_26 (nand_26_out, nand_18_out, nand_14_out);
  nand nand_27 (nand_27_out, Q1, nand_19_out);
  nand nand_28 (nand_28_out, nand_19_out, nand_19_out);
  nand nand_29 (nand_29_out, nand_19_out, nand_15_out);
  nand nand_30 (nand_30_out, Q0, nand_20_out);
  nand nand_31 (nand_31_out, nand_20_out, nand_20_out);
  nand nand_32 (nand_32_out, nand_20_out, nand_16_out);
  nand nand_33 (nand_33_out, nand_24_out, nand_26_out);
  nand nand_34 (nand_34_out, nand_27_out, nand_29_out);
  nand nand_35 (nand_35_out, nand_30_out, nand_32_out);
  nand nand_36 (nand_36_out, nand_21_out, nand_23_out);
  nand nand_37 (nand_37_out, nand_22_out, I1);
  nand nand_38 (nand_38_out, nand_36_out, I0);
  nand nand_39 (nand_39_out, nand_25_out, I1);
  nand nand_40 (nand_40_out, nand_33_out, I0);
  nand nand_41 (nand_41_out, nand_28_out, I1);
  nand nand_42 (nand_42_out, nand_34_out, I0);
  nand nand_43 (nand_43_out, nand_31_out, I1);
  nand nand_44 (nand_44_out, nand_35_out, I0);
  nand nand_45 (nand_45_out, nand_37_out, nand_38_out);
  nand nand_46 (nand_46_out, nand_39_out, nand_40_out);
  nand nand_47 (nand_47_out, nand_41_out, nand_42_out);
  nand nand_48 (nand_48_out, nand_43_out, nand_44_out);
  nand nand_49 (nand_49_out, nand_45_out, nand_74_out);
  nand nand_50 (nand_50_out, nand_46_out, nand_75_out);
  nand nand_51 (nand_51_out, nand_47_out, nand_76_out);
  nand nand_52 (nand_52_out, nand_48_out, Cin);
  nand nand_53 (nand_53_out, nand_45_out, nand_49_out);
  nand nand_54 (nand_54_out, nand_49_out, nand_74_out);
  nand nand_55 (nand_55_out, nand_49_out, nand_17_out);
  nand nand_56 (nand_56_out, nand_46_out, nand_50_out);
  nand nand_57 (nand_57_out, nand_50_out, nand_75_out);
  nand nand_58 (nand_58_out, nand_50_out, nand_18_out);
  nand nand_59 (nand_59_out, nand_47_out, nand_51_out);
  nand nand_60 (nand_60_out, nand_51_out, nand_76_out);
  nand nand_61 (nand_61_out, nand_51_out, nand_19_out);
  nand nand_62 (nand_62_out, nand_48_out, nand_52_out);
  nand nand_63 (nand_63_out, nand_52_out, Cin);
  nand nand_64 (nand_64_out, nand_52_out, nand_20_out);
  nand nand_65 (nand_65_out, nand_53_out, nand_54_out);
  nand nand_66 (nand_66_out, nand_55_out, SC);
  nand nand_67 (nand_67_out, nand_56_out, nand_57_out);
  nand nand_68 (nand_68_out, nand_58_out, SC);
  nand nand_69 (nand_69_out, nand_59_out, nand_60_out);
  nand nand_70 (nand_70_out, nand_61_out, SC);
  nand nand_71 (nand_71_out, nand_62_out, nand_63_out);
  nand nand_72 (nand_72_out, nand_64_out, SC);
  nand nand_73 (nand_73_out, nand_66_out, nand_66_out);
  nand nand_74 (nand_74_out, nand_68_out, nand_68_out);
  nand nand_75 (nand_75_out, nand_70_out, nand_70_out);
  nand nand_76 (nand_76_out, nand_72_out, nand_72_out);
  nand nand_77 (nand_77_out, CLK, CLK);
  nand nand_78 (nand_78_out, nand_65_out, nand_77_out);
  nand nand_79 (nand_79_out, nand_78_out, nand_77_out);
  nand nand_80 (nand_80_out, nand_67_out, nand_77_out);
  nand nand_81 (nand_81_out, nand_80_out, nand_77_out);
  nand nand_82 (nand_82_out, nand_69_out, nand_77_out);
  nand nand_83 (nand_83_out, nand_82_out, nand_77_out);
  nand nand_84 (nand_84_out, nand_71_out, nand_77_out);
  nand nand_85 (nand_85_out, nand_84_out, nand_77_out);
  nand nand_86 (nand_86_out, nand_78_out, nand_87_out);
  nand nand_87 (nand_87_out, nand_86_out, nand_79_out);
  nand nand_88 (nand_88_out, nand_80_out, nand_89_out);
  nand nand_89 (nand_89_out, nand_88_out, nand_81_out);
  nand nand_90 (nand_90_out, nand_82_out, nand_91_out);
  nand nand_91 (nand_91_out, nand_90_out, nand_83_out);
  nand nand_92 (nand_92_out, nand_84_out, nand_93_out);
  nand nand_93 (nand_93_out, nand_92_out, nand_85_out);
  nand nand_94 (nand_94_out, nand_86_out, CLK);
  nand nand_95 (nand_95_out, nand_94_out, CLK);
  nand nand_96 (nand_96_out, nand_88_out, CLK);
  nand nand_97 (nand_97_out, nand_96_out, CLK);
  nand nand_98 (nand_98_out, nand_90_out, CLK);
  nand nand_99 (nand_99_out, nand_98_out, CLK);
  nand nand_100 (nand_100_out, nand_92_out, CLK);
  nand nand_101 (nand_101_out, nand_100_out, CLK);
  nand nand_102 (Q3, nand_94_out, nand_103_out);
  nand nand_103 (nand_103_out, Q3, nand_95_out);
  nand nand_104 (Q2, nand_96_out, nand_105_out);
  nand nand_105 (nand_105_out, Q2, nand_97_out);
  nand nand_106 (Q1, nand_98_out, nand_107_out);
  nand nand_107 (nand_107_out, Q1, nand_99_out);
  nand nand_108 (Q0, nand_100_out, nand_109_out);
  nand nand_109 (nand_109_out, Q0, nand_101_out);

  // Other names for the same wires on the sheet: AL = SC

  // Notes on the sheet:
  //   CLK: Hz: 2147483647
  //   4-bit ALU
  //   Master Slave arrangement using gated D-type latches
endmodule
