// Digital circuit 74153_equiv.dig as structural Verilog
module _74153_equiv (
  input  C,
  input  S0,
  input  D,
  input  A,
  input  B,
  input  S1,
  output Fout
);

  wire nand_1_out, nand_2_out, nand_3_out, nand_4_out, nand_5_out, nand_6_out, nand_7_out, nand_8_out,
       nand_9_out, nand_10_out;

  nand nand_1 (nand_1_out, S0, S0);
  nand nand_2 (nand_2_out, S1, S1);
  nand nand_3 (nand_3_out, D, S0);
  nand nand_4 (nand_4_out, C, nand_1_out);
  nand nand_5 (nand_5_out, B, S0);
  nand nand_6 (nand_6_out, A, nand_1_out);
  nand nand_7 (nand_7_out, nand_3_out, nand_4_out);
  nand nand_8 (nand_8_out, nand_5_out, nand_6_out);
  nand nand_9 (nand_9_out, S1, nand_7_out);
  nand nand_10 (nand_10_out, nand_8_out, nand_2_out);
  nand nand_11 (Fout, nand_9_out, nand_10_out);
  LED led_1 (.in(Fout));

  // Notes on the sheet:
  //   4:1 Multiplexer (74153 equiv).
endmodule
