// Digital circuit 74219_testbed.dig as structural Verilog
module _74219_testbed (
  input  A3,
  input  A2,
  input  A1,
  input  A0,
  input  CLR,
  input  LD,
  input  nCE,
  input  nWE,
  input  DN,
  input  UP
);

  wire B0, B1, B2, B3;
  wire [3:0] _74193_1_pin15;

  Seven_Seg_Hex seven_seg_hex_1 (.d(_74193_1_pin15), .dp(1'b0));
  Seven_Seg_Hex seven_seg_hex_2 (.d({B3, B2, B1, B0}), .dp(1'b0));
  _74193 _74193_1 (
    .pin1(_74193_1_pin15[1]), .pin2(B1), .pin3(B0), .pin4(DN), .pin5(UP), .pin6(B2), .pin7(B3), .pin8(1'b0),
    .pin9(_74193_1_pin15[3]), .pin10(_74193_1_pin15[2]), .pin11(LD), .pin14(CLR), .pin15(_74193_1_pin15[0]),
    .pin16(1'b1));  // open: pin12, pin13
  _74219 _74219_1 (
    .pin1(A0), .pin2(nCE), .pin3(nWE), .pin4(B0), .pin5(_74193_1_pin15[0]), .pin6(B1),
    .pin7(_74193_1_pin15[1]), .pin8(1'b0), .pin9(_74193_1_pin15[2]), .pin10(B2), .pin11(_74193_1_pin15[3]),
    .pin12(B3), .pin13(A3), .pin14(A2), .pin15(A1), .pin16(1'b1));

  // Notes on the sheet:
  //   RAM
  //   COUNTER
endmodule
