// Digital circuit Bit_slice_ALU_4.dig as structural Verilog
module Bit_slice_ALU_4 (
  input  in_1,
  input  in_2,
  input  in_3,
  input  in_4,
  input  A_INV,
  input  B_INV,
  input  SETnCLC,
  input  clk,
  input  in_11,
  output SUM,
  output Cout
);

  wire and_1_out, button_1_out, button_2_out, button_3_out, button_4_out, button_5_out, button_6_out,
       button_7_out, button_8_out, button_9_out, d_ff_1_nq, d_ff_2_nq, d_ff_3_nq, d_ff_4_nq, d_ff_5_nq,
       d_ff_6_nq, d_ff_7_nq, d_ff_7_q, IC1_pin11, IC1_pin12, IC1_pin13, IC1_pin14, IC2_pin7, IC2_pin9,
       IC2_pin10, IC2_pin11, IC2_pin12, IC2_pin13, IC2_pin14, IC2_pin15, IC3_pin3, IC3_pin4, IC3_pin5,
       IC3_pin6, IC3_pin10, IC3_pin11, IC3_pin12, IC3_pin13, IC3_pin14, IC4_pin3, IC4_pin4, IC4_pin5,
       IC4_pin6, IC4_pin10, IC4_pin11, IC4_pin12, IC4_pin13, IC4_pin14, IC11_pin9, IC12_pin3, IC12_pin4,
       IC12_pin5, IC12_pin6, IC12_pin10, IC12_pin11, IC12_pin12, IC12_pin13, IC13_pin14, IC15_pin13,
       IC15_pin15, IC16_2_nq, IC16_nq, IC17_pin2, nand_1_out, nand_2_out, not_2_out, xor_1_out, xor_2_out,
       xor_3_out, xor_4_out;
  wire [3:0] IC5_p21, IC6_pin10, IC7_p21, IC8_pin10, IC13_pin4, IC13_pin15, IC14_pin4, IC14_pin15,
       IC15_pin14, IC16_q;

  LED led_1 (.in(IC4_pin5));
  LED led_2 (.in(IC4_pin6));
  LED led_3 (.in(IC4_pin3));
  LED led_4 (.in(IC4_pin4));
  _74161 IC4 (
    .pin1(1'b1), .pin2(clk), .pin3(IC4_pin3), .pin4(IC4_pin4), .pin5(IC4_pin5), .pin6(IC4_pin6), .pin7(1'b1),
    .pin8(1'b0), .pin9(1'b1), .pin10(IC4_pin10), .pin11(IC4_pin11), .pin12(IC4_pin12), .pin13(IC4_pin13),
    .pin14(IC4_pin14), .pin16(1'b1));  // open: pin15
  LED led_5 (.in(IC3_pin5));
  LED led_6 (.in(IC3_pin6));
  LED led_7 (.in(IC3_pin3));
  LED led_8 (.in(IC3_pin4));
  _74161 IC3 (
    .pin1(1'b1), .pin2(clk), .pin3(IC3_pin3), .pin4(IC3_pin4), .pin5(IC3_pin5), .pin6(IC3_pin6), .pin7(1'b1),
    .pin8(1'b0), .pin9(1'b1), .pin10(IC3_pin10), .pin11(IC3_pin11), .pin12(IC3_pin12), .pin13(IC3_pin13),
    .pin14(IC3_pin14), .pin15(IC4_pin10), .pin16(1'b1));
  _74164 IC17 (
    .pin1(1'b1), .pin2(IC17_pin2), .pin3(IC3_pin3), .pin4(IC3_pin4), .pin5(IC3_pin5), .pin6(IC3_pin6),
    .pin7(1'b0), .pin8(clk), .pin9(1'b1), .pin10(IC4_pin3), .pin11(IC4_pin4), .pin12(IC4_pin5),
    .pin13(IC4_pin6), .pin14(1'b1));
  // Probe INC_PC on IC3_pin10
  LED led_9 (.in(IC4_pin12));
  LED led_10 (.in(IC4_pin11));
  LED led_11 (.in(IC4_pin14));
  LED led_12 (.in(IC4_pin13));
  LED led_13 (.in(IC3_pin12));
  LED led_14 (.in(IC3_pin11));
  LED led_15 (.in(IC3_pin14));
  LED led_16 (.in(IC3_pin13));
  _74161 IC1 (
    .pin1(1'b1), .pin2(clk), .pin3(in_1), .pin4(in_2), .pin5(in_3), .pin6(in_4), .pin7(1'b1), .pin8(1'b0),
    .pin9(1'b1), .pin10(1'b1), .pin11(IC1_pin11), .pin12(IC1_pin12), .pin13(IC1_pin13), .pin14(IC1_pin14),
    .pin16(1'b1));  // open: pin15
  // ROM2K IC5: pin names not known; wires that end beside it: IC4_pin11, IC4_pin12, IC4_pin13, IC4_pin14, IC3_pin11, IC3_pin12, IC3_pin13, IC3_pin14, IC6_pin10[0], IC6_pin10[1], IC6_pin10[2], 1'b0, 1'b1, 1'b0, 1'b0, 1'b1, 1'b0, 1'b0, 1'b0, IC5_p21[3], IC5_p21[2], IC5_p21[1]
  // ROM2KB IC7: pin names not known; wires that end beside it: IC4_pin11, IC4_pin12, IC4_pin13, IC4_pin14, IC3_pin11, IC3_pin12, IC3_pin13, IC3_pin14, IC8_pin10[0], IC8_pin10[1], IC8_pin10[2], 1'b0, 1'b1, 1'b0, 1'b0, 1'b1, 1'b0, 1'b0, 1'b0, IC7_p21[3], IC7_p21[2], IC7_p21[1]
  _74138 IC2 (
    .pin1(IC1_pin14), .pin2(IC1_pin13), .pin3(IC1_pin12), .pin4(1'b0), .pin5(1'b0), .pin6(1'b1),
    .pin7(IC2_pin7), .pin8(1'b0), .pin9(IC2_pin9), .pin10(IC2_pin10), .pin11(IC2_pin11), .pin12(IC2_pin12),
    .pin13(IC2_pin13), .pin14(IC2_pin14), .pin15(IC2_pin15), .pin16(1'b1));
  _74166 IC6 (
    .pin1(1'b0), .pin2(IC5_p21[3]), .pin3(IC5_p21[2]), .pin4(IC5_p21[1]), .pin5(IC5_p21[0]), .pin6(1'b0),
    .pin7(clk), .pin8(1'b0), .pin9(1'b1), .pin10(IC6_pin10[3]), .pin11(IC6_pin10[2]), .pin12(IC6_pin10[1]),
    .pin13(IC17_pin2), .pin14(IC6_pin10[0]), .pin15(IC2_pin15), .pin16(1'b1));
  _74166 IC8 (
    .pin1(1'b0), .pin2(IC7_p21[3]), .pin3(IC7_p21[2]), .pin4(IC7_p21[1]), .pin5(IC7_p21[0]), .pin6(1'b0),
    .pin7(clk), .pin8(1'b0), .pin9(1'b1), .pin10(IC8_pin10[3]), .pin11(IC8_pin10[2]), .pin12(IC8_pin10[1]),
    .pin14(IC8_pin10[0]), .pin15(IC2_pin15), .pin16(1'b1));  // open: pin13
  LED led_17 (.in(IC5_p21[3]));
  LED led_18 (.in(IC7_p21[3]));
  not not_1 (IC3_pin10, IC2_pin7);
  LED led_19 (.in(IC5_p21[1]));
  LED led_20 (.in(IC5_p21[2]));
  LED led_21 (.in(IC7_p21[1]));
  LED led_22 (.in(IC7_p21[2]));
  LED led_23 (.in(IC6_pin10[3]));
  LED led_24 (.in(IC5_p21[0]));
  LED led_25 (.in(IC8_pin10[3]));
  LED led_26 (.in(IC7_p21[0]));
  // Probe ~LD on IC2_pin15
  LED led_27 (.in(IC2_pin15));
  LED led_28 (.in(IC2_pin14));
  LED led_29 (.in(IC2_pin13));
  LED led_30 (.in(IC2_pin12));
  LED led_31 (.in(IC2_pin11));
  LED led_32 (.in(IC2_pin10));
  LED led_33 (.in(IC2_pin9));
  LED led_34 (.in(IC2_pin7));
  not not_2 (not_2_out, IC2_pin14);
  LED led_35 (.in(IC6_pin10[1]));
  LED led_36 (.in(IC6_pin10[2]));
  LED led_37 (.in(IC8_pin10[1]));
  LED led_38 (.in(IC8_pin10[2]));
  LED led_39 (.in(IC6_pin10[0]));
  LED led_40 (.in(IC8_pin10[0]));
  Seven_Seg_Hex seven_seg_hex_1 (.d(IC5_p21), .dp(1'b0));
  Seven_Seg_Hex seven_seg_hex_2 (.d(IC7_p21));  // open: dp
  Seven_Seg_Hex seven_seg_hex_3 (.d(IC6_pin10), .dp(1'b0));
  Seven_Seg_Hex seven_seg_hex_4 (.d(IC8_pin10));  // open: dp
  and and_1 (and_1_out, SETnCLC, not_2_out);
  _7474 IC11 (
    .pin1(1'b0), .pin2(1'b0), .pin3(1'b0), .pin4(1'b0), .pin7(1'b0), .pin9(IC11_pin9), .pin10(1'b1),
    .pin11(clk), .pin12(Cout), .pin13(1'b1), .pin14(1'b1));  // open: pin5, pin6, pin8
  LED led_41 (.in(IC16_q[3]));
  D_FF IC16 (.D(IC16_nq), .C(button_1_out), .Q(IC16_q[3]), .nQ(IC16_nq));
  Button button_1 (.out(button_1_out));
  LED led_42 (.in(IC16_q[2]));
  D_FF d_ff_1 (.D(d_ff_1_nq), .C(button_2_out), .Q(IC16_q[2]), .nQ(d_ff_1_nq));
  Button button_2 (.out(button_2_out));
  LED led_43 (.in(IC16_q[1]));
  D_FF d_ff_2 (.D(d_ff_2_nq), .C(button_3_out), .Q(IC16_q[1]), .nQ(d_ff_2_nq));
  Button button_3 (.out(button_3_out));
  xor xor_1 (xor_1_out, and_1_out, IC11_pin9);
  LED led_44 (.in(IC16_q[0]));
  D_FF d_ff_3 (.D(d_ff_3_nq), .C(button_4_out), .Q(IC16_q[0]), .nQ(d_ff_3_nq));
  Button button_4 (.out(button_4_out));
  // Probe CLK on clk
  LED led_45 (.in(in_11));
  _74166 IC15 (
    .pin1(1'b0), .pin2(IC16_q[3]), .pin3(IC16_q[2]), .pin4(IC16_q[1]), .pin5(IC16_q[0]), .pin6(1'b0),
    .pin7(clk), .pin8(1'b0), .pin9(1'b1), .pin10(IC15_pin14[3]), .pin11(IC15_pin14[2]),
    .pin12(IC15_pin14[1]), .pin13(IC15_pin13), .pin14(IC15_pin14[0]), .pin15(IC15_pin15), .pin16(1'b1));
  LED led_46 (.in(IC15_pin14[3]));
  D_FF d_ff_4 (.D(d_ff_4_nq), .C(button_5_out), .Q(IC15_pin14[3]), .nQ(d_ff_4_nq));
  Button button_5 (.out(button_5_out));
  LED led_47 (.in(IC15_pin13));
  LED led_48 (.in(IC15_pin14[2]));
  D_FF d_ff_5 (.D(d_ff_5_nq), .C(button_6_out), .Q(IC15_pin14[2]), .nQ(d_ff_5_nq));
  Button button_6 (.out(button_6_out));
  LED led_49 (.in(xor_1_out));
  xor xor_2 (xor_2_out, in_11, B_INV);
  xor xor_3 (xor_3_out, IC15_pin13, A_INV);
  LED led_50 (.in(IC15_pin14[1]));
  D_FF d_ff_6 (.D(d_ff_6_nq), .C(button_7_out), .Q(IC15_pin14[1]), .nQ(d_ff_6_nq));
  Button button_7 (.out(button_7_out));
  LED led_51 (.in(IC15_pin14[0]));
  D_FF IC16_2 (.D(IC16_2_nq), .C(button_8_out), .Q(IC15_pin14[0]), .nQ(IC16_2_nq));
  Button button_8 (.out(button_8_out));
  xor xor_4 (xor_4_out, xor_3_out, xor_2_out);
  nand nand_1 (nand_1_out, xor_2_out, xor_3_out);
  Seven_Seg_Hex seven_seg_hex_5 (.d(IC16_q), .dp(1'b0));
  LED led_52 (.in(IC12_pin4));
  LED led_53 (.in(IC12_pin3));
  _74164 IC12 (
    .pin1(1'b1), .pin2(SUM), .pin3(IC12_pin3), .pin4(IC12_pin4), .pin5(IC12_pin5), .pin6(IC12_pin6),
    .pin7(1'b0), .pin8(clk), .pin9(1'b1), .pin10(IC12_pin10), .pin11(IC12_pin11), .pin12(IC12_pin12),
    .pin13(IC12_pin13), .pin14(1'b1));
  Seven_Seg_Hex seven_seg_hex_6 (.d(IC15_pin14), .dp(1'b0));
  LED led_54 (.in(IC12_pin6));
  LED led_55 (.in(IC12_pin5));
  xor xor_5 (SUM, xor_4_out, xor_1_out);
  nand nand_2 (nand_2_out, xor_4_out, xor_1_out);
  or or_1 (IC15_pin15, d_ff_7_q, IC2_pin15);
  D_FF d_ff_7 (.D(d_ff_7_nq), .C(button_9_out), .Q(d_ff_7_q), .nQ(d_ff_7_nq));
  LED led_56 (.in(IC12_pin11));
  LED led_57 (.in(IC12_pin10));
  LED led_58 (.in(IC15_pin15));
  Button button_9 (.out(button_9_out));
  LED led_59 (.in(IC12_pin13));
  LED led_60 (.in(IC12_pin12));
  nand nand_3 (Cout, nand_2_out, nand_1_out);
  _74595 IC13 (
    .pin1(IC13_pin15[2]), .pin2(IC13_pin15[1]), .pin3(IC13_pin15[0]), .pin4(IC13_pin4[3]),
    .pin5(IC13_pin4[2]), .pin6(IC13_pin4[1]), .pin7(IC13_pin4[0]), .pin8(1'b0), .pin9(SUM), .pin10(1'b1),
    .pin11(not_2_out), .pin12(clk), .pin13(1'b0), .pin14(IC13_pin14), .pin15(IC13_pin15[3]), .pin16(1'b1));
  LED led_61 (.in(IC13_pin15[2]));
  LED led_62 (.in(IC13_pin15[3]));
  LED led_63 (.in(IC13_pin15[0]));
  LED led_64 (.in(IC13_pin15[1]));
  LED led_65 (.in(IC13_pin4[2]));
  LED led_66 (.in(IC13_pin4[3]));
  LED led_67 (.in(IC13_pin4[0]));
  LED led_68 (.in(IC13_pin4[1]));
  Seven_Seg_Hex seven_seg_hex_7 (.d(IC13_pin15), .dp(1'b0));
  Seven_Seg_Hex seven_seg_hex_8 (.d(IC13_pin4), .dp(1'b0));
  LED led_69 (.in(IC14_pin15[3]));
  _74595 IC14 (
    .pin1(IC14_pin15[2]), .pin2(IC14_pin15[1]), .pin3(IC14_pin15[0]), .pin4(IC14_pin4[3]),
    .pin5(IC14_pin4[2]), .pin6(IC14_pin4[1]), .pin7(IC14_pin4[0]), .pin8(1'b0), .pin9(IC13_pin14),
    .pin10(1'b1), .pin11(not_2_out), .pin12(clk), .pin13(1'b0), .pin15(IC14_pin15[3]), .pin16(1'b1));  // open: pin14
  LED led_70 (.in(IC14_pin15[1]));
  LED led_71 (.in(IC14_pin15[2]));
  LED led_72 (.in(IC14_pin4[3]));
  LED led_73 (.in(IC14_pin15[0]));
  LED led_74 (.in(IC14_pin4[1]));
  LED led_75 (.in(IC14_pin4[2]));
  LED led_76 (.in(IC14_pin4[0]));
  Seven_Seg_Hex seven_seg_hex_9 (.d(IC14_pin15), .dp(1'b0));
  Seven_Seg_Hex seven_seg_hex_10 (.d(IC14_pin4), .dp(1'b0));

  // Notes on the sheet:
  //   Program Counter
  //   Jump Register
  //   Sequence ROM A
  //   Sequence ROM B
  //   Bit Counter
  //   Bit Slot Decoder
  //   A Register
  //   B Register
  //   Bit Slot
  //   SET CARRY LOGIC
  //   Carry FF
  //   Toggle Switch Numeric Entry
  //   Full Adder using XOR and NAND gates
  //   B
  //   A
  //   ALU Result Register
  //   Cin
  //   IC9 (XOR) IC10 (NAND)
  //   Deposit
  //   Output Display Registers
endmodule
