// Digital circuit Compute_Module_1.dig as structural Verilog
module Compute_Module_1 (
  input  SEL_PC,
  input  SEL_DATA,
  input  CLK,
  input  in_4,
  input  in_5,
  input  in_6,
  input  in_7,
  input  in_8,
  input  in_9,
  input  D0,
  input  D1,
  input  D2,
  input  D3,
  input  D4,
  input  D5,
  input  D6,
  input  D7,
  input  D8,
  input  D9,
  input  D10,
  input  D11,
  input  D12,
  input  D13,
  input  D14,
  input  D15,
  input  AL,
  output A0,
  output A1,
  output A2,
  output A3,
  output A4,
  output A5,
  output A6,
  output A7,
  output A8,
  output A9,
  output A10,
  output A11
);

  wire cm_1_1_p18, cm_1_1_p19, cm_1_1_p20, cm_1_1_p21, cm_1_1_p22, cm_1_1_p23;
  wire [3:0] cm_1_2_dout0, cm_1_2_dout7, undriven, undriven_2;

  Seven_Seg_Hex seven_seg_hex_1 (.d({A0, A1, A2, A3}), .dp(1'b0));
  Seven_Seg_Hex seven_seg_hex_2 (.d({D15, D14, D13, D12}), .dp(1'b0));
  Seven_Seg_Hex seven_seg_hex_3 (.d(cm_1_2_dout7), .dp(1'b0));
  Seven_Seg_Hex seven_seg_hex_4 (.d({A4, A5, A6, A7}), .dp(1'b0));
  Seven_Seg_Hex seven_seg_hex_5 (.d({D11, D10, D9, D8}), .dp(1'b0));
  Seven_Seg_Hex seven_seg_hex_6 (.d(cm_1_2_dout0), .dp(1'b0));
  Seven_Seg_Hex seven_seg_hex_7 (.d({A8, A9, A10, A11}), .dp(1'b0));
  Seven_Seg_Hex seven_seg_hex_8 (.d({D7, D6, D5, D4}), .dp(1'b0));
  Seven_Seg_Hex seven_seg_hex_9 (.d(undriven), .dp(1'b0));
  Seven_Seg_Hex seven_seg_hex_10 (.d({D3, D2, D1, D0}), .dp(1'b0));
  Seven_Seg_Hex seven_seg_hex_11 (.d(undriven_2), .dp(1'b0));
  // CM_1 cm_1_1: pin names not known; wires that end beside it: AL, in_4, in_5, in_6, in_7, in_8, D0, D1, D2, D3, D4, D5, D6, D7, undriven_2[0], undriven_2[1], 1'b1, cm_1_1_p18, cm_1_1_p19, cm_1_1_p20, cm_1_1_p21, cm_1_1_p22, cm_1_1_p23, SEL_PC, SEL_DATA, in_9
  CM_1 cm_1_2 (
    .Din0(D8), .Cin(cm_1_1_p22), .Dout0(cm_1_2_dout0[0]), .Dout1(cm_1_2_dout0[1]), .Dout2(cm_1_2_dout0[2]),
    .Dout3(cm_1_2_dout0[3]), .Din2(D10), .Din3(D11), .Din4(D12), .Dout4(cm_1_2_dout7[0]),
    .Dout5(cm_1_2_dout7[1]), .Dout6(cm_1_2_dout7[2]), .Dout7(cm_1_2_dout7[3]), .Din5(D13), .Din6(D14),
    .Din7(D15), .A3(A2), .A2(A3), .A1(A4), .A0(A5), .A5(A0), .A4(A1), .IR2(cm_1_1_p19), .IR3(cm_1_1_p18),
    .IR0(cm_1_1_p21), .IR1(cm_1_1_p20), .Din1(D9), .VCC(1'b1), .GND(1'b0), .CLK(CLK), .AL(AL), .A7(SEL_DATA),
    .A6(cm_1_1_p23), .PCout(SEL_PC));  // open: PCin, Sel_Data, Sel_PC, Cout

  // Notes on the sheet:
  //   CLK: Hz: 10
  //   ADDRESS
  //   DATA IN
  //   DATA OUT
endmodule
