// Digital circuit Compute_Module_2.dig as structural Verilog
module Compute_Module_2 (
  input  SEL_PC,
  input  SEL_DATA,
  input  CLK,
  input  in_4,
  input  in_5,
  input  D0,
  input  D1,
  input  D2,
  input  D3,
  input  D4,
  input  D5,
  input  D6,
  input  D7,
  input  D8,
  input  D9,
  input  D10,
  input  D11,
  input  D12,
  input  D13,
  input  D14,
  input  D15,
  input  in_34,
  input  in_35,
  output A0,
  output A1,
  output A2,
  output A3,
  output A4,
  output A5,
  output A6,
  output A7,
  output A8,
  output A9,
  output A10,
  output A11
);

  wire AC7, AL, AR0, AR1, AR2, AR3, CM_L_p18, CM_L_p19, CM_L_p20, CM_L_p21, CM_L_p22, CM_L_p23, CO,
       diodebackward_1_out, diodebackward_5_out, diodebackward_7_out, diodebackward_9_out,
       diodebackward_27_out, EH, EL, IC18_pin9, IC18_pin10, IC18_pin11, IC18_pin12, IC18_pin13, IC18_pin14,
       IC18_pin15, IC19_pin7, IC19_pin9, IC19_pin10, IC19_pin11, IC19_pin12, IC19_pin13, IC19_pin14,
       IC19_pin15, IC20_2_pin16, IC20_2_pin17, IC20_2_pin18, IC20_pin7, IC20_pin9, IC20_pin12, IC20_pin13,
       IC20_pin14, IC20_pin15, IC22_pin7, IR0, IR1, IR2, IR3, IR4, IR5, IR6, IX, nAE, nBF, nDE, nIE, nJMP,
       nLD, nOE, nOL, not_1_out, not_2_out, nPH, nPL, nWE, nXL, nYL, pullup_6_out, pullup_8_out;
  wire [2:0] _74541_1_pin8;
  wire [3:0] _74541_1_pin5, CM_H_dout0, CM_H_dout7;

  _74573 _74573_1 (
    .pin1(1'b0), .pin2(D8), .pin3(D9), .pin4(D10), .pin5(D11), .pin6(D12), .pin7(D13), .pin8(D14),
    .pin9(D15), .pin10(1'b0), .pin11(CLK), .pin12(1'b0), .pin13(IR6), .pin14(IR5), .pin15(IR4), .pin16(IR3),
    .pin17(IR2), .pin18(IR1), .pin19(IR0), .pin20(1'b1));
  _74153 IC22 (
    .pin1(nJMP), .pin2(CO), .pin3(1'b0), .pin4(IR4), .pin5(IR3), .pin6(IR2), .pin7(IC22_pin7), .pin8(1'b0),
    .pin10(1'b1), .pin11(1'b1), .pin12(1'b1), .pin13(1'b1), .pin14(AC7), .pin15(1'b1), .pin16(1'b1));  // open: pin9
  _74139 IC21 (
    .pin1(1'b0), .pin2(IR0), .pin3(IR1), .pin4(nDE), .pin5(nOE), .pin6(nAE), .pin7(nIE), .pin8(1'b0),
    .pin12(nBF), .pin13(IR2), .pin14(IR3), .pin15(IR4), .pin16(1'b1));  // open: pin9, pin10, pin11
  _74138 IC20 (
    .pin1(IR2), .pin2(IR3), .pin3(IR4), .pin4(1'b0), .pin5(1'b0), .pin6(1'b1), .pin7(IC20_pin7), .pin8(1'b0),
    .pin9(IC20_pin9), .pin10(nYL), .pin11(nXL), .pin12(IC20_pin12), .pin13(IC20_pin13), .pin14(IC20_pin14),
    .pin15(IC20_pin15), .pin16(1'b1));
  _74138 IC18 (
    .pin1(IR4), .pin2(IR5), .pin3(IR6), .pin4(1'b0), .pin5(1'b0), .pin6(1'b1), .pin7(nJMP), .pin8(1'b0),
    .pin9(IC18_pin9), .pin10(IC18_pin10), .pin11(IC18_pin11), .pin12(IC18_pin12), .pin13(IC18_pin13),
    .pin14(IC18_pin14), .pin15(IC18_pin15), .pin16(1'b1));
  _74138 IC19 (
    .pin1(IR4), .pin2(IR5), .pin3(IR6), .pin4(1'b0), .pin5(1'b0), .pin6(1'b0), .pin7(IC19_pin7), .pin8(1'b0),
    .pin9(IC19_pin9), .pin10(IC19_pin10), .pin11(IC19_pin11), .pin12(IC19_pin12), .pin13(IC19_pin13),
    .pin14(IC19_pin14), .pin15(IC19_pin15), .pin16(1'b1));
  DiodeBackward diodebackward_1 (.in(IC20_pin15), .out(diodebackward_1_out));
  DiodeBackward diodebackward_2 (.in(IC20_pin14), .out(diodebackward_1_out));
  DiodeBackward diodebackward_3 (.in(IC20_pin13), .out(diodebackward_1_out));
  DiodeBackward diodebackward_4 (.in(IC20_pin12), .out(diodebackward_1_out));
  DiodeBackward diodebackward_5 (.in(IR6), .out(diodebackward_5_out));
  DiodeBackward diodebackward_6 (.in(nJMP), .out(diodebackward_5_out));
  not not_1 (not_1_out, IC22_pin7);
  PullUp pullup_1 (.out(diodebackward_1_out));
  DiodeBackward diodebackward_7 (.in(IC20_pin9), .out(diodebackward_7_out));
  DiodeBackward diodebackward_8 (.in(IC20_pin7), .out(diodebackward_7_out));
  PullUp pullup_2 (.out(diodebackward_5_out));
  DiodeBackward diodebackward_9 (.in(IC18_pin15), .out(diodebackward_9_out));
  DiodeBackward diodebackward_10 (.in(IC18_pin14), .out(diodebackward_9_out));
  DiodeBackward diodebackward_11 (.in(IC18_pin13), .out(diodebackward_9_out));
  DiodeBackward diodebackward_12 (.in(IC18_pin11), .out(diodebackward_9_out));
  PullUp pullup_3 (.out(diodebackward_7_out));
  PullUp pullup_4 (.out(EL));
  DiodeBackward diodebackward_13 (.in(IC20_pin14), .out(EL));
  DiodeBackward diodebackward_14 (.in(IC20_pin12), .out(EL));
  DiodeBackward diodebackward_15 (.in(IC20_pin7), .out(EL));
  PullUp pullup_5 (.out(diodebackward_9_out));
  PullUp pullup_6 (.out(pullup_6_out));
  DiodeBackward diodebackward_16 (.in(IC18_pin15), .out(pullup_6_out));
  DiodeBackward diodebackward_17 (.in(IC18_pin13), .out(pullup_6_out));
  DiodeBackward diodebackward_18 (.in(IC18_pin12), .out(pullup_6_out));
  DiodeBackward diodebackward_19 (.in(IC18_pin11), .out(pullup_6_out));
  DiodeBackward diodebackward_20 (.in(IC18_pin9), .out(pullup_6_out));
  or or_1 (nPH, nJMP, nBF);
  PullUp pullup_7 (.out(EH));
  DiodeBackward diodebackward_21 (.in(IC20_pin13), .out(EH));
  DiodeBackward diodebackward_22 (.in(IC20_pin12), .out(EH));
  DiodeBackward diodebackward_23 (.in(IC20_pin7), .out(EH));
  PullUp pullup_8 (.out(pullup_8_out));
  DiodeBackward diodebackward_24 (.in(IC18_pin13), .out(pullup_8_out));
  DiodeBackward diodebackward_25 (.in(IC18_pin12), .out(pullup_8_out));
  DiodeBackward diodebackward_26 (.in(IC18_pin10), .out(pullup_8_out));
  DiodeBackward diodebackward_27 (.in(IC18_pin10), .out(diodebackward_27_out));
  DiodeBackward diodebackward_28 (.in(IC18_pin9), .out(diodebackward_27_out));
  PullUp pullup_9 (.out(diodebackward_27_out));
  _74540 IC20_2 (
    .pin1(1'b0), .pin2(1'b0), .pin3(1'b0), .pin4(1'b0), .pin5(diodebackward_27_out), .pin6(pullup_8_out),
    .pin7(pullup_6_out), .pin8(diodebackward_9_out), .pin9(diodebackward_5_out), .pin10(1'b0), .pin11(AL),
    .pin12(AR3), .pin13(AR2), .pin14(AR1), .pin15(AR0), .pin16(IC20_2_pin16), .pin17(IC20_2_pin17),
    .pin18(IC20_2_pin18), .pin19(1'b0), .pin20(1'b1));
  DiodeBackward diodebackward_29 (.in(not_1_out), .out(nPL));
  DiodeBackward diodebackward_30 (.in(nPH), .out(nPL));
  PullUp pullup_10 (.out(nPL));
  not not_2 (not_2_out, IC18_pin9);
  not not_3 (IX, IC20_pin7);
  or or_2 (nOL, diodebackward_7_out, not_2_out);
  or or_3 (nLD, diodebackward_1_out, not_2_out);
  or or_4 (nWE, CLK, IC18_pin9);
  Seven_Seg_Hex seven_seg_hex_1 (.d({A11, A10, A9, A8}), .dp(1'b0));
  Seven_Seg_Hex seven_seg_hex_2 (.d({D15, D14, D13, D12}), .dp(1'b0));
  Seven_Seg_Hex seven_seg_hex_3 (.d(CM_H_dout7), .dp(1'b0));
  Seven_Seg_Hex seven_seg_hex_4 (.d({A7, A6, A5, A4}), .dp(1'b0));
  Seven_Seg_Hex seven_seg_hex_5 (.d({D11, D10, D9, D8}), .dp(1'b0));
  Seven_Seg_Hex seven_seg_hex_6 (.d(CM_H_dout0), .dp(1'b0));
  Seven_Seg_Hex seven_seg_hex_7 (.d({A3, A2, A1, A0}), .dp(1'b0));
  Seven_Seg_Hex seven_seg_hex_8 (.d({D7, D6, D5, D4}), .dp(1'b0));
  Seven_Seg_Hex seven_seg_hex_9 (.d({AC7, _74541_1_pin8}), .dp(1'b0));
  Seven_Seg_Hex seven_seg_hex_10 (.d({D3, D2, D1, D0}), .dp(1'b0));
  Seven_Seg_Hex seven_seg_hex_11 (.d(_74541_1_pin5), .dp(1'b0));
  // CM_1 CM_L: pin names not known; wires that end beside it: AL, AR3, AR2, AR1, AR0, in_4, D0, D1, D2, D3, D4, D5, D6, D7, _74541_1_pin5[0], _74541_1_pin5[1], 1'b1, CM_L_p18, CM_L_p19, CM_L_p20, CM_L_p21, CM_L_p22, CM_L_p23, SEL_PC, SEL_DATA, in_5
  CM_1 CM_H (
    .Din0(D8), .Cin(CM_L_p22), .Dout0(CM_H_dout0[0]), .Dout1(CM_H_dout0[1]), .Dout2(CM_H_dout0[2]),
    .Dout3(CM_H_dout0[3]), .Din2(D10), .Din3(D11), .Din4(D12), .Dout4(CM_H_dout7[0]), .Dout5(CM_H_dout7[1]),
    .Dout6(CM_H_dout7[2]), .Dout7(CM_H_dout7[3]), .Din5(D13), .Din6(D14), .Din7(D15), .A3(A9), .A2(A8),
    .A1(A7), .PCin(CO), .A0(A6), .A5(A11), .A4(A10), .IR2(CM_L_p19), .IR3(CM_L_p18), .IR0(CM_L_p21),
    .IR1(CM_L_p20), .Din1(D9), .VCC(1'b1), .GND(1'b0), .CLK(CLK), .AL(AL), .A7(SEL_DATA), .A6(CM_L_p23),
    .PCout(SEL_PC));  // open: Sel_Data, Sel_PC, Cout
  _74541 _74541_1 (
    .pin1(nWE), .pin2(_74541_1_pin5[0]), .pin3(_74541_1_pin5[1]), .pin4(_74541_1_pin5[2]),
    .pin5(_74541_1_pin5[3]), .pin6(_74541_1_pin8[0]), .pin7(_74541_1_pin8[1]), .pin8(_74541_1_pin8[2]),
    .pin9(AC7), .pin10(1'b0), .pin11(D7), .pin12(D6), .pin13(D5), .pin14(D4), .pin15(D3), .pin16(D2),
    .pin17(D1), .pin18(D0), .pin19(nWE), .pin20(1'b1));
  _74541 _74541_2 (
    .pin1(nWE), .pin2(CM_H_dout0[0]), .pin3(CM_H_dout0[1]), .pin4(CM_H_dout0[2]), .pin5(CM_H_dout0[3]),
    .pin6(CM_H_dout7[0]), .pin7(CM_H_dout7[1]), .pin8(CM_H_dout7[2]), .pin9(CM_H_dout7[3]), .pin10(1'b0),
    .pin11(D15), .pin12(D14), .pin13(D13), .pin14(D12), .pin15(D11), .pin16(D10), .pin17(D9), .pin18(D8),
    .pin19(nWE), .pin20(1'b1));
  // A623308A RAM_L: pin names not known; wires that end beside it: 1'b0, A7, A6, A5, A4, A3, A2, A1, A0, D0, D1, 1'b1, nWE, A8, A9, A11, in_35, A10, in_34, D7
  // A623308A RAM_H: pin names not known; wires that end beside it: D2, 1'b0, 1'b0, A7, A6, A5, A4, A3, A2, A1, A0, D8, D9, D10, 1'b0, D3, 1'b1, nWE, A8, A9, A11, nOE, A10, 1'b1, D15

  // Other names for the same wires on the sheet: CLK1 = CLK

  // Notes on the sheet:
  //   CLK: Hz: 10
  //   CONTROL UNIT
  //   16-bit Jump Detector
  //   LOAD
  //   AND
  //   OR
  //   XOR
  //   ADD
  //   SUB
  //   STORE
  //   JMP
  //   ~W
  //   INST 8
  //   INST 9
  //   INST A
  //   INST B
  //   INST C
  //   INST D
  //   INST E
  //   INST F
  //   ADDRESS
  //   DATA IN
  //   DATA OUT
  //   BUFFER TO BUS
endmodule
