// Digital circuit DTL_3to8_decoder.dig as structural Verilog
module DTL_3to8_decoder (
  input  A,
  input  B,
  input  C,
  input  nE,
  output out_1,
  output out_2,
  output out_3,
  output out_4,
  output out_5,
  output out_6,
  output out_7,
  output out_8
);

  wire not_1_out, not_2_out, not_3_out, not_4_out, pullup_1_out, pullup_2_out, pullup_3_out, pullup_4_out,
       pullup_5_out, pullup_6_out, pullup_7_out, pullup_8_out;

  not not_1 (not_1_out, A);
  not not_2 (not_2_out, B);
  not not_3 (not_3_out, C);
  not not_4 (not_4_out, nE);
  PullUp pullup_1 (.out(pullup_1_out));
  DiodeBackward diodebackward_1 (.in(not_1_out), .out(pullup_1_out));
  DiodeBackward diodebackward_2 (.in(not_2_out), .out(pullup_1_out));
  DiodeBackward diodebackward_3 (.in(not_3_out), .out(pullup_1_out));
  DiodeBackward diodebackward_4 (.in(not_4_out), .out(pullup_1_out));
  PullUp pullup_2 (.out(pullup_2_out));
  DiodeBackward diodebackward_5 (.in(A), .out(pullup_2_out));
  DiodeBackward diodebackward_6 (.in(not_2_out), .out(pullup_2_out));
  DiodeBackward diodebackward_7 (.in(not_3_out), .out(pullup_2_out));
  DiodeBackward diodebackward_8 (.in(not_4_out), .out(pullup_2_out));
  PullUp pullup_3 (.out(pullup_3_out));
  DiodeBackward diodebackward_9 (.in(not_1_out), .out(pullup_3_out));
  DiodeBackward diodebackward_10 (.in(B), .out(pullup_3_out));
  DiodeBackward diodebackward_11 (.in(not_3_out), .out(pullup_3_out));
  DiodeBackward diodebackward_12 (.in(not_4_out), .out(pullup_3_out));
  PullUp pullup_4 (.out(pullup_4_out));
  DiodeBackward diodebackward_13 (.in(A), .out(pullup_4_out));
  DiodeBackward diodebackward_14 (.in(B), .out(pullup_4_out));
  DiodeBackward diodebackward_15 (.in(not_3_out), .out(pullup_4_out));
  DiodeBackward diodebackward_16 (.in(not_4_out), .out(pullup_4_out));
  PullUp pullup_5 (.out(pullup_5_out));
  DiodeBackward diodebackward_17 (.in(not_1_out), .out(pullup_5_out));
  DiodeBackward diodebackward_18 (.in(not_2_out), .out(pullup_5_out));
  DiodeBackward diodebackward_19 (.in(C), .out(pullup_5_out));
  DiodeBackward diodebackward_20 (.in(not_4_out), .out(pullup_5_out));
  PullUp pullup_6 (.out(pullup_6_out));
  DiodeBackward diodebackward_21 (.in(A), .out(pullup_6_out));
  DiodeBackward diodebackward_22 (.in(not_2_out), .out(pullup_6_out));
  DiodeBackward diodebackward_23 (.in(C), .out(pullup_6_out));
  DiodeBackward diodebackward_24 (.in(not_4_out), .out(pullup_6_out));
  PullUp pullup_7 (.out(pullup_7_out));
  DiodeBackward diodebackward_25 (.in(not_1_out), .out(pullup_7_out));
  DiodeBackward diodebackward_26 (.in(B), .out(pullup_7_out));
  DiodeBackward diodebackward_27 (.in(C), .out(pullup_7_out));
  DiodeBackward diodebackward_28 (.in(not_4_out), .out(pullup_7_out));
  PullUp pullup_8 (.out(pullup_8_out));
  DiodeBackward diodebackward_29 (.in(A), .out(pullup_8_out));
  DiodeBackward diodebackward_30 (.in(B), .out(pullup_8_out));
  DiodeBackward diodebackward_31 (.in(C), .out(pullup_8_out));
  DiodeBackward diodebackward_32 (.in(not_4_out), .out(pullup_8_out));
  not not_5 (out_8, pullup_1_out);
  not not_6 (out_7, pullup_2_out);
  not not_7 (out_6, pullup_3_out);
  not not_8 (out_5, pullup_4_out);
  not not_9 (out_4, pullup_5_out);
  not not_10 (out_3, pullup_6_out);
  not not_11 (out_2, pullup_7_out);
  not not_12 (out_1, pullup_8_out);

  // Notes on the sheet:
  //   3 to 8 line decoder
endmodule
