// Digital circuit DTL_3to8_decoder_2.dig as structural Verilog
module DTL_3to8_decoder_2 (
  input  A,
  input  B,
  input  C,
  input  nE,
  input  S0,
  input  S1,
  input  A0,
  input  nE1,
  input  A1,
  input  A2,
  input  A3,
  input  nE2,
  input  B1,
  input  B2,
  input  B3,
  input  B0,
  input  A_2,
  input  B_2,
  input  Cin,
  input  in_33,
  input  in_34,
  input  in_35,
  input  in_36,
  input  D,
  input  CLK,
  input  CLK_2,
  input  D_2,
  input  CLK_3,
  input  nSET,
  input  nRESET,
  input  DATA,
  input  nSET_2,
  input  nRESET_2,
  input  B_3,
  input  A_3,
  input  I0,
  input  I1,
  input  I2,
  input  I3,
  input  Cin_2,
  input  I0_2,
  input  I1_2,
  input  I2_2,
  input  I3_2,
  input  A_4,
  input  B_4,
  input  Cin_3,
  input  I0_3,
  input  I1_3,
  input  S0_2,
  input  S1_2,
  input  D0,
  input  S2,
  input  D1,
  input  D2,
  input  D3,
  input  D4,
  input  D5,
  input  D6,
  input  D7,
  input  CLK_4,
  input  nRES,
  input  CLK_5,
  input  nRES_2,
  input  Din,
  input  CLK_6,
  input  nRES_3,
  input  Din_2,
  output out_1,
  output out_2,
  output out_3,
  output out_4,
  output out_5,
  output out_6,
  output out_7,
  output out_8,
  output out_17,
  output out_18,
  output CARRY,
  output SUM,
  output out_32,
  output Q,
  output nQ,
  output Q_2,
  output nQ_2,
  output Q_3,
  output nQ_3,
  output Q_4,
  output nQ_4,
  output out_58,
  output out_64,
  output CARRY_2,
  output Fout,
  output out_78
);

  wire diodebackward_1_out, diodebackward_3_out, diodebackward_6_out, diodebackward_9_out,
       diodebackward_44_out, diodebackward_46_out, diodebackward_73_out, diodebackward_75_out,
       diodebackward_78_out, diodebackward_81_out, diodebackward_116_out, diodebackward_118_out,
       diodebackward_121_out, diodebackward_123_out, diodebackward_126_out, diodebackward_129_out,
       diodebackward_132_out, diodebackward_134_out, diodebackward_149_out, diodebackward_153_out,
       diodebackward_157_out, diodebackward_161_out, diodebackward_165_out, diodebackward_169_out,
       diodebackward_173_out, diodebackward_177_out, diodebackward_185_out, diodebackward_187_out,
       diodebackward_190_out, diodebackward_193_out, diodebackward_204_out, diodebackward_206_out,
       diodebackward_224_out, diodebackward_227_out, diodebackward_230_out, diodebackward_233_out,
       diodebackward_236_out, diodebackward_238_out, diodebackward_240_out, diodebackward_242_out,
       diodebackward_245_out, diodebackward_247_out, diodebackward_249_out, diodebackward_258_out,
       diodebackward_285_out, diodebackward_287_out, diodebackward_293_out, diodebackward_295_out,
       diodebackward_298_out, diodebackward_301_out, diodebackward_319_out, diodebackward_321_out,
       diodebackward_323_out, diodebackward_325_out, diodebackward_327_out, diodebackward_329_out,
       diodebackward_331_out, diodebackward_333_out, diodebackward_336_out, diodebackward_340_out,
       diodebackward_351_out, diodebackward_353_out, diodebackward_355_out, diodebackward_357_out,
       diodebackward_360_out, diodebackward_363_out, diodebackward_366_out, diodebackward_380_out,
       diodebackward_383_out, diodebackward_391_out, diodebackward_393_out, diodebackward_396_out,
       diodebackward_399_out, diodebackward_402_out, diodebackward_404_out, diodebackward_407_out,
       diodebackward_409_out, diodebackward_412_out, diodebackward_415_out, diodebackward_418_out,
       diodebackward_420_out, diodebackward_439_out, diodebackward_441_out, diodebackward_444_out,
       diodebackward_447_out, diodebackward_450_out, diodebackward_452_out, diodebackward_455_out,
       diodebackward_457_out, diodebackward_460_out, diodebackward_463_out, diodebackward_466_out,
       diodebackward_468_out, diodebackward_487_out, diodebackward_489_out, diodebackward_492_out,
       diodebackward_495_out, diodebackward_498_out, diodebackward_500_out, not_1_out, not_2_out, not_3_out,
       not_4_out, not_5_out, not_6_out, not_7_out, not_8_out, not_9_out, not_10_out, not_11_out, not_12_out,
       not_13_out, not_14_out, not_15_out, not_17_out, not_19_out, not_20_out, not_21_out, not_22_out,
       not_24_out, not_25_out, not_26_out, not_27_out, not_28_out, not_29_out, not_30_out, not_31_out,
       not_32_out, not_42_out, not_43_out, not_44_out, not_45_out, not_46_out, not_48_out, not_49_out,
       not_50_out, not_51_out, not_52_out, not_53_out, not_54_out, not_55_out, not_56_out, not_57_out,
       not_58_out, not_59_out, not_60_out, not_61_out, not_62_out, not_63_out, not_64_out, not_65_out,
       not_66_out, not_70_out, not_71_out, not_72_out, not_73_out, not_75_out, not_76_out, not_77_out,
       not_78_out, not_79_out, not_80_out, not_81_out, not_82_out, not_83_out, not_84_out, not_85_out,
       not_86_out, not_87_out, not_88_out, not_89_out, not_90_out, not_91_out, not_92_out, not_93_out,
       not_94_out, not_97_out, not_101_out, not_102_out, not_103_out, not_104_out, not_105_out, not_107_out,
       not_108_out, not_109_out, not_110_out, not_111_out, not_112_out, not_113_out, not_114_out,
       not_115_out, not_116_out, not_117_out, not_118_out, not_119_out, not_120_out, not_121_out,
       not_122_out, not_123_out, not_128_out, not_129_out, not_131_out, not_132_out, not_133_out,
       not_135_out, not_136_out, not_137_out, not_138_out, not_142_out, not_143_out, not_144_out,
       not_145_out, not_146_out, not_147_out, not_148_out, not_149_out, not_153_out, not_154_out,
       not_155_out, not_156_out, not_157_out, not_159_out, not_160_out, not_161_out, not_162_out,
       not_163_out, not_165_out, not_166_out, not_167_out, not_168_out, not_169_out, not_171_out,
       not_172_out, not_173_out, not_174_out, not_175_out, not_177_out, not_178_out, not_179_out,
       not_180_out, not_181_out, not_183_out, not_184_out, not_185_out, not_186_out, not_187_out,
       not_189_out, not_190_out, not_191_out, not_192_out, not_193_out, not_195_out, pullup_1_out,
       pullup_2_out, pullup_3_out, pullup_4_out, pullup_5_out, pullup_6_out, pullup_7_out, pullup_8_out,
       pullup_15_out, pullup_16_out, pullup_17_out, pullup_18_out, pullup_19_out, pullup_20_out,
       pullup_21_out, pullup_26_out, pullup_27_out, pullup_28_out, pullup_29_out, pullup_30_out,
       pullup_31_out, pullup_32_out, pullup_33_out, pullup_42_out, pullup_43_out, pullup_44_out,
       pullup_45_out, pullup_54_out, pullup_55_out, pullup_56_out, pullup_63_out, pullup_64_out,
       pullup_65_out, pullup_66_out, pullup_67_out, pullup_68_out, pullup_80_out, pullup_81_out,
       pullup_82_out, pullup_84_out, pullup_85_out, pullup_86_out, pullup_87_out, pullup_88_out,
       pullup_89_out, pullup_90_out, pullup_91_out, pullup_94_out, pullup_95_out, pullup_100_out,
       pullup_101_out, pullup_102_out, pullup_103_out, pullup_104_out, pullup_105_out, pullup_106_out,
       pullup_117_out, pullup_118_out, pullup_119_out, pullup_120_out, pullup_128_out, pullup_129_out,
       pullup_130_out, pullup_131_out, pullup_132_out, pullup_133_out, pullup_148_out, pullup_149_out,
       pullup_150_out, pullup_151_out, pullup_152_out, pullup_153_out, pullup_166_out, pullup_167_out,
       pullup_168_out, pullup_169_out, pullup_170_out, pullup_171_out;
  wire [3:0] not_47_out, not_74_out, not_170_out, not_176_out;

  not not_1 (not_1_out, S0_2);
  not not_2 (not_2_out, S1_2);
  not not_3 (not_3_out, S2);
  DiodeBackward diodebackward_1 (.in(not_7_out), .out(diodebackward_1_out));
  DiodeBackward diodebackward_2 (.in(not_5_out), .out(diodebackward_1_out));
  DiodeBackward diodebackward_3 (.in(not_4_out), .out(diodebackward_3_out));
  DiodeBackward diodebackward_4 (.in(CLK_4), .out(diodebackward_3_out));
  DiodeBackward diodebackward_5 (.in(nRES), .out(diodebackward_3_out));
  DiodeBackward diodebackward_6 (.in(not_5_out), .out(diodebackward_6_out));
  DiodeBackward diodebackward_7 (.in(CLK_4), .out(diodebackward_6_out));
  DiodeBackward diodebackward_8 (.in(not_7_out), .out(diodebackward_6_out));
  DiodeBackward diodebackward_9 (.in(not_6_out), .out(diodebackward_9_out));
  DiodeBackward diodebackward_10 (.in(not_17_out), .out(diodebackward_9_out));
  DiodeBackward diodebackward_11 (.in(nRES), .out(diodebackward_9_out));
  PullUp pullup_1 (.out(pullup_1_out));
  DiodeBackward diodebackward_12 (.in(not_1_out), .out(pullup_1_out));
  DiodeBackward diodebackward_13 (.in(not_2_out), .out(pullup_1_out));
  DiodeBackward diodebackward_14 (.in(not_3_out), .out(pullup_1_out));
  DiodeBackward diodebackward_15 (.in(D0), .out(pullup_1_out));
  PullUp pullup_2 (.out(pullup_2_out));
  DiodeBackward diodebackward_16 (.in(S0_2), .out(pullup_2_out));
  DiodeBackward diodebackward_17 (.in(not_2_out), .out(pullup_2_out));
  DiodeBackward diodebackward_18 (.in(not_3_out), .out(pullup_2_out));
  DiodeBackward diodebackward_19 (.in(D1), .out(pullup_2_out));
  PullUp pullup_3 (.out(pullup_3_out));
  DiodeBackward diodebackward_20 (.in(not_1_out), .out(pullup_3_out));
  DiodeBackward diodebackward_21 (.in(S1_2), .out(pullup_3_out));
  DiodeBackward diodebackward_22 (.in(not_3_out), .out(pullup_3_out));
  DiodeBackward diodebackward_23 (.in(D2), .out(pullup_3_out));
  PullUp pullup_4 (.out(pullup_4_out));
  DiodeBackward diodebackward_24 (.in(S0_2), .out(pullup_4_out));
  DiodeBackward diodebackward_25 (.in(S1_2), .out(pullup_4_out));
  DiodeBackward diodebackward_26 (.in(not_3_out), .out(pullup_4_out));
  DiodeBackward diodebackward_27 (.in(D3), .out(pullup_4_out));
  PullUp pullup_5 (.out(pullup_5_out));
  DiodeBackward diodebackward_28 (.in(not_1_out), .out(pullup_5_out));
  DiodeBackward diodebackward_29 (.in(not_2_out), .out(pullup_5_out));
  DiodeBackward diodebackward_30 (.in(S2), .out(pullup_5_out));
  DiodeBackward diodebackward_31 (.in(D4), .out(pullup_5_out));
  PullUp pullup_6 (.out(pullup_6_out));
  DiodeBackward diodebackward_32 (.in(S0_2), .out(pullup_6_out));
  DiodeBackward diodebackward_33 (.in(not_2_out), .out(pullup_6_out));
  DiodeBackward diodebackward_34 (.in(S2), .out(pullup_6_out));
  DiodeBackward diodebackward_35 (.in(D5), .out(pullup_6_out));
  PullUp pullup_7 (.out(pullup_7_out));
  DiodeBackward diodebackward_36 (.in(not_1_out), .out(pullup_7_out));
  DiodeBackward diodebackward_37 (.in(S1_2), .out(pullup_7_out));
  DiodeBackward diodebackward_38 (.in(S2), .out(pullup_7_out));
  DiodeBackward diodebackward_39 (.in(D6), .out(pullup_7_out));
  PullUp pullup_8 (.out(pullup_8_out));
  DiodeBackward diodebackward_40 (.in(S0_2), .out(pullup_8_out));
  DiodeBackward diodebackward_41 (.in(S1_2), .out(pullup_8_out));
  DiodeBackward diodebackward_42 (.in(S2), .out(pullup_8_out));
  DiodeBackward diodebackward_43 (.in(D7), .out(pullup_8_out));
  PullUp pullup_9 (.out(diodebackward_1_out));
  not not_4 (not_4_out, diodebackward_1_out);
  PullUp pullup_10 (.out(diodebackward_3_out));
  not not_5 (not_5_out, diodebackward_3_out);
  PullUp pullup_11 (.out(diodebackward_6_out));
  not not_6 (not_6_out, diodebackward_6_out);
  PullUp pullup_12 (.out(diodebackward_9_out));
  not not_7 (not_7_out, diodebackward_9_out);
  not not_8 (not_8_out, pullup_1_out);
  not not_9 (not_9_out, pullup_2_out);
  not not_10 (not_10_out, pullup_3_out);
  not not_11 (not_11_out, pullup_4_out);
  not not_12 (not_12_out, pullup_5_out);
  not not_13 (not_13_out, pullup_6_out);
  not not_14 (not_14_out, pullup_7_out);
  not not_15 (not_15_out, pullup_8_out);
  Seven_Seg_Hex seven_seg_hex_1 (.d(not_47_out), .dp(1'b0));
  DiodeBackward diodebackward_44 (.in(not_5_out), .out(diodebackward_44_out));
  DiodeBackward diodebackward_45 (.in(not_17_out), .out(diodebackward_44_out));
  DiodeBackward diodebackward_46 (.in(not_47_out[0]), .out(diodebackward_46_out));
  DiodeBackward diodebackward_47 (.in(not_6_out), .out(diodebackward_46_out));
  DiodeBackward diodebackward_48 (.in(nRES), .out(diodebackward_46_out));
  PullUp pullup_13 (.out(diodebackward_44_out));
  not not_16 (not_47_out[0], diodebackward_44_out);
  PullUp pullup_14 (.out(diodebackward_46_out));
  not not_17 (not_17_out, diodebackward_46_out);
  PullUp pullup_15 (.out(pullup_15_out));
  DiodeBackward diodebackward_49 (.in(not_8_out), .out(pullup_15_out));
  not not_18 (out_78, pullup_15_out);
  DiodeBackward diodebackward_50 (.in(not_9_out), .out(pullup_15_out));
  DiodeBackward diodebackward_51 (.in(not_10_out), .out(pullup_15_out));
  DiodeBackward diodebackward_52 (.in(not_11_out), .out(pullup_15_out));
  DiodeBackward diodebackward_53 (.in(not_12_out), .out(pullup_15_out));
  DiodeBackward diodebackward_54 (.in(not_13_out), .out(pullup_15_out));
  DiodeBackward diodebackward_55 (.in(not_14_out), .out(pullup_15_out));
  DiodeBackward diodebackward_56 (.in(not_15_out), .out(pullup_15_out));
  LED Q0 (.in(not_47_out[0]));
  PullUp pullup_16 (.out(pullup_16_out));
  DiodeBackward diodebackward_57 (.in(not_22_out), .out(pullup_16_out));
  DiodeBackward diodebackward_58 (.in(not_20_out), .out(pullup_16_out));
  PullUp pullup_17 (.out(pullup_17_out));
  DiodeBackward diodebackward_59 (.in(not_19_out), .out(pullup_17_out));
  DiodeBackward diodebackward_60 (.in(not_17_out), .out(pullup_17_out));
  DiodeBackward diodebackward_61 (.in(nRES), .out(pullup_17_out));
  PullUp pullup_18 (.out(pullup_18_out));
  DiodeBackward diodebackward_62 (.in(not_20_out), .out(pullup_18_out));
  DiodeBackward diodebackward_63 (.in(not_17_out), .out(pullup_18_out));
  DiodeBackward diodebackward_64 (.in(not_22_out), .out(pullup_18_out));
  PullUp pullup_19 (.out(pullup_19_out));
  DiodeBackward diodebackward_65 (.in(not_21_out), .out(pullup_19_out));
  DiodeBackward diodebackward_66 (.in(not_24_out), .out(pullup_19_out));
  DiodeBackward diodebackward_67 (.in(nRES), .out(pullup_19_out));
  not not_19 (not_19_out, pullup_16_out);
  not not_20 (not_20_out, pullup_17_out);
  not not_21 (not_21_out, pullup_18_out);
  not not_22 (not_22_out, pullup_19_out);
  PullUp pullup_20 (.out(pullup_20_out));
  DiodeBackward diodebackward_68 (.in(not_20_out), .out(pullup_20_out));
  DiodeBackward diodebackward_69 (.in(not_24_out), .out(pullup_20_out));
  PullUp pullup_21 (.out(pullup_21_out));
  DiodeBackward diodebackward_70 (.in(not_47_out[1]), .out(pullup_21_out));
  DiodeBackward diodebackward_71 (.in(not_21_out), .out(pullup_21_out));
  DiodeBackward diodebackward_72 (.in(nRES), .out(pullup_21_out));
  not not_23 (not_47_out[1], pullup_20_out);
  not not_24 (not_24_out, pullup_21_out);
  LED Q1 (.in(not_47_out[1]));
  not not_25 (not_25_out, A);
  not not_26 (not_26_out, B);
  not not_27 (not_27_out, C);
  not not_28 (not_28_out, nE);
  DiodeBackward diodebackward_73 (.in(not_32_out), .out(diodebackward_73_out));
  DiodeBackward diodebackward_74 (.in(not_30_out), .out(diodebackward_73_out));
  DiodeBackward diodebackward_75 (.in(not_29_out), .out(diodebackward_75_out));
  DiodeBackward diodebackward_76 (.in(not_24_out), .out(diodebackward_75_out));
  DiodeBackward diodebackward_77 (.in(nRES), .out(diodebackward_75_out));
  DiodeBackward diodebackward_78 (.in(not_30_out), .out(diodebackward_78_out));
  DiodeBackward diodebackward_79 (.in(not_24_out), .out(diodebackward_78_out));
  DiodeBackward diodebackward_80 (.in(not_32_out), .out(diodebackward_78_out));
  DiodeBackward diodebackward_81 (.in(not_31_out), .out(diodebackward_81_out));
  DiodeBackward diodebackward_82 (.in(not_42_out), .out(diodebackward_81_out));
  DiodeBackward diodebackward_83 (.in(nRES), .out(diodebackward_81_out));
  PullUp pullup_22 (.out(diodebackward_73_out));
  not not_29 (not_29_out, diodebackward_73_out);
  PullUp pullup_23 (.out(diodebackward_75_out));
  not not_30 (not_30_out, diodebackward_75_out);
  PullUp pullup_24 (.out(diodebackward_78_out));
  not not_31 (not_31_out, diodebackward_78_out);
  PullUp pullup_25 (.out(diodebackward_81_out));
  not not_32 (not_32_out, diodebackward_81_out);
  PullUp pullup_26 (.out(pullup_26_out));
  DiodeBackward diodebackward_84 (.in(not_25_out), .out(pullup_26_out));
  DiodeBackward diodebackward_85 (.in(not_26_out), .out(pullup_26_out));
  DiodeBackward diodebackward_86 (.in(not_27_out), .out(pullup_26_out));
  DiodeBackward diodebackward_87 (.in(not_28_out), .out(pullup_26_out));
  PullUp pullup_27 (.out(pullup_27_out));
  DiodeBackward diodebackward_88 (.in(A), .out(pullup_27_out));
  DiodeBackward diodebackward_89 (.in(not_26_out), .out(pullup_27_out));
  DiodeBackward diodebackward_90 (.in(not_27_out), .out(pullup_27_out));
  DiodeBackward diodebackward_91 (.in(not_28_out), .out(pullup_27_out));
  PullUp pullup_28 (.out(pullup_28_out));
  DiodeBackward diodebackward_92 (.in(not_25_out), .out(pullup_28_out));
  DiodeBackward diodebackward_93 (.in(B), .out(pullup_28_out));
  DiodeBackward diodebackward_94 (.in(not_27_out), .out(pullup_28_out));
  DiodeBackward diodebackward_95 (.in(not_28_out), .out(pullup_28_out));
  PullUp pullup_29 (.out(pullup_29_out));
  DiodeBackward diodebackward_96 (.in(A), .out(pullup_29_out));
  DiodeBackward diodebackward_97 (.in(B), .out(pullup_29_out));
  DiodeBackward diodebackward_98 (.in(not_27_out), .out(pullup_29_out));
  DiodeBackward diodebackward_99 (.in(not_28_out), .out(pullup_29_out));
  PullUp pullup_30 (.out(pullup_30_out));
  DiodeBackward diodebackward_100 (.in(not_25_out), .out(pullup_30_out));
  DiodeBackward diodebackward_101 (.in(not_26_out), .out(pullup_30_out));
  DiodeBackward diodebackward_102 (.in(C), .out(pullup_30_out));
  DiodeBackward diodebackward_103 (.in(not_28_out), .out(pullup_30_out));
  PullUp pullup_31 (.out(pullup_31_out));
  DiodeBackward diodebackward_104 (.in(A), .out(pullup_31_out));
  DiodeBackward diodebackward_105 (.in(not_26_out), .out(pullup_31_out));
  DiodeBackward diodebackward_106 (.in(C), .out(pullup_31_out));
  DiodeBackward diodebackward_107 (.in(not_28_out), .out(pullup_31_out));
  PullUp pullup_32 (.out(pullup_32_out));
  DiodeBackward diodebackward_108 (.in(not_25_out), .out(pullup_32_out));
  DiodeBackward diodebackward_109 (.in(B), .out(pullup_32_out));
  DiodeBackward diodebackward_110 (.in(C), .out(pullup_32_out));
  DiodeBackward diodebackward_111 (.in(not_28_out), .out(pullup_32_out));
  PullUp pullup_33 (.out(pullup_33_out));
  DiodeBackward diodebackward_112 (.in(A), .out(pullup_33_out));
  DiodeBackward diodebackward_113 (.in(B), .out(pullup_33_out));
  DiodeBackward diodebackward_114 (.in(C), .out(pullup_33_out));
  DiodeBackward diodebackward_115 (.in(not_28_out), .out(pullup_33_out));
  DiodeBackward diodebackward_116 (.in(not_30_out), .out(diodebackward_116_out));
  DiodeBackward diodebackward_117 (.in(not_42_out), .out(diodebackward_116_out));
  DiodeBackward diodebackward_118 (.in(not_47_out[2]), .out(diodebackward_118_out));
  DiodeBackward diodebackward_119 (.in(not_31_out), .out(diodebackward_118_out));
  DiodeBackward diodebackward_120 (.in(nRES), .out(diodebackward_118_out));
  not not_33 (out_8, pullup_26_out);
  not not_34 (out_7, pullup_27_out);
  not not_35 (out_6, pullup_28_out);
  not not_36 (out_5, pullup_29_out);
  not not_37 (out_4, pullup_30_out);
  not not_38 (out_3, pullup_31_out);
  not not_39 (out_2, pullup_32_out);
  not not_40 (out_1, pullup_33_out);
  PullUp pullup_34 (.out(diodebackward_116_out));
  not not_41 (not_47_out[2], diodebackward_116_out);
  PullUp pullup_35 (.out(diodebackward_118_out));
  not not_42 (not_42_out, diodebackward_118_out);
  LED Q2 (.in(not_47_out[2]));
  DiodeBackward diodebackward_121 (.in(not_46_out), .out(diodebackward_121_out));
  DiodeBackward diodebackward_122 (.in(not_44_out), .out(diodebackward_121_out));
  DiodeBackward diodebackward_123 (.in(not_43_out), .out(diodebackward_123_out));
  DiodeBackward diodebackward_124 (.in(not_42_out), .out(diodebackward_123_out));
  DiodeBackward diodebackward_125 (.in(nRES), .out(diodebackward_123_out));
  DiodeBackward diodebackward_126 (.in(not_44_out), .out(diodebackward_126_out));
  DiodeBackward diodebackward_127 (.in(not_42_out), .out(diodebackward_126_out));
  DiodeBackward diodebackward_128 (.in(not_46_out), .out(diodebackward_126_out));
  DiodeBackward diodebackward_129 (.in(not_45_out), .out(diodebackward_129_out));
  DiodeBackward diodebackward_130 (.in(not_48_out), .out(diodebackward_129_out));
  DiodeBackward diodebackward_131 (.in(nRES), .out(diodebackward_129_out));
  PullUp pullup_36 (.out(diodebackward_121_out));
  not not_43 (not_43_out, diodebackward_121_out);
  PullUp pullup_37 (.out(diodebackward_123_out));
  not not_44 (not_44_out, diodebackward_123_out);
  PullUp pullup_38 (.out(diodebackward_126_out));
  not not_45 (not_45_out, diodebackward_126_out);
  PullUp pullup_39 (.out(diodebackward_129_out));
  not not_46 (not_46_out, diodebackward_129_out);
  DiodeBackward diodebackward_132 (.in(not_44_out), .out(diodebackward_132_out));
  DiodeBackward diodebackward_133 (.in(not_48_out), .out(diodebackward_132_out));
  DiodeBackward diodebackward_134 (.in(not_47_out[3]), .out(diodebackward_134_out));
  DiodeBackward diodebackward_135 (.in(not_45_out), .out(diodebackward_134_out));
  DiodeBackward diodebackward_136 (.in(nRES), .out(diodebackward_134_out));
  PullUp pullup_40 (.out(diodebackward_132_out));
  not not_47 (not_47_out[3], diodebackward_132_out);
  PullUp pullup_41 (.out(diodebackward_134_out));
  not not_48 (not_48_out, diodebackward_134_out);
  LED Q3 (.in(not_47_out[3]));
  not not_49 (not_49_out, B_3);
  not not_50 (not_50_out, A_3);
  not not_51 (not_51_out, nE1);
  not not_52 (not_52_out, S0);
  not not_53 (not_53_out, S1);
  not not_54 (not_54_out, nE2);
  PullUp pullup_42 (.out(pullup_42_out));
  DiodeBackward diodebackward_137 (.in(not_49_out), .out(pullup_42_out));
  not not_55 (not_55_out, pullup_42_out);
  DiodeBackward diodebackward_138 (.in(not_50_out), .out(pullup_42_out));
  DiodeBackward diodebackward_139 (.in(I0), .out(pullup_42_out));
  PullUp pullup_43 (.out(pullup_43_out));
  DiodeBackward diodebackward_140 (.in(B_3), .out(pullup_43_out));
  not not_56 (not_56_out, pullup_43_out);
  DiodeBackward diodebackward_141 (.in(not_50_out), .out(pullup_43_out));
  DiodeBackward diodebackward_142 (.in(I1), .out(pullup_43_out));
  PullUp pullup_44 (.out(pullup_44_out));
  DiodeBackward diodebackward_143 (.in(not_49_out), .out(pullup_44_out));
  not not_57 (not_57_out, pullup_44_out);
  DiodeBackward diodebackward_144 (.in(A_3), .out(pullup_44_out));
  DiodeBackward diodebackward_145 (.in(I2), .out(pullup_44_out));
  PullUp pullup_45 (.out(pullup_45_out));
  DiodeBackward diodebackward_146 (.in(B_3), .out(pullup_45_out));
  not not_58 (not_58_out, pullup_45_out);
  DiodeBackward diodebackward_147 (.in(A_3), .out(pullup_45_out));
  DiodeBackward diodebackward_148 (.in(I3), .out(pullup_45_out));
  DiodeBackward diodebackward_149 (.in(not_52_out), .out(diodebackward_149_out));
  DiodeBackward diodebackward_150 (.in(not_53_out), .out(diodebackward_149_out));
  DiodeBackward diodebackward_151 (.in(A0), .out(diodebackward_149_out));
  DiodeBackward diodebackward_152 (.in(not_51_out), .out(diodebackward_149_out));
  DiodeBackward diodebackward_153 (.in(S0), .out(diodebackward_153_out));
  DiodeBackward diodebackward_154 (.in(not_53_out), .out(diodebackward_153_out));
  DiodeBackward diodebackward_155 (.in(A1), .out(diodebackward_153_out));
  DiodeBackward diodebackward_156 (.in(not_51_out), .out(diodebackward_153_out));
  DiodeBackward diodebackward_157 (.in(not_52_out), .out(diodebackward_157_out));
  DiodeBackward diodebackward_158 (.in(S1), .out(diodebackward_157_out));
  DiodeBackward diodebackward_159 (.in(A2), .out(diodebackward_157_out));
  DiodeBackward diodebackward_160 (.in(not_51_out), .out(diodebackward_157_out));
  DiodeBackward diodebackward_161 (.in(S0), .out(diodebackward_161_out));
  DiodeBackward diodebackward_162 (.in(S1), .out(diodebackward_161_out));
  DiodeBackward diodebackward_163 (.in(A3), .out(diodebackward_161_out));
  DiodeBackward diodebackward_164 (.in(not_51_out), .out(diodebackward_161_out));
  DiodeBackward diodebackward_165 (.in(not_52_out), .out(diodebackward_165_out));
  DiodeBackward diodebackward_166 (.in(not_53_out), .out(diodebackward_165_out));
  DiodeBackward diodebackward_167 (.in(B0), .out(diodebackward_165_out));
  DiodeBackward diodebackward_168 (.in(not_54_out), .out(diodebackward_165_out));
  DiodeBackward diodebackward_169 (.in(S0), .out(diodebackward_169_out));
  DiodeBackward diodebackward_170 (.in(not_53_out), .out(diodebackward_169_out));
  DiodeBackward diodebackward_171 (.in(B1), .out(diodebackward_169_out));
  DiodeBackward diodebackward_172 (.in(not_54_out), .out(diodebackward_169_out));
  DiodeBackward diodebackward_173 (.in(not_52_out), .out(diodebackward_173_out));
  DiodeBackward diodebackward_174 (.in(S1), .out(diodebackward_173_out));
  DiodeBackward diodebackward_175 (.in(B2), .out(diodebackward_173_out));
  DiodeBackward diodebackward_176 (.in(not_54_out), .out(diodebackward_173_out));
  DiodeBackward diodebackward_177 (.in(S0), .out(diodebackward_177_out));
  DiodeBackward diodebackward_178 (.in(S1), .out(diodebackward_177_out));
  DiodeBackward diodebackward_179 (.in(B3), .out(diodebackward_177_out));
  DiodeBackward diodebackward_180 (.in(not_54_out), .out(diodebackward_177_out));
  PullUp pullup_46 (.out(diodebackward_149_out));
  not not_59 (not_59_out, diodebackward_149_out);
  PullUp pullup_47 (.out(diodebackward_153_out));
  not not_60 (not_60_out, diodebackward_153_out);
  PullUp pullup_48 (.out(diodebackward_157_out));
  not not_61 (not_61_out, diodebackward_157_out);
  PullUp pullup_49 (.out(diodebackward_161_out));
  not not_62 (not_62_out, diodebackward_161_out);
  PullUp pullup_50 (.out(diodebackward_165_out));
  not not_63 (not_63_out, diodebackward_165_out);
  PullUp pullup_51 (.out(diodebackward_169_out));
  not not_64 (not_64_out, diodebackward_169_out);
  PullUp pullup_52 (.out(diodebackward_173_out));
  not not_65 (not_65_out, diodebackward_173_out);
  PullUp pullup_53 (.out(diodebackward_177_out));
  not not_66 (not_66_out, diodebackward_177_out);
  PullUp pullup_54 (.out(pullup_54_out));
  DiodeBackward diodebackward_181 (.in(not_55_out), .out(pullup_54_out));
  DiodeBackward diodebackward_182 (.in(not_56_out), .out(pullup_54_out));
  DiodeBackward diodebackward_183 (.in(not_57_out), .out(pullup_54_out));
  DiodeBackward diodebackward_184 (.in(not_58_out), .out(pullup_54_out));
  DiodeBackward diodebackward_185 (.in(not_73_out), .out(diodebackward_185_out));
  DiodeBackward diodebackward_186 (.in(not_71_out), .out(diodebackward_185_out));
  DiodeBackward diodebackward_187 (.in(not_70_out), .out(diodebackward_187_out));
  DiodeBackward diodebackward_188 (.in(CLK_5), .out(diodebackward_187_out));
  DiodeBackward diodebackward_189 (.in(nRES_2), .out(diodebackward_187_out));
  DiodeBackward diodebackward_190 (.in(not_71_out), .out(diodebackward_190_out));
  DiodeBackward diodebackward_191 (.in(CLK_5), .out(diodebackward_190_out));
  DiodeBackward diodebackward_192 (.in(not_73_out), .out(diodebackward_190_out));
  DiodeBackward diodebackward_193 (.in(not_72_out), .out(diodebackward_193_out));
  DiodeBackward diodebackward_194 (.in(Din), .out(diodebackward_193_out));
  DiodeBackward diodebackward_195 (.in(nRES_2), .out(diodebackward_193_out));
  not not_67 (out_58, pullup_54_out);
  PullUp pullup_55 (.out(pullup_55_out));
  DiodeBackward diodebackward_196 (.in(not_59_out), .out(pullup_55_out));
  not not_68 (out_17, pullup_55_out);
  DiodeBackward diodebackward_197 (.in(not_60_out), .out(pullup_55_out));
  DiodeBackward diodebackward_198 (.in(not_61_out), .out(pullup_55_out));
  DiodeBackward diodebackward_199 (.in(not_62_out), .out(pullup_55_out));
  PullUp pullup_56 (.out(pullup_56_out));
  DiodeBackward diodebackward_200 (.in(not_63_out), .out(pullup_56_out));
  not not_69 (out_18, pullup_56_out);
  DiodeBackward diodebackward_201 (.in(not_64_out), .out(pullup_56_out));
  DiodeBackward diodebackward_202 (.in(not_65_out), .out(pullup_56_out));
  DiodeBackward diodebackward_203 (.in(not_66_out), .out(pullup_56_out));
  PullUp pullup_57 (.out(diodebackward_185_out));
  not not_70 (not_70_out, diodebackward_185_out);
  PullUp pullup_58 (.out(diodebackward_187_out));
  not not_71 (not_71_out, diodebackward_187_out);
  PullUp pullup_59 (.out(diodebackward_190_out));
  not not_72 (not_72_out, diodebackward_190_out);
  PullUp pullup_60 (.out(diodebackward_193_out));
  not not_73 (not_73_out, diodebackward_193_out);
  Seven_Seg_Hex seven_seg_hex_2 (.d(not_74_out), .dp(1'b0));
  DiodeBackward diodebackward_204 (.in(not_71_out), .out(diodebackward_204_out));
  DiodeBackward diodebackward_205 (.in(not_75_out), .out(diodebackward_204_out));
  DiodeBackward diodebackward_206 (.in(not_74_out[0]), .out(diodebackward_206_out));
  DiodeBackward diodebackward_207 (.in(not_72_out), .out(diodebackward_206_out));
  DiodeBackward diodebackward_208 (.in(nRES_2), .out(diodebackward_206_out));
  PullUp pullup_61 (.out(diodebackward_204_out));
  not not_74 (not_74_out[0], diodebackward_204_out);
  PullUp pullup_62 (.out(diodebackward_206_out));
  not not_75 (not_75_out, diodebackward_206_out);
  LED Q4 (.in(not_74_out[0]));
  not not_76 (not_76_out, out_58);
  not not_77 (not_77_out, Cin_2);
  PullUp pullup_63 (.out(pullup_63_out));
  DiodeBackward diodebackward_209 (.in(in_33), .out(pullup_63_out));
  not not_78 (not_78_out, pullup_63_out);
  DiodeBackward diodebackward_210 (.in(in_34), .out(pullup_63_out));
  PullUp pullup_64 (.out(pullup_64_out));
  DiodeBackward diodebackward_211 (.in(in_35), .out(pullup_64_out));
  not not_79 (not_79_out, pullup_64_out);
  DiodeBackward diodebackward_212 (.in(in_36), .out(pullup_64_out));
  PullUp pullup_65 (.out(pullup_65_out));
  not not_80 (not_80_out, pullup_65_out);
  DiodeBackward diodebackward_213 (.in(not_83_out), .out(pullup_65_out));
  DiodeBackward diodebackward_214 (.in(not_81_out), .out(pullup_65_out));
  PullUp pullup_66 (.out(pullup_66_out));
  DiodeBackward diodebackward_215 (.in(not_80_out), .out(pullup_66_out));
  not not_81 (not_81_out, pullup_66_out);
  DiodeBackward diodebackward_216 (.in(CLK_5), .out(pullup_66_out));
  DiodeBackward diodebackward_217 (.in(nRES_2), .out(pullup_66_out));
  PullUp pullup_67 (.out(pullup_67_out));
  DiodeBackward diodebackward_218 (.in(not_81_out), .out(pullup_67_out));
  not not_82 (not_82_out, pullup_67_out);
  DiodeBackward diodebackward_219 (.in(CLK_5), .out(pullup_67_out));
  DiodeBackward diodebackward_220 (.in(not_83_out), .out(pullup_67_out));
  PullUp pullup_68 (.out(pullup_68_out));
  DiodeBackward diodebackward_221 (.in(not_82_out), .out(pullup_68_out));
  not not_83 (not_83_out, pullup_68_out);
  DiodeBackward diodebackward_222 (.in(not_74_out[0]), .out(pullup_68_out));
  DiodeBackward diodebackward_223 (.in(nRES_2), .out(pullup_68_out));
  DiodeBackward diodebackward_224 (.in(not_76_out), .out(diodebackward_224_out));
  DiodeBackward diodebackward_225 (.in(not_77_out), .out(diodebackward_224_out));
  DiodeBackward diodebackward_226 (.in(I0_2), .out(diodebackward_224_out));
  DiodeBackward diodebackward_227 (.in(out_58), .out(diodebackward_227_out));
  DiodeBackward diodebackward_228 (.in(not_77_out), .out(diodebackward_227_out));
  DiodeBackward diodebackward_229 (.in(I1_2), .out(diodebackward_227_out));
  DiodeBackward diodebackward_230 (.in(not_76_out), .out(diodebackward_230_out));
  DiodeBackward diodebackward_231 (.in(Cin_2), .out(diodebackward_230_out));
  DiodeBackward diodebackward_232 (.in(I2_2), .out(diodebackward_230_out));
  DiodeBackward diodebackward_233 (.in(out_58), .out(diodebackward_233_out));
  DiodeBackward diodebackward_234 (.in(Cin_2), .out(diodebackward_233_out));
  DiodeBackward diodebackward_235 (.in(I3_2), .out(diodebackward_233_out));
  DiodeBackward diodebackward_236 (.in(A_2), .out(diodebackward_236_out));
  DiodeBackward diodebackward_237 (.in(pullup_85_out), .out(diodebackward_236_out));
  DiodeBackward diodebackward_238 (.in(pullup_85_out), .out(diodebackward_238_out));
  DiodeBackward diodebackward_239 (.in(B_2), .out(diodebackward_238_out));
  DiodeBackward diodebackward_240 (.in(pullup_85_out), .out(diodebackward_240_out));
  DiodeBackward diodebackward_241 (.in(Cin), .out(diodebackward_240_out));
  DiodeBackward diodebackward_242 (.in(B_2), .out(diodebackward_242_out));
  DiodeBackward diodebackward_243 (.in(A_2), .out(diodebackward_242_out));
  DiodeBackward diodebackward_244 (.in(Cin), .out(diodebackward_242_out));
  DiodeBackward diodebackward_245 (.in(Cin), .out(diodebackward_245_out));
  DiodeBackward diodebackward_246 (.in(B_2), .out(diodebackward_245_out));
  DiodeBackward diodebackward_247 (.in(A_2), .out(diodebackward_247_out));
  DiodeBackward diodebackward_248 (.in(B_2), .out(diodebackward_247_out));
  DiodeBackward diodebackward_249 (.in(A_2), .out(diodebackward_249_out));
  DiodeBackward diodebackward_250 (.in(Cin), .out(diodebackward_249_out));
  PullUp pullup_69 (.out(diodebackward_224_out));
  not not_84 (not_84_out, diodebackward_224_out);
  PullUp pullup_70 (.out(diodebackward_227_out));
  not not_85 (not_85_out, diodebackward_227_out);
  PullUp pullup_71 (.out(diodebackward_230_out));
  not not_86 (not_86_out, diodebackward_230_out);
  PullUp pullup_72 (.out(diodebackward_233_out));
  not not_87 (not_87_out, diodebackward_233_out);
  PullUp pullup_73 (.out(diodebackward_236_out));
  not not_88 (not_88_out, diodebackward_236_out);
  PullUp pullup_74 (.out(diodebackward_238_out));
  not not_89 (not_89_out, diodebackward_238_out);
  PullUp pullup_75 (.out(diodebackward_240_out));
  not not_90 (not_90_out, diodebackward_240_out);
  PullUp pullup_76 (.out(diodebackward_242_out));
  not not_91 (not_91_out, diodebackward_242_out);
  PullUp pullup_77 (.out(diodebackward_245_out));
  not not_92 (not_92_out, diodebackward_245_out);
  PullUp pullup_78 (.out(diodebackward_247_out));
  not not_93 (not_93_out, diodebackward_247_out);
  PullUp pullup_79 (.out(diodebackward_249_out));
  not not_94 (not_94_out, diodebackward_249_out);
  PullUp pullup_80 (.out(pullup_80_out));
  DiodeBackward diodebackward_251 (.in(not_78_out), .out(pullup_80_out));
  DiodeBackward diodebackward_252 (.in(not_79_out), .out(pullup_80_out));
  not not_95 (out_32, pullup_80_out);
  PullUp pullup_81 (.out(pullup_81_out));
  DiodeBackward diodebackward_253 (.in(not_81_out), .out(pullup_81_out));
  not not_96 (not_74_out[1], pullup_81_out);
  DiodeBackward diodebackward_254 (.in(not_97_out), .out(pullup_81_out));
  PullUp pullup_82 (.out(pullup_82_out));
  DiodeBackward diodebackward_255 (.in(not_74_out[1]), .out(pullup_82_out));
  not not_97 (not_97_out, pullup_82_out);
  DiodeBackward diodebackward_256 (.in(not_82_out), .out(pullup_82_out));
  DiodeBackward diodebackward_257 (.in(nRES_2), .out(pullup_82_out));
  DiodeBackward diodebackward_258 (.in(not_84_out), .out(diodebackward_258_out));
  DiodeBackward diodebackward_259 (.in(not_85_out), .out(diodebackward_258_out));
  DiodeBackward diodebackward_260 (.in(not_86_out), .out(diodebackward_258_out));
  DiodeBackward diodebackward_261 (.in(not_87_out), .out(diodebackward_258_out));
  LED Q5 (.in(not_74_out[1]));
  PullUp pullup_83 (.out(diodebackward_258_out));
  not not_98 (out_64, diodebackward_258_out);
  PullUp pullup_84 (.out(pullup_84_out));
  DiodeBackward diodebackward_262 (.in(not_88_out), .out(pullup_84_out));
  DiodeBackward diodebackward_263 (.in(not_89_out), .out(pullup_84_out));
  DiodeBackward diodebackward_264 (.in(not_90_out), .out(pullup_84_out));
  DiodeBackward diodebackward_265 (.in(not_91_out), .out(pullup_84_out));
  PullUp pullup_85 (.out(pullup_85_out));
  DiodeBackward diodebackward_266 (.in(not_92_out), .out(pullup_85_out));
  DiodeBackward diodebackward_267 (.in(not_93_out), .out(pullup_85_out));
  DiodeBackward diodebackward_268 (.in(not_94_out), .out(pullup_85_out));
  not not_99 (SUM, pullup_84_out);
  not not_100 (CARRY, pullup_85_out);
  PullUp pullup_86 (.out(pullup_86_out));
  DiodeBackward diodebackward_269 (.in(not_104_out), .out(pullup_86_out));
  DiodeBackward diodebackward_270 (.in(not_102_out), .out(pullup_86_out));
  PullUp pullup_87 (.out(pullup_87_out));
  DiodeBackward diodebackward_271 (.in(not_101_out), .out(pullup_87_out));
  DiodeBackward diodebackward_272 (.in(CLK_5), .out(pullup_87_out));
  DiodeBackward diodebackward_273 (.in(nRES_2), .out(pullup_87_out));
  PullUp pullup_88 (.out(pullup_88_out));
  DiodeBackward diodebackward_274 (.in(not_102_out), .out(pullup_88_out));
  DiodeBackward diodebackward_275 (.in(CLK_5), .out(pullup_88_out));
  DiodeBackward diodebackward_276 (.in(not_104_out), .out(pullup_88_out));
  PullUp pullup_89 (.out(pullup_89_out));
  DiodeBackward diodebackward_277 (.in(not_103_out), .out(pullup_89_out));
  DiodeBackward diodebackward_278 (.in(not_74_out[1]), .out(pullup_89_out));
  DiodeBackward diodebackward_279 (.in(nRES_2), .out(pullup_89_out));
  not not_101 (not_101_out, pullup_86_out);
  not not_102 (not_102_out, pullup_87_out);
  not not_103 (not_103_out, pullup_88_out);
  not not_104 (not_104_out, pullup_89_out);
  PullUp pullup_90 (.out(pullup_90_out));
  DiodeBackward diodebackward_280 (.in(not_102_out), .out(pullup_90_out));
  DiodeBackward diodebackward_281 (.in(not_107_out), .out(pullup_90_out));
  PullUp pullup_91 (.out(pullup_91_out));
  DiodeBackward diodebackward_282 (.in(not_74_out[2]), .out(pullup_91_out));
  DiodeBackward diodebackward_283 (.in(not_103_out), .out(pullup_91_out));
  DiodeBackward diodebackward_284 (.in(nRES_2), .out(pullup_91_out));
  not not_105 (not_105_out, D);
  not not_106 (not_74_out[2], pullup_90_out);
  not not_107 (not_107_out, pullup_91_out);
  LED Q6 (.in(not_74_out[2]));
  DiodeBackward diodebackward_285 (.in(CLK_2), .out(diodebackward_285_out));
  DiodeBackward diodebackward_286 (.in(D_2), .out(diodebackward_285_out));
  DiodeBackward diodebackward_287 (.in(not_109_out), .out(diodebackward_287_out));
  DiodeBackward diodebackward_288 (.in(CLK_2), .out(diodebackward_287_out));
  not not_108 (not_108_out, CLK);
  PullUp pullup_92 (.out(diodebackward_285_out));
  not not_109 (not_109_out, diodebackward_285_out);
  PullUp pullup_93 (.out(diodebackward_287_out));
  not not_110 (not_110_out, diodebackward_287_out);
  PullUp pullup_94 (.out(pullup_94_out));
  DiodeBackward diodebackward_289 (.in(D), .out(pullup_94_out));
  not not_111 (not_111_out, pullup_94_out);
  DiodeBackward diodebackward_290 (.in(not_108_out), .out(pullup_94_out));
  PullUp pullup_95 (.out(pullup_95_out));
  DiodeBackward diodebackward_291 (.in(not_108_out), .out(pullup_95_out));
  not not_112 (not_112_out, pullup_95_out);
  DiodeBackward diodebackward_292 (.in(not_105_out), .out(pullup_95_out));
  DiodeBackward diodebackward_293 (.in(not_116_out), .out(diodebackward_293_out));
  DiodeBackward diodebackward_294 (.in(not_114_out), .out(diodebackward_293_out));
  DiodeBackward diodebackward_295 (.in(not_113_out), .out(diodebackward_295_out));
  DiodeBackward diodebackward_296 (.in(CLK_5), .out(diodebackward_295_out));
  DiodeBackward diodebackward_297 (.in(nRES_2), .out(diodebackward_295_out));
  DiodeBackward diodebackward_298 (.in(not_114_out), .out(diodebackward_298_out));
  DiodeBackward diodebackward_299 (.in(CLK_5), .out(diodebackward_298_out));
  DiodeBackward diodebackward_300 (.in(not_116_out), .out(diodebackward_298_out));
  DiodeBackward diodebackward_301 (.in(not_115_out), .out(diodebackward_301_out));
  DiodeBackward diodebackward_302 (.in(not_74_out[2]), .out(diodebackward_301_out));
  DiodeBackward diodebackward_303 (.in(nRES_2), .out(diodebackward_301_out));
  PullUp pullup_96 (.out(diodebackward_293_out));
  not not_113 (not_113_out, diodebackward_293_out);
  PullUp pullup_97 (.out(diodebackward_295_out));
  not not_114 (not_114_out, diodebackward_295_out);
  PullUp pullup_98 (.out(diodebackward_298_out));
  not not_115 (not_115_out, diodebackward_298_out);
  PullUp pullup_99 (.out(diodebackward_301_out));
  not not_116 (not_116_out, diodebackward_301_out);
  PullUp pullup_100 (.out(pullup_100_out));
  DiodeBackward diodebackward_304 (.in(A_4), .out(pullup_100_out));
  not not_117 (not_117_out, pullup_100_out);
  DiodeBackward diodebackward_305 (.in(not_133_out), .out(pullup_100_out));
  PullUp pullup_101 (.out(pullup_101_out));
  DiodeBackward diodebackward_306 (.in(not_133_out), .out(pullup_101_out));
  not not_118 (not_118_out, pullup_101_out);
  DiodeBackward diodebackward_307 (.in(B_4), .out(pullup_101_out));
  PullUp pullup_102 (.out(pullup_102_out));
  DiodeBackward diodebackward_308 (.in(not_133_out), .out(pullup_102_out));
  not not_119 (not_119_out, pullup_102_out);
  DiodeBackward diodebackward_309 (.in(Cin_3), .out(pullup_102_out));
  PullUp pullup_103 (.out(pullup_103_out));
  DiodeBackward diodebackward_310 (.in(B_4), .out(pullup_103_out));
  not not_120 (not_120_out, pullup_103_out);
  DiodeBackward diodebackward_311 (.in(A_4), .out(pullup_103_out));
  DiodeBackward diodebackward_312 (.in(Cin_3), .out(pullup_103_out));
  PullUp pullup_104 (.out(pullup_104_out));
  DiodeBackward diodebackward_313 (.in(Cin_3), .out(pullup_104_out));
  not not_121 (not_121_out, pullup_104_out);
  DiodeBackward diodebackward_314 (.in(B_4), .out(pullup_104_out));
  PullUp pullup_105 (.out(pullup_105_out));
  DiodeBackward diodebackward_315 (.in(A_4), .out(pullup_105_out));
  not not_122 (not_122_out, pullup_105_out);
  DiodeBackward diodebackward_316 (.in(B_4), .out(pullup_105_out));
  PullUp pullup_106 (.out(pullup_106_out));
  DiodeBackward diodebackward_317 (.in(A_4), .out(pullup_106_out));
  not not_123 (not_123_out, pullup_106_out);
  DiodeBackward diodebackward_318 (.in(Cin_3), .out(pullup_106_out));
  DiodeBackward diodebackward_319 (.in(nSET_2), .out(diodebackward_319_out));
  DiodeBackward diodebackward_320 (.in(nQ_4), .out(diodebackward_319_out));
  DiodeBackward diodebackward_321 (.in(Q_4), .out(diodebackward_321_out));
  DiodeBackward diodebackward_322 (.in(nRESET_2), .out(diodebackward_321_out));
  DiodeBackward diodebackward_323 (.in(not_109_out), .out(diodebackward_323_out));
  DiodeBackward diodebackward_324 (.in(nQ_2), .out(diodebackward_323_out));
  DiodeBackward diodebackward_325 (.in(Q_2), .out(diodebackward_325_out));
  DiodeBackward diodebackward_326 (.in(not_110_out), .out(diodebackward_325_out));
  DiodeBackward diodebackward_327 (.in(not_111_out), .out(diodebackward_327_out));
  DiodeBackward diodebackward_328 (.in(not_129_out), .out(diodebackward_327_out));
  DiodeBackward diodebackward_329 (.in(not_128_out), .out(diodebackward_329_out));
  DiodeBackward diodebackward_330 (.in(not_112_out), .out(diodebackward_329_out));
  PullUp pullup_107 (.out(diodebackward_319_out));
  not not_124 (Q_4, diodebackward_319_out);
  PullUp pullup_108 (.out(diodebackward_321_out));
  not not_125 (nQ_4, diodebackward_321_out);
  PullUp pullup_109 (.out(diodebackward_323_out));
  not not_126 (Q_2, diodebackward_323_out);
  PullUp pullup_110 (.out(diodebackward_325_out));
  not not_127 (nQ_2, diodebackward_325_out);
  PullUp pullup_111 (.out(diodebackward_327_out));
  not not_128 (not_128_out, diodebackward_327_out);
  PullUp pullup_112 (.out(diodebackward_329_out));
  not not_129 (not_129_out, diodebackward_329_out);
  DiodeBackward diodebackward_331 (.in(not_114_out), .out(diodebackward_331_out));
  DiodeBackward diodebackward_332 (.in(not_131_out), .out(diodebackward_331_out));
  DiodeBackward diodebackward_333 (.in(not_74_out[3]), .out(diodebackward_333_out));
  DiodeBackward diodebackward_334 (.in(not_115_out), .out(diodebackward_333_out));
  DiodeBackward diodebackward_335 (.in(nRES_2), .out(diodebackward_333_out));
  DiodeBackward diodebackward_336 (.in(not_117_out), .out(diodebackward_336_out));
  DiodeBackward diodebackward_337 (.in(not_118_out), .out(diodebackward_336_out));
  DiodeBackward diodebackward_338 (.in(not_119_out), .out(diodebackward_336_out));
  DiodeBackward diodebackward_339 (.in(not_120_out), .out(diodebackward_336_out));
  DiodeBackward diodebackward_340 (.in(not_121_out), .out(diodebackward_340_out));
  DiodeBackward diodebackward_341 (.in(not_122_out), .out(diodebackward_340_out));
  DiodeBackward diodebackward_342 (.in(not_123_out), .out(diodebackward_340_out));
  PullUp pullup_113 (.out(diodebackward_331_out));
  not not_130 (not_74_out[3], diodebackward_331_out);
  PullUp pullup_114 (.out(diodebackward_333_out));
  not not_131 (not_131_out, diodebackward_333_out);
  PullUp pullup_115 (.out(diodebackward_336_out));
  not not_132 (not_132_out, diodebackward_336_out);
  PullUp pullup_116 (.out(diodebackward_340_out));
  LED Q7 (.in(not_74_out[3]));
  not not_133 (not_133_out, CARRY_2);
  not not_134 (CARRY_2, diodebackward_340_out);
  PullUp pullup_117 (.out(pullup_117_out));
  DiodeBackward diodebackward_343 (.in(CLK), .out(pullup_117_out));
  not not_135 (not_135_out, pullup_117_out);
  DiodeBackward diodebackward_344 (.in(not_128_out), .out(pullup_117_out));
  PullUp pullup_118 (.out(pullup_118_out));
  DiodeBackward diodebackward_345 (.in(not_129_out), .out(pullup_118_out));
  not not_136 (not_136_out, pullup_118_out);
  DiodeBackward diodebackward_346 (.in(CLK), .out(pullup_118_out));
  PullUp pullup_119 (.out(pullup_119_out));
  DiodeBackward diodebackward_347 (.in(not_132_out), .out(pullup_119_out));
  DiodeBackward diodebackward_348 (.in(I0_3), .out(pullup_119_out));
  PullUp pullup_120 (.out(pullup_120_out));
  DiodeBackward diodebackward_349 (.in(I1_3), .out(pullup_120_out));
  DiodeBackward diodebackward_350 (.in(CARRY_2), .out(pullup_120_out));
  DiodeBackward diodebackward_351 (.in(not_135_out), .out(diodebackward_351_out));
  DiodeBackward diodebackward_352 (.in(nQ), .out(diodebackward_351_out));
  DiodeBackward diodebackward_353 (.in(Q), .out(diodebackward_353_out));
  DiodeBackward diodebackward_354 (.in(not_136_out), .out(diodebackward_353_out));
  not not_137 (not_137_out, pullup_119_out);
  not not_138 (not_138_out, pullup_120_out);
  PullUp pullup_121 (.out(diodebackward_351_out));
  not not_139 (Q, diodebackward_351_out);
  PullUp pullup_122 (.out(diodebackward_353_out));
  not not_140 (nQ, diodebackward_353_out);
  DiodeBackward diodebackward_355 (.in(not_137_out), .out(diodebackward_355_out));
  DiodeBackward diodebackward_356 (.in(not_138_out), .out(diodebackward_355_out));
  PullUp pullup_123 (.out(diodebackward_355_out));
  not not_141 (Fout, diodebackward_355_out);
  DiodeBackward diodebackward_357 (.in(nSET), .out(diodebackward_357_out));
  DiodeBackward diodebackward_358 (.in(not_145_out), .out(diodebackward_357_out));
  DiodeBackward diodebackward_359 (.in(not_143_out), .out(diodebackward_357_out));
  DiodeBackward diodebackward_360 (.in(not_142_out), .out(diodebackward_360_out));
  DiodeBackward diodebackward_361 (.in(CLK_3), .out(diodebackward_360_out));
  DiodeBackward diodebackward_362 (.in(nRESET), .out(diodebackward_360_out));
  DiodeBackward diodebackward_363 (.in(not_143_out), .out(diodebackward_363_out));
  DiodeBackward diodebackward_364 (.in(CLK_3), .out(diodebackward_363_out));
  DiodeBackward diodebackward_365 (.in(not_145_out), .out(diodebackward_363_out));
  DiodeBackward diodebackward_366 (.in(not_144_out), .out(diodebackward_366_out));
  DiodeBackward diodebackward_367 (.in(DATA), .out(diodebackward_366_out));
  DiodeBackward diodebackward_368 (.in(nRESET), .out(diodebackward_366_out));
  PullUp pullup_124 (.out(diodebackward_357_out));
  not not_142 (not_142_out, diodebackward_357_out);
  PullUp pullup_125 (.out(diodebackward_360_out));
  not not_143 (not_143_out, diodebackward_360_out);
  PullUp pullup_126 (.out(diodebackward_363_out));
  not not_144 (not_144_out, diodebackward_363_out);
  PullUp pullup_127 (.out(diodebackward_366_out));
  not not_145 (not_145_out, diodebackward_366_out);
  PullUp pullup_128 (.out(pullup_128_out));
  DiodeBackward diodebackward_369 (.in(not_149_out), .out(pullup_128_out));
  DiodeBackward diodebackward_370 (.in(not_147_out), .out(pullup_128_out));
  PullUp pullup_129 (.out(pullup_129_out));
  DiodeBackward diodebackward_371 (.in(not_146_out), .out(pullup_129_out));
  DiodeBackward diodebackward_372 (.in(CLK_6), .out(pullup_129_out));
  DiodeBackward diodebackward_373 (.in(nRES_3), .out(pullup_129_out));
  PullUp pullup_130 (.out(pullup_130_out));
  DiodeBackward diodebackward_374 (.in(not_147_out), .out(pullup_130_out));
  DiodeBackward diodebackward_375 (.in(CLK_6), .out(pullup_130_out));
  DiodeBackward diodebackward_376 (.in(not_149_out), .out(pullup_130_out));
  PullUp pullup_131 (.out(pullup_131_out));
  DiodeBackward diodebackward_377 (.in(not_148_out), .out(pullup_131_out));
  DiodeBackward diodebackward_378 (.in(Din_2), .out(pullup_131_out));
  DiodeBackward diodebackward_379 (.in(nRES_3), .out(pullup_131_out));
  not not_146 (not_146_out, pullup_128_out);
  not not_147 (not_147_out, pullup_129_out);
  not not_148 (not_148_out, pullup_130_out);
  not not_149 (not_149_out, pullup_131_out);
  DiodeBackward diodebackward_380 (.in(nSET), .out(diodebackward_380_out));
  DiodeBackward diodebackward_381 (.in(not_143_out), .out(diodebackward_380_out));
  DiodeBackward diodebackward_382 (.in(nQ_3), .out(diodebackward_380_out));
  DiodeBackward diodebackward_383 (.in(Q_3), .out(diodebackward_383_out));
  DiodeBackward diodebackward_384 (.in(not_144_out), .out(diodebackward_383_out));
  DiodeBackward diodebackward_385 (.in(nRESET), .out(diodebackward_383_out));
  Seven_Seg_Hex seven_seg_hex_3 (.d(not_170_out), .dp(1'b0));
  PullUp pullup_132 (.out(pullup_132_out));
  DiodeBackward diodebackward_386 (.in(not_147_out), .out(pullup_132_out));
  DiodeBackward diodebackward_387 (.in(not_153_out), .out(pullup_132_out));
  PullUp pullup_133 (.out(pullup_133_out));
  DiodeBackward diodebackward_388 (.in(not_170_out[0]), .out(pullup_133_out));
  DiodeBackward diodebackward_389 (.in(not_148_out), .out(pullup_133_out));
  DiodeBackward diodebackward_390 (.in(nRES_3), .out(pullup_133_out));
  PullUp pullup_134 (.out(diodebackward_380_out));
  not not_150 (Q_3, diodebackward_380_out);
  PullUp pullup_135 (.out(diodebackward_383_out));
  not not_151 (nQ_3, diodebackward_383_out);
  not not_152 (not_170_out[0], pullup_132_out);
  not not_153 (not_153_out, pullup_133_out);
  LED Q8 (.in(not_170_out[0]));
  DiodeBackward diodebackward_391 (.in(not_157_out), .out(diodebackward_391_out));
  DiodeBackward diodebackward_392 (.in(not_155_out), .out(diodebackward_391_out));
  DiodeBackward diodebackward_393 (.in(not_154_out), .out(diodebackward_393_out));
  DiodeBackward diodebackward_394 (.in(CLK_6), .out(diodebackward_393_out));
  DiodeBackward diodebackward_395 (.in(nRES_3), .out(diodebackward_393_out));
  DiodeBackward diodebackward_396 (.in(not_155_out), .out(diodebackward_396_out));
  DiodeBackward diodebackward_397 (.in(CLK_6), .out(diodebackward_396_out));
  DiodeBackward diodebackward_398 (.in(not_157_out), .out(diodebackward_396_out));
  DiodeBackward diodebackward_399 (.in(not_156_out), .out(diodebackward_399_out));
  DiodeBackward diodebackward_400 (.in(not_170_out[0]), .out(diodebackward_399_out));
  DiodeBackward diodebackward_401 (.in(nRES_3), .out(diodebackward_399_out));
  PullUp pullup_136 (.out(diodebackward_391_out));
  not not_154 (not_154_out, diodebackward_391_out);
  PullUp pullup_137 (.out(diodebackward_393_out));
  not not_155 (not_155_out, diodebackward_393_out);
  PullUp pullup_138 (.out(diodebackward_396_out));
  not not_156 (not_156_out, diodebackward_396_out);
  PullUp pullup_139 (.out(diodebackward_399_out));
  not not_157 (not_157_out, diodebackward_399_out);
  DiodeBackward diodebackward_402 (.in(not_155_out), .out(diodebackward_402_out));
  DiodeBackward diodebackward_403 (.in(not_159_out), .out(diodebackward_402_out));
  DiodeBackward diodebackward_404 (.in(not_170_out[1]), .out(diodebackward_404_out));
  DiodeBackward diodebackward_405 (.in(not_156_out), .out(diodebackward_404_out));
  DiodeBackward diodebackward_406 (.in(nRES_3), .out(diodebackward_404_out));
  PullUp pullup_140 (.out(diodebackward_402_out));
  not not_158 (not_170_out[1], diodebackward_402_out);
  PullUp pullup_141 (.out(diodebackward_404_out));
  not not_159 (not_159_out, diodebackward_404_out);
  LED Q9 (.in(not_170_out[1]));
  DiodeBackward diodebackward_407 (.in(not_163_out), .out(diodebackward_407_out));
  DiodeBackward diodebackward_408 (.in(not_161_out), .out(diodebackward_407_out));
  DiodeBackward diodebackward_409 (.in(not_160_out), .out(diodebackward_409_out));
  DiodeBackward diodebackward_410 (.in(CLK_6), .out(diodebackward_409_out));
  DiodeBackward diodebackward_411 (.in(nRES_3), .out(diodebackward_409_out));
  DiodeBackward diodebackward_412 (.in(not_161_out), .out(diodebackward_412_out));
  DiodeBackward diodebackward_413 (.in(CLK_6), .out(diodebackward_412_out));
  DiodeBackward diodebackward_414 (.in(not_163_out), .out(diodebackward_412_out));
  DiodeBackward diodebackward_415 (.in(not_162_out), .out(diodebackward_415_out));
  DiodeBackward diodebackward_416 (.in(not_170_out[1]), .out(diodebackward_415_out));
  DiodeBackward diodebackward_417 (.in(nRES_3), .out(diodebackward_415_out));
  PullUp pullup_142 (.out(diodebackward_407_out));
  not not_160 (not_160_out, diodebackward_407_out);
  PullUp pullup_143 (.out(diodebackward_409_out));
  not not_161 (not_161_out, diodebackward_409_out);
  PullUp pullup_144 (.out(diodebackward_412_out));
  not not_162 (not_162_out, diodebackward_412_out);
  PullUp pullup_145 (.out(diodebackward_415_out));
  not not_163 (not_163_out, diodebackward_415_out);
  DiodeBackward diodebackward_418 (.in(not_161_out), .out(diodebackward_418_out));
  DiodeBackward diodebackward_419 (.in(not_165_out), .out(diodebackward_418_out));
  DiodeBackward diodebackward_420 (.in(not_170_out[2]), .out(diodebackward_420_out));
  DiodeBackward diodebackward_421 (.in(not_162_out), .out(diodebackward_420_out));
  DiodeBackward diodebackward_422 (.in(nRES_3), .out(diodebackward_420_out));
  PullUp pullup_146 (.out(diodebackward_418_out));
  not not_164 (not_170_out[2], diodebackward_418_out);
  PullUp pullup_147 (.out(diodebackward_420_out));
  not not_165 (not_165_out, diodebackward_420_out);
  LED Q10 (.in(not_170_out[2]));
  PullUp pullup_148 (.out(pullup_148_out));
  DiodeBackward diodebackward_423 (.in(not_169_out), .out(pullup_148_out));
  DiodeBackward diodebackward_424 (.in(not_167_out), .out(pullup_148_out));
  PullUp pullup_149 (.out(pullup_149_out));
  DiodeBackward diodebackward_425 (.in(not_166_out), .out(pullup_149_out));
  DiodeBackward diodebackward_426 (.in(CLK_6), .out(pullup_149_out));
  DiodeBackward diodebackward_427 (.in(nRES_3), .out(pullup_149_out));
  PullUp pullup_150 (.out(pullup_150_out));
  DiodeBackward diodebackward_428 (.in(not_167_out), .out(pullup_150_out));
  DiodeBackward diodebackward_429 (.in(CLK_6), .out(pullup_150_out));
  DiodeBackward diodebackward_430 (.in(not_169_out), .out(pullup_150_out));
  PullUp pullup_151 (.out(pullup_151_out));
  DiodeBackward diodebackward_431 (.in(not_168_out), .out(pullup_151_out));
  DiodeBackward diodebackward_432 (.in(not_170_out[2]), .out(pullup_151_out));
  DiodeBackward diodebackward_433 (.in(nRES_3), .out(pullup_151_out));
  not not_166 (not_166_out, pullup_148_out);
  not not_167 (not_167_out, pullup_149_out);
  not not_168 (not_168_out, pullup_150_out);
  not not_169 (not_169_out, pullup_151_out);
  PullUp pullup_152 (.out(pullup_152_out));
  DiodeBackward diodebackward_434 (.in(not_167_out), .out(pullup_152_out));
  DiodeBackward diodebackward_435 (.in(not_171_out), .out(pullup_152_out));
  PullUp pullup_153 (.out(pullup_153_out));
  DiodeBackward diodebackward_436 (.in(not_170_out[3]), .out(pullup_153_out));
  DiodeBackward diodebackward_437 (.in(not_168_out), .out(pullup_153_out));
  DiodeBackward diodebackward_438 (.in(nRES_3), .out(pullup_153_out));
  not not_170 (not_170_out[3], pullup_152_out);
  not not_171 (not_171_out, pullup_153_out);
  LED Q11 (.in(not_170_out[3]));
  DiodeBackward diodebackward_439 (.in(not_175_out), .out(diodebackward_439_out));
  DiodeBackward diodebackward_440 (.in(not_173_out), .out(diodebackward_439_out));
  DiodeBackward diodebackward_441 (.in(not_172_out), .out(diodebackward_441_out));
  DiodeBackward diodebackward_442 (.in(CLK_6), .out(diodebackward_441_out));
  DiodeBackward diodebackward_443 (.in(nRES_3), .out(diodebackward_441_out));
  DiodeBackward diodebackward_444 (.in(not_173_out), .out(diodebackward_444_out));
  DiodeBackward diodebackward_445 (.in(CLK_6), .out(diodebackward_444_out));
  DiodeBackward diodebackward_446 (.in(not_175_out), .out(diodebackward_444_out));
  DiodeBackward diodebackward_447 (.in(not_174_out), .out(diodebackward_447_out));
  DiodeBackward diodebackward_448 (.in(not_170_out[3]), .out(diodebackward_447_out));
  DiodeBackward diodebackward_449 (.in(nRES_3), .out(diodebackward_447_out));
  PullUp pullup_154 (.out(diodebackward_439_out));
  not not_172 (not_172_out, diodebackward_439_out);
  PullUp pullup_155 (.out(diodebackward_441_out));
  not not_173 (not_173_out, diodebackward_441_out);
  PullUp pullup_156 (.out(diodebackward_444_out));
  not not_174 (not_174_out, diodebackward_444_out);
  PullUp pullup_157 (.out(diodebackward_447_out));
  not not_175 (not_175_out, diodebackward_447_out);
  Seven_Seg_Hex seven_seg_hex_4 (.d(not_176_out), .dp(1'b0));
  DiodeBackward diodebackward_450 (.in(not_173_out), .out(diodebackward_450_out));
  DiodeBackward diodebackward_451 (.in(not_177_out), .out(diodebackward_450_out));
  DiodeBackward diodebackward_452 (.in(not_176_out[0]), .out(diodebackward_452_out));
  DiodeBackward diodebackward_453 (.in(not_174_out), .out(diodebackward_452_out));
  DiodeBackward diodebackward_454 (.in(nRES_3), .out(diodebackward_452_out));
  PullUp pullup_158 (.out(diodebackward_450_out));
  not not_176 (not_176_out[0], diodebackward_450_out);
  PullUp pullup_159 (.out(diodebackward_452_out));
  not not_177 (not_177_out, diodebackward_452_out);
  LED Q12 (.in(not_176_out[0]));
  DiodeBackward diodebackward_455 (.in(not_181_out), .out(diodebackward_455_out));
  DiodeBackward diodebackward_456 (.in(not_179_out), .out(diodebackward_455_out));
  DiodeBackward diodebackward_457 (.in(not_178_out), .out(diodebackward_457_out));
  DiodeBackward diodebackward_458 (.in(CLK_6), .out(diodebackward_457_out));
  DiodeBackward diodebackward_459 (.in(nRES_3), .out(diodebackward_457_out));
  DiodeBackward diodebackward_460 (.in(not_179_out), .out(diodebackward_460_out));
  DiodeBackward diodebackward_461 (.in(CLK_6), .out(diodebackward_460_out));
  DiodeBackward diodebackward_462 (.in(not_181_out), .out(diodebackward_460_out));
  DiodeBackward diodebackward_463 (.in(not_180_out), .out(diodebackward_463_out));
  DiodeBackward diodebackward_464 (.in(not_176_out[0]), .out(diodebackward_463_out));
  DiodeBackward diodebackward_465 (.in(nRES_3), .out(diodebackward_463_out));
  PullUp pullup_160 (.out(diodebackward_455_out));
  not not_178 (not_178_out, diodebackward_455_out);
  PullUp pullup_161 (.out(diodebackward_457_out));
  not not_179 (not_179_out, diodebackward_457_out);
  PullUp pullup_162 (.out(diodebackward_460_out));
  not not_180 (not_180_out, diodebackward_460_out);
  PullUp pullup_163 (.out(diodebackward_463_out));
  not not_181 (not_181_out, diodebackward_463_out);
  DiodeBackward diodebackward_466 (.in(not_179_out), .out(diodebackward_466_out));
  DiodeBackward diodebackward_467 (.in(not_183_out), .out(diodebackward_466_out));
  DiodeBackward diodebackward_468 (.in(not_176_out[1]), .out(diodebackward_468_out));
  DiodeBackward diodebackward_469 (.in(not_180_out), .out(diodebackward_468_out));
  DiodeBackward diodebackward_470 (.in(nRES_3), .out(diodebackward_468_out));
  PullUp pullup_164 (.out(diodebackward_466_out));
  not not_182 (not_176_out[1], diodebackward_466_out);
  PullUp pullup_165 (.out(diodebackward_468_out));
  not not_183 (not_183_out, diodebackward_468_out);
  LED Q13 (.in(not_176_out[1]));
  PullUp pullup_166 (.out(pullup_166_out));
  not not_184 (not_184_out, pullup_166_out);
  DiodeBackward diodebackward_471 (.in(not_187_out), .out(pullup_166_out));
  DiodeBackward diodebackward_472 (.in(not_185_out), .out(pullup_166_out));
  PullUp pullup_167 (.out(pullup_167_out));
  DiodeBackward diodebackward_473 (.in(not_184_out), .out(pullup_167_out));
  not not_185 (not_185_out, pullup_167_out);
  DiodeBackward diodebackward_474 (.in(CLK_6), .out(pullup_167_out));
  DiodeBackward diodebackward_475 (.in(nRES_3), .out(pullup_167_out));
  PullUp pullup_168 (.out(pullup_168_out));
  DiodeBackward diodebackward_476 (.in(not_185_out), .out(pullup_168_out));
  not not_186 (not_186_out, pullup_168_out);
  DiodeBackward diodebackward_477 (.in(CLK_6), .out(pullup_168_out));
  DiodeBackward diodebackward_478 (.in(not_187_out), .out(pullup_168_out));
  PullUp pullup_169 (.out(pullup_169_out));
  DiodeBackward diodebackward_479 (.in(not_186_out), .out(pullup_169_out));
  not not_187 (not_187_out, pullup_169_out);
  DiodeBackward diodebackward_480 (.in(not_176_out[1]), .out(pullup_169_out));
  DiodeBackward diodebackward_481 (.in(nRES_3), .out(pullup_169_out));
  PullUp pullup_170 (.out(pullup_170_out));
  DiodeBackward diodebackward_482 (.in(not_185_out), .out(pullup_170_out));
  not not_188 (not_176_out[2], pullup_170_out);
  DiodeBackward diodebackward_483 (.in(not_189_out), .out(pullup_170_out));
  PullUp pullup_171 (.out(pullup_171_out));
  DiodeBackward diodebackward_484 (.in(not_176_out[2]), .out(pullup_171_out));
  not not_189 (not_189_out, pullup_171_out);
  DiodeBackward diodebackward_485 (.in(not_186_out), .out(pullup_171_out));
  DiodeBackward diodebackward_486 (.in(nRES_3), .out(pullup_171_out));
  LED Q14 (.in(not_176_out[2]));
  DiodeBackward diodebackward_487 (.in(not_193_out), .out(diodebackward_487_out));
  DiodeBackward diodebackward_488 (.in(not_191_out), .out(diodebackward_487_out));
  DiodeBackward diodebackward_489 (.in(not_190_out), .out(diodebackward_489_out));
  DiodeBackward diodebackward_490 (.in(CLK_6), .out(diodebackward_489_out));
  DiodeBackward diodebackward_491 (.in(nRES_3), .out(diodebackward_489_out));
  DiodeBackward diodebackward_492 (.in(not_191_out), .out(diodebackward_492_out));
  DiodeBackward diodebackward_493 (.in(CLK_6), .out(diodebackward_492_out));
  DiodeBackward diodebackward_494 (.in(not_193_out), .out(diodebackward_492_out));
  DiodeBackward diodebackward_495 (.in(not_192_out), .out(diodebackward_495_out));
  DiodeBackward diodebackward_496 (.in(not_176_out[2]), .out(diodebackward_495_out));
  DiodeBackward diodebackward_497 (.in(nRES_3), .out(diodebackward_495_out));
  PullUp pullup_172 (.out(diodebackward_487_out));
  not not_190 (not_190_out, diodebackward_487_out);
  PullUp pullup_173 (.out(diodebackward_489_out));
  not not_191 (not_191_out, diodebackward_489_out);
  PullUp pullup_174 (.out(diodebackward_492_out));
  not not_192 (not_192_out, diodebackward_492_out);
  PullUp pullup_175 (.out(diodebackward_495_out));
  not not_193 (not_193_out, diodebackward_495_out);
  DiodeBackward diodebackward_498 (.in(not_191_out), .out(diodebackward_498_out));
  DiodeBackward diodebackward_499 (.in(not_195_out), .out(diodebackward_498_out));
  DiodeBackward diodebackward_500 (.in(not_176_out[3]), .out(diodebackward_500_out));
  DiodeBackward diodebackward_501 (.in(not_192_out), .out(diodebackward_500_out));
  DiodeBackward diodebackward_502 (.in(nRES_3), .out(diodebackward_500_out));
  PullUp pullup_176 (.out(diodebackward_498_out));
  not not_194 (not_176_out[3], diodebackward_498_out);
  PullUp pullup_177 (.out(diodebackward_500_out));
  not not_195 (not_195_out, diodebackward_500_out);
  LED Q15 (.in(not_176_out[3]));

  // Notes on the sheet:
  //   1 of 8 selector (74xx151)
  //   4 bit counter with asynchronous reset
  //   3 to 8 line decoder (74xx138)
  //   Dual 4 input multiplexer (74xx153)
  //   AND-OR / Data Selector
  //   Full Adder (74xx80)
  //   4 bit Shift Register
  //   Gated Latch
  //   Edge Triggered Master-Slave Flip Flop
  //   Full Adder
  //   SR Flip Flop
  //   AND-OR Selector
  //   00      Zero
  //   01       XOR/ADD
  //   10      AND
  //   11      OR
  //   Edge Triggered D-type Flip Flop
  //   8 bit Shift Register
endmodule
