// Digital circuit DTL_4NAND.dig as structural Verilog
module DTL_4NAND (
  input  in_1,
  input  in_2,
  input  in_3,
  input  in_4,
  output out_5
);

  wire pullup_1_out;

  PullUp pullup_1 (.out(pullup_1_out));
  DiodeBackward diodebackward_1 (.in(in_1), .out(pullup_1_out));
  not not_1 (out_5, pullup_1_out);
  DiodeBackward diodebackward_2 (.in(in_2), .out(pullup_1_out));
  DiodeBackward diodebackward_3 (.in(in_3), .out(pullup_1_out));
  DiodeBackward diodebackward_4 (.in(in_4), .out(pullup_1_out));

  // Notes on the sheet:
  //   4-Input NAND
endmodule
