// Digital circuit DTL_74163.dig as structural Verilog
module DTL_74163 (
  input  nLD_COUNT,
  input  RES,
  input  INC,
  input  D0,
  input  D1,
  input  D2,
  input  D3,
  input  CLK,
  input  clk_2,
  output Q0,
  output Q1,
  output Q2,
  output Q3
);

  wire diodebackward_9_out, diodebackward_11_out, diodebackward_13_out, diodebackward_15_out,
       diodebackward_17_out, diodebackward_19_out, diodebackward_21_out, diodebackward_23_out,
       diodebackward_25_out, diodebackward_27_out, diodebackward_29_out, diodebackward_31_out,
       diodebackward_101_out, diodebackward_103_out, diodebackward_106_out, diodebackward_108_out,
       diodebackward_111_out, diodebackward_113_out, diodebackward_116_out, diodebackward_118_out, not_1_out,
       not_2_out, not_3_out, not_4_out, not_5_out, not_6_out, not_7_out, not_8_out, not_9_out, not_10_out,
       not_11_out, not_12_out, not_13_out, not_14_out, not_15_out, not_16_out, not_17_out, not_18_out,
       not_19_out, not_20_out, not_21_out, not_22_out, not_23_out, not_24_out, not_25_out, not_26_out,
       not_27_out, not_28_out, not_29_out, not_30_out, not_31_out, not_32_out, not_33_out, not_34_out,
       not_35_out, not_36_out, not_37_out, not_38_out, not_39_out, not_40_out, not_41_out, not_42_out,
       not_43_out, not_44_out, not_45_out, not_46_out, not_47_out, not_48_out, not_49_out, not_50_out,
       not_51_out, not_52_out, not_54_out, not_56_out, not_58_out, not_60_out, pullup_1_out, pullup_2_out,
       pullup_3_out, pullup_4_out, pullup_17_out, pullup_18_out, pullup_19_out, pullup_20_out, pullup_21_out,
       pullup_22_out, pullup_23_out, pullup_24_out, pullup_25_out, pullup_26_out, pullup_27_out,
       pullup_28_out, pullup_29_out, pullup_30_out, pullup_31_out, pullup_32_out, pullup_33_out,
       pullup_34_out, pullup_35_out, pullup_36_out, pullup_37_out, pullup_38_out, pullup_39_out,
       pullup_40_out, pullup_41_out, pullup_42_out, pullup_43_out, pullup_44_out;

  PullUp pullup_1 (.out(pullup_1_out));
  DiodeBackward diodebackward_1 (.in(INC), .out(pullup_1_out));
  DiodeBackward diodebackward_2 (.in(Q0), .out(pullup_1_out));
  PullUp pullup_2 (.out(pullup_2_out));
  DiodeBackward diodebackward_3 (.in(not_2_out), .out(pullup_2_out));
  DiodeBackward diodebackward_4 (.in(Q1), .out(pullup_2_out));
  PullUp pullup_3 (.out(pullup_3_out));
  DiodeBackward diodebackward_5 (.in(not_4_out), .out(pullup_3_out));
  DiodeBackward diodebackward_6 (.in(Q2), .out(pullup_3_out));
  PullUp pullup_4 (.out(pullup_4_out));
  DiodeBackward diodebackward_7 (.in(not_6_out), .out(pullup_4_out));
  DiodeBackward diodebackward_8 (.in(Q3), .out(pullup_4_out));
  not not_1 (not_1_out, pullup_1_out);
  not not_2 (not_2_out, not_1_out);
  not not_3 (not_3_out, pullup_2_out);
  not not_4 (not_4_out, not_3_out);
  not not_5 (not_5_out, pullup_3_out);
  not not_6 (not_6_out, not_5_out);
  not not_7 (not_7_out, pullup_4_out);
  not not_8 (not_8_out, not_7_out);
  DiodeBackward diodebackward_9 (.in(INC), .out(diodebackward_9_out));
  DiodeBackward diodebackward_10 (.in(not_1_out), .out(diodebackward_9_out));
  DiodeBackward diodebackward_11 (.in(not_1_out), .out(diodebackward_11_out));
  DiodeBackward diodebackward_12 (.in(Q0), .out(diodebackward_11_out));
  DiodeBackward diodebackward_13 (.in(not_2_out), .out(diodebackward_13_out));
  DiodeBackward diodebackward_14 (.in(not_3_out), .out(diodebackward_13_out));
  DiodeBackward diodebackward_15 (.in(not_3_out), .out(diodebackward_15_out));
  DiodeBackward diodebackward_16 (.in(Q1), .out(diodebackward_15_out));
  DiodeBackward diodebackward_17 (.in(not_4_out), .out(diodebackward_17_out));
  DiodeBackward diodebackward_18 (.in(not_5_out), .out(diodebackward_17_out));
  DiodeBackward diodebackward_19 (.in(not_5_out), .out(diodebackward_19_out));
  DiodeBackward diodebackward_20 (.in(Q2), .out(diodebackward_19_out));
  DiodeBackward diodebackward_21 (.in(not_6_out), .out(diodebackward_21_out));
  DiodeBackward diodebackward_22 (.in(not_7_out), .out(diodebackward_21_out));
  DiodeBackward diodebackward_23 (.in(not_7_out), .out(diodebackward_23_out));
  DiodeBackward diodebackward_24 (.in(Q3), .out(diodebackward_23_out));
  PullUp pullup_5 (.out(diodebackward_9_out));
  not not_9 (not_9_out, diodebackward_9_out);
  PullUp pullup_6 (.out(diodebackward_11_out));
  not not_10 (not_10_out, diodebackward_11_out);
  PullUp pullup_7 (.out(diodebackward_13_out));
  not not_11 (not_11_out, diodebackward_13_out);
  PullUp pullup_8 (.out(diodebackward_15_out));
  not not_12 (not_12_out, diodebackward_15_out);
  PullUp pullup_9 (.out(diodebackward_17_out));
  not not_13 (not_13_out, diodebackward_17_out);
  PullUp pullup_10 (.out(diodebackward_19_out));
  not not_14 (not_14_out, diodebackward_19_out);
  PullUp pullup_11 (.out(diodebackward_21_out));
  not not_15 (not_15_out, diodebackward_21_out);
  PullUp pullup_12 (.out(diodebackward_23_out));
  not not_16 (not_16_out, diodebackward_23_out);
  DiodeBackward diodebackward_25 (.in(not_9_out), .out(diodebackward_25_out));
  DiodeBackward diodebackward_26 (.in(not_10_out), .out(diodebackward_25_out));
  DiodeBackward diodebackward_27 (.in(not_11_out), .out(diodebackward_27_out));
  DiodeBackward diodebackward_28 (.in(not_12_out), .out(diodebackward_27_out));
  DiodeBackward diodebackward_29 (.in(not_13_out), .out(diodebackward_29_out));
  DiodeBackward diodebackward_30 (.in(not_14_out), .out(diodebackward_29_out));
  DiodeBackward diodebackward_31 (.in(not_15_out), .out(diodebackward_31_out));
  DiodeBackward diodebackward_32 (.in(not_16_out), .out(diodebackward_31_out));
  PullUp pullup_13 (.out(diodebackward_25_out));
  not not_17 (not_17_out, diodebackward_25_out);
  PullUp pullup_14 (.out(diodebackward_27_out));
  not not_18 (not_18_out, diodebackward_27_out);
  PullUp pullup_15 (.out(diodebackward_29_out));
  not not_19 (not_19_out, diodebackward_29_out);
  PullUp pullup_16 (.out(diodebackward_31_out));
  not not_20 (not_20_out, diodebackward_31_out);
  not not_21 (not_21_out, nLD_COUNT);
  not not_22 (not_22_out, nLD_COUNT);
  not not_23 (not_23_out, nLD_COUNT);
  not not_24 (not_24_out, nLD_COUNT);
  PullUp pullup_17 (.out(pullup_17_out));
  DiodeBackward diodebackward_33 (.in(not_17_out), .out(pullup_17_out));
  not not_25 (not_25_out, pullup_17_out);
  DiodeBackward diodebackward_34 (.in(nLD_COUNT), .out(pullup_17_out));
  PullUp pullup_18 (.out(pullup_18_out));
  DiodeBackward diodebackward_35 (.in(not_21_out), .out(pullup_18_out));
  not not_26 (not_26_out, pullup_18_out);
  DiodeBackward diodebackward_36 (.in(D0), .out(pullup_18_out));
  PullUp pullup_19 (.out(pullup_19_out));
  DiodeBackward diodebackward_37 (.in(not_18_out), .out(pullup_19_out));
  not not_27 (not_27_out, pullup_19_out);
  DiodeBackward diodebackward_38 (.in(nLD_COUNT), .out(pullup_19_out));
  PullUp pullup_20 (.out(pullup_20_out));
  DiodeBackward diodebackward_39 (.in(not_22_out), .out(pullup_20_out));
  not not_28 (not_28_out, pullup_20_out);
  DiodeBackward diodebackward_40 (.in(D1), .out(pullup_20_out));
  PullUp pullup_21 (.out(pullup_21_out));
  DiodeBackward diodebackward_41 (.in(not_19_out), .out(pullup_21_out));
  not not_29 (not_29_out, pullup_21_out);
  DiodeBackward diodebackward_42 (.in(nLD_COUNT), .out(pullup_21_out));
  PullUp pullup_22 (.out(pullup_22_out));
  DiodeBackward diodebackward_43 (.in(not_23_out), .out(pullup_22_out));
  not not_30 (not_30_out, pullup_22_out);
  DiodeBackward diodebackward_44 (.in(D2), .out(pullup_22_out));
  PullUp pullup_23 (.out(pullup_23_out));
  DiodeBackward diodebackward_45 (.in(not_20_out), .out(pullup_23_out));
  not not_31 (not_31_out, pullup_23_out);
  DiodeBackward diodebackward_46 (.in(nLD_COUNT), .out(pullup_23_out));
  PullUp pullup_24 (.out(pullup_24_out));
  DiodeBackward diodebackward_47 (.in(not_24_out), .out(pullup_24_out));
  not not_32 (not_32_out, pullup_24_out);
  DiodeBackward diodebackward_48 (.in(D3), .out(pullup_24_out));
  PullUp pullup_25 (.out(pullup_25_out));
  DiodeBackward diodebackward_49 (.in(not_25_out), .out(pullup_25_out));
  not not_33 (not_33_out, pullup_25_out);
  DiodeBackward diodebackward_50 (.in(not_26_out), .out(pullup_25_out));
  PullUp pullup_26 (.out(pullup_26_out));
  DiodeBackward diodebackward_51 (.in(not_27_out), .out(pullup_26_out));
  not not_34 (not_34_out, pullup_26_out);
  DiodeBackward diodebackward_52 (.in(not_28_out), .out(pullup_26_out));
  PullUp pullup_27 (.out(pullup_27_out));
  DiodeBackward diodebackward_53 (.in(not_29_out), .out(pullup_27_out));
  not not_35 (not_35_out, pullup_27_out);
  DiodeBackward diodebackward_54 (.in(not_30_out), .out(pullup_27_out));
  PullUp pullup_28 (.out(pullup_28_out));
  DiodeBackward diodebackward_55 (.in(not_31_out), .out(pullup_28_out));
  not not_36 (not_36_out, pullup_28_out);
  DiodeBackward diodebackward_56 (.in(not_32_out), .out(pullup_28_out));
  PullUp pullup_29 (.out(pullup_29_out));
  not not_37 (not_37_out, pullup_29_out);
  DiodeBackward diodebackward_57 (.in(not_40_out), .out(pullup_29_out));
  DiodeBackward diodebackward_58 (.in(not_38_out), .out(pullup_29_out));
  PullUp pullup_30 (.out(pullup_30_out));
  DiodeBackward diodebackward_59 (.in(not_37_out), .out(pullup_30_out));
  not not_38 (not_38_out, pullup_30_out);
  DiodeBackward diodebackward_60 (.in(clk_2), .out(pullup_30_out));
  DiodeBackward diodebackward_61 (.in(RES), .out(pullup_30_out));
  PullUp pullup_31 (.out(pullup_31_out));
  DiodeBackward diodebackward_62 (.in(not_38_out), .out(pullup_31_out));
  not not_39 (not_39_out, pullup_31_out);
  DiodeBackward diodebackward_63 (.in(clk_2), .out(pullup_31_out));
  DiodeBackward diodebackward_64 (.in(not_40_out), .out(pullup_31_out));
  PullUp pullup_32 (.out(pullup_32_out));
  DiodeBackward diodebackward_65 (.in(not_39_out), .out(pullup_32_out));
  not not_40 (not_40_out, pullup_32_out);
  DiodeBackward diodebackward_66 (.in(not_33_out), .out(pullup_32_out));
  DiodeBackward diodebackward_67 (.in(RES), .out(pullup_32_out));
  PullUp pullup_33 (.out(pullup_33_out));
  not not_41 (not_41_out, pullup_33_out);
  DiodeBackward diodebackward_68 (.in(not_44_out), .out(pullup_33_out));
  DiodeBackward diodebackward_69 (.in(not_42_out), .out(pullup_33_out));
  PullUp pullup_34 (.out(pullup_34_out));
  DiodeBackward diodebackward_70 (.in(not_41_out), .out(pullup_34_out));
  not not_42 (not_42_out, pullup_34_out);
  DiodeBackward diodebackward_71 (.in(clk_2), .out(pullup_34_out));
  DiodeBackward diodebackward_72 (.in(RES), .out(pullup_34_out));
  PullUp pullup_35 (.out(pullup_35_out));
  DiodeBackward diodebackward_73 (.in(not_42_out), .out(pullup_35_out));
  not not_43 (not_43_out, pullup_35_out);
  DiodeBackward diodebackward_74 (.in(clk_2), .out(pullup_35_out));
  DiodeBackward diodebackward_75 (.in(not_44_out), .out(pullup_35_out));
  PullUp pullup_36 (.out(pullup_36_out));
  DiodeBackward diodebackward_76 (.in(not_43_out), .out(pullup_36_out));
  not not_44 (not_44_out, pullup_36_out);
  DiodeBackward diodebackward_77 (.in(not_34_out), .out(pullup_36_out));
  DiodeBackward diodebackward_78 (.in(RES), .out(pullup_36_out));
  PullUp pullup_37 (.out(pullup_37_out));
  not not_45 (not_45_out, pullup_37_out);
  DiodeBackward diodebackward_79 (.in(not_48_out), .out(pullup_37_out));
  DiodeBackward diodebackward_80 (.in(not_46_out), .out(pullup_37_out));
  PullUp pullup_38 (.out(pullup_38_out));
  DiodeBackward diodebackward_81 (.in(not_45_out), .out(pullup_38_out));
  not not_46 (not_46_out, pullup_38_out);
  DiodeBackward diodebackward_82 (.in(clk_2), .out(pullup_38_out));
  DiodeBackward diodebackward_83 (.in(RES), .out(pullup_38_out));
  PullUp pullup_39 (.out(pullup_39_out));
  DiodeBackward diodebackward_84 (.in(not_46_out), .out(pullup_39_out));
  not not_47 (not_47_out, pullup_39_out);
  DiodeBackward diodebackward_85 (.in(clk_2), .out(pullup_39_out));
  DiodeBackward diodebackward_86 (.in(not_48_out), .out(pullup_39_out));
  PullUp pullup_40 (.out(pullup_40_out));
  DiodeBackward diodebackward_87 (.in(not_47_out), .out(pullup_40_out));
  not not_48 (not_48_out, pullup_40_out);
  DiodeBackward diodebackward_88 (.in(not_35_out), .out(pullup_40_out));
  DiodeBackward diodebackward_89 (.in(RES), .out(pullup_40_out));
  PullUp pullup_41 (.out(pullup_41_out));
  not not_49 (not_49_out, pullup_41_out);
  DiodeBackward diodebackward_90 (.in(not_52_out), .out(pullup_41_out));
  DiodeBackward diodebackward_91 (.in(not_50_out), .out(pullup_41_out));
  PullUp pullup_42 (.out(pullup_42_out));
  DiodeBackward diodebackward_92 (.in(not_49_out), .out(pullup_42_out));
  not not_50 (not_50_out, pullup_42_out);
  DiodeBackward diodebackward_93 (.in(clk_2), .out(pullup_42_out));
  DiodeBackward diodebackward_94 (.in(RES), .out(pullup_42_out));
  PullUp pullup_43 (.out(pullup_43_out));
  DiodeBackward diodebackward_95 (.in(not_50_out), .out(pullup_43_out));
  not not_51 (not_51_out, pullup_43_out);
  DiodeBackward diodebackward_96 (.in(clk_2), .out(pullup_43_out));
  DiodeBackward diodebackward_97 (.in(not_52_out), .out(pullup_43_out));
  PullUp pullup_44 (.out(pullup_44_out));
  DiodeBackward diodebackward_98 (.in(not_51_out), .out(pullup_44_out));
  not not_52 (not_52_out, pullup_44_out);
  DiodeBackward diodebackward_99 (.in(not_36_out), .out(pullup_44_out));
  DiodeBackward diodebackward_100 (.in(RES), .out(pullup_44_out));
  DiodeBackward diodebackward_101 (.in(not_38_out), .out(diodebackward_101_out));
  DiodeBackward diodebackward_102 (.in(not_54_out), .out(diodebackward_101_out));
  DiodeBackward diodebackward_103 (.in(Q0), .out(diodebackward_103_out));
  DiodeBackward diodebackward_104 (.in(not_39_out), .out(diodebackward_103_out));
  DiodeBackward diodebackward_105 (.in(RES), .out(diodebackward_103_out));
  DiodeBackward diodebackward_106 (.in(not_42_out), .out(diodebackward_106_out));
  DiodeBackward diodebackward_107 (.in(not_56_out), .out(diodebackward_106_out));
  DiodeBackward diodebackward_108 (.in(Q1), .out(diodebackward_108_out));
  DiodeBackward diodebackward_109 (.in(not_43_out), .out(diodebackward_108_out));
  DiodeBackward diodebackward_110 (.in(RES), .out(diodebackward_108_out));
  DiodeBackward diodebackward_111 (.in(not_46_out), .out(diodebackward_111_out));
  DiodeBackward diodebackward_112 (.in(not_58_out), .out(diodebackward_111_out));
  DiodeBackward diodebackward_113 (.in(Q2), .out(diodebackward_113_out));
  DiodeBackward diodebackward_114 (.in(not_47_out), .out(diodebackward_113_out));
  DiodeBackward diodebackward_115 (.in(RES), .out(diodebackward_113_out));
  DiodeBackward diodebackward_116 (.in(not_50_out), .out(diodebackward_116_out));
  DiodeBackward diodebackward_117 (.in(not_60_out), .out(diodebackward_116_out));
  DiodeBackward diodebackward_118 (.in(Q3), .out(diodebackward_118_out));
  DiodeBackward diodebackward_119 (.in(not_51_out), .out(diodebackward_118_out));
  DiodeBackward diodebackward_120 (.in(RES), .out(diodebackward_118_out));
  PullUp pullup_45 (.out(diodebackward_101_out));
  not not_53 (Q0, diodebackward_101_out);
  PullUp pullup_46 (.out(diodebackward_103_out));
  not not_54 (not_54_out, diodebackward_103_out);
  PullUp pullup_47 (.out(diodebackward_106_out));
  not not_55 (Q1, diodebackward_106_out);
  PullUp pullup_48 (.out(diodebackward_108_out));
  not not_56 (not_56_out, diodebackward_108_out);
  PullUp pullup_49 (.out(diodebackward_111_out));
  not not_57 (Q2, diodebackward_111_out);
  PullUp pullup_50 (.out(diodebackward_113_out));
  not not_58 (not_58_out, diodebackward_113_out);
  PullUp pullup_51 (.out(diodebackward_116_out));
  not not_59 (Q3, diodebackward_116_out);
  PullUp pullup_52 (.out(diodebackward_118_out));
  not not_60 (not_60_out, diodebackward_118_out);
  Seven_Seg_Hex seven_seg_hex_1 (.d({Q3, Q2, Q1, Q0}), .dp(1'b0));

  // Notes on the sheet:
  //   clk_2: Hz: 2
  //   4-bit Program Counter in 60 gates
  //   Half Adder
  //   Load/Count Multiplexer
  //   Edge Triggered D-type Flip Flop
endmodule
