// Digital circuit DTL_half_adder.dig as structural Verilog
module DTL_half_adder (
  input  B,
  input  A,
  output Fout,
  output Cout
);

  wire diodebackward_1_out, not_1_out, not_2_out, not_3_out, pullup_2_out, pullup_3_out, pullup_4_out,
       pullup_5_out;

  DiodeBackward diodebackward_1 (.in(A), .out(diodebackward_1_out));
  DiodeBackward diodebackward_2 (.in(B), .out(diodebackward_1_out));
  PullUp pullup_1 (.out(diodebackward_1_out));
  not not_1 (not_1_out, diodebackward_1_out);
  PullUp pullup_2 (.out(pullup_2_out));
  DiodeBackward diodebackward_3 (.in(A), .out(pullup_2_out));
  not not_2 (not_2_out, pullup_2_out);
  DiodeBackward diodebackward_4 (.in(not_1_out), .out(pullup_2_out));
  PullUp pullup_3 (.out(pullup_3_out));
  DiodeBackward diodebackward_5 (.in(not_1_out), .out(pullup_3_out));
  not not_3 (not_3_out, pullup_3_out);
  DiodeBackward diodebackward_6 (.in(B), .out(pullup_3_out));
  PullUp pullup_4 (.out(pullup_4_out));
  DiodeBackward diodebackward_7 (.in(not_1_out), .out(pullup_4_out));
  not not_4 (Cout, pullup_4_out);
  PullUp pullup_5 (.out(pullup_5_out));
  DiodeBackward diodebackward_8 (.in(not_2_out), .out(pullup_5_out));
  not not_5 (Fout, pullup_5_out);
  DiodeBackward diodebackward_9 (.in(not_3_out), .out(pullup_5_out));
endmodule
