// Digital circuit Master_Slave_Flip_Flop.dig as structural Verilog
module Master_Slave_Flip_Flop (
  input  Data,
  input  Clock
);

  wire nand_1_out, nand_2_out, nand_3_out, nand_4_out, nand_5_out, nand_6_out, nand_7_out, nand_8_out,
       nand_9_out, nand_10_out;

  nand nand_1 (nand_1_out, Data, Data);
  nand nand_2 (nand_2_out, Clock, Clock);
  nand nand_3 (nand_3_out, Data, nand_2_out);
  nand nand_4 (nand_4_out, nand_2_out, nand_1_out);
  nand nand_5 (nand_5_out, nand_3_out, nand_6_out);
  nand nand_6 (nand_6_out, nand_5_out, nand_4_out);
  nand nand_7 (nand_7_out, nand_5_out, Clock);
  nand nand_8 (nand_8_out, Clock, nand_6_out);
  nand nand_9 (nand_9_out, nand_7_out, nand_10_out);
  nand nand_10 (nand_10_out, nand_9_out, nand_8_out);
  LED led_1 (.in(nand_9_out));

  // Notes on the sheet:
  //   Master
  //   Slave
  //   Q
  //   ~Q
endmodule
