// Digital circuit UD_counter.dig as structural Verilog
module UD_counter (
  input  in_1,
  input  in_2,
  input  in_3,
  input  in_4,
  input  in_5,
  input  in_6,
  input  in_7,
  input  in_8,
  input  in_9,
  input  in_10,
  input  in_11,
  input  in_12,
  input  in_13,
  input  in_14,
  input  in_15,
  input  in_16,
  input  in_17,
  input  in_18,
  input  in_19,
  input  in_20,
  input  in_21,
  input  in_22,
  input  in_23,
  input  in_24,
  input  in_25,
  input  in_26,
  input  in_27,
  input  in_28,
  input  in_29,
  input  in_30,
  input  in_31,
  input  in_32,
  input  CLK,
  input  in_34
);

  wire _74173_1_pin11, _74173_1_pin12, _74173_1_pin13, _74173_1_pin14, _74173_2_pin11, _74173_2_pin12,
       _74173_2_pin13, _74173_2_pin14, _74173_3_pin11, _74173_3_pin12, _74173_3_pin13, _74173_3_pin14,
       _74173_4_pin11, _74173_4_pin12, _74173_4_pin13, _74173_4_pin14, _74193_1_pin1, _74193_1_pin9,
       _74193_1_pin10, _74193_1_pin12, _74193_1_pin13, _74193_1_pin15, _74193_2_pin1, _74193_2_pin9,
       _74193_2_pin10, _74193_2_pin12, _74193_2_pin13, _74193_2_pin15, _74193_3_pin1, _74193_3_pin9,
       _74193_3_pin10, _74193_3_pin12, _74193_3_pin13, _74193_3_pin15, _74193_4_pin1, _74193_4_pin9,
       _74193_4_pin10, _74193_4_pin15, _74541_1_pin11, _74541_1_pin12, _74541_1_pin13, _74541_1_pin14,
       _74541_1_pin15, _74541_1_pin16, _74541_1_pin17, _74541_1_pin18, _74541_2_pin11, _74541_2_pin12,
       _74541_2_pin13, _74541_2_pin14, _74541_2_pin15, _74541_2_pin16, _74541_2_pin17, _74541_2_pin18,
       IC1_pin11, IC1_pin12, IC1_pin13, IC1_pin14, IC2_pin7, IC2_pin9, IC2_pin10, IC2_pin11, IC2_pin12,
       IC2_pin13, IC2_pin14, IC2_pin15;
  wire [3:0] _74193_1_pin7, _74193_2_pin7, _74193_3_pin7, _74193_4_pin7;

  _74161 IC1 (
    .pin1(1'b1), .pin2(CLK), .pin3(in_29), .pin4(in_30), .pin5(in_31), .pin6(in_32), .pin7(1'b1),
    .pin8(1'b0), .pin9(1'b1), .pin10(1'b1), .pin11(IC1_pin11), .pin12(IC1_pin12), .pin13(IC1_pin13),
    .pin14(IC1_pin14), .pin16(1'b1));  // open: pin15
  _74138 IC2 (
    .pin1(IC1_pin14), .pin2(IC1_pin13), .pin3(IC1_pin12), .pin4(1'b0), .pin5(1'b0), .pin6(CLK),
    .pin7(IC2_pin7), .pin8(1'b0), .pin9(IC2_pin9), .pin10(IC2_pin10), .pin11(IC2_pin11), .pin12(IC2_pin12),
    .pin13(IC2_pin13), .pin14(IC2_pin14), .pin15(IC2_pin15), .pin16(1'b1));
  // Probe T0 on IC2_pin15
  // Probe T1 on IC2_pin14
  // Probe T2 on IC2_pin13
  // Probe T3 on IC2_pin12
  // Probe T4 on IC2_pin11
  // Probe T5 on IC2_pin10
  // Probe T6 on IC2_pin9
  // Probe T7 on IC2_pin7
  LED led_1 (.in(IC2_pin15));
  LED led_2 (.in(IC2_pin14));
  LED led_3 (.in(IC2_pin13));
  LED led_4 (.in(IC2_pin12));
  LED led_5 (.in(IC2_pin11));
  LED led_6 (.in(IC2_pin10));
  LED led_7 (.in(IC2_pin9));
  LED led_8 (.in(IC2_pin7));
  _74541 _74541_1 (
    .pin1(in_34), .pin2(in_12), .pin3(in_13), .pin4(in_14), .pin5(in_15), .pin6(in_16), .pin7(in_17),
    .pin8(in_18), .pin9(in_19), .pin10(1'b0), .pin11(_74541_1_pin11), .pin12(_74541_1_pin12),
    .pin13(_74541_1_pin13), .pin14(_74541_1_pin14), .pin15(_74541_1_pin15), .pin16(_74541_1_pin16),
    .pin17(_74541_1_pin17), .pin18(_74541_1_pin18), .pin19(in_34), .pin20(1'b1));
  _74541 _74541_2 (
    .pin1(in_34), .pin2(in_20), .pin3(in_21), .pin4(in_22), .pin5(in_23), .pin6(in_24), .pin7(in_25),
    .pin8(in_26), .pin9(in_27), .pin10(1'b0), .pin11(_74541_2_pin11), .pin12(_74541_2_pin12),
    .pin13(_74541_2_pin13), .pin14(_74541_2_pin14), .pin15(_74541_2_pin15), .pin16(_74541_2_pin16),
    .pin17(_74541_2_pin17), .pin18(_74541_2_pin18), .pin19(in_34), .pin20(1'b1));
  Seven_Seg_Hex seven_seg_hex_1 (.d(_74193_4_pin7), .dp(1'b0));
  Seven_Seg_Hex seven_seg_hex_2 (.d(_74193_3_pin7), .dp(1'b0));
  Seven_Seg_Hex seven_seg_hex_3 (.d(_74193_2_pin7), .dp(1'b0));
  _74193 _74193_1 (
    .pin1(_74193_1_pin1), .pin2(_74193_1_pin7[1]), .pin3(_74193_1_pin7[0]), .pin4(in_1), .pin5(in_2),
    .pin6(_74193_1_pin7[2]), .pin7(_74193_1_pin7[3]), .pin8(1'b0), .pin9(_74193_1_pin9),
    .pin10(_74193_1_pin10), .pin11(in_3), .pin12(_74193_1_pin12), .pin13(_74193_1_pin13), .pin14(in_4),
    .pin15(_74193_1_pin15), .pin16(1'b1));
  Seven_Seg_Hex seven_seg_hex_4 (.d(_74193_1_pin7), .dp(1'b0));
  _74173 _74173_1 (
    .pin1(1'b0), .pin2(1'b0), .pin3(_74193_1_pin15), .pin4(_74193_1_pin1), .pin5(_74193_1_pin10),
    .pin6(_74193_1_pin9), .pin7(in_5), .pin8(1'b0), .pin9(1'b0), .pin10(1'b0), .pin11(_74173_1_pin11),
    .pin12(_74173_1_pin12), .pin13(_74173_1_pin13), .pin14(_74173_1_pin14), .pin15(1'b0), .pin16(1'b1));
  _74219 _74219_1 (
    .pin1(in_8), .pin2(in_6), .pin3(in_7), .pin4(_74541_1_pin18), .pin5(_74173_1_pin14),
    .pin6(_74541_1_pin17), .pin7(_74173_1_pin13), .pin8(1'b0), .pin9(_74173_1_pin12), .pin10(_74541_1_pin16),
    .pin11(_74173_1_pin11), .pin12(_74541_1_pin15), .pin13(in_11), .pin14(in_10), .pin15(in_9), .pin16(1'b1));
  _74193 _74193_2 (
    .pin1(_74193_2_pin1), .pin2(_74193_2_pin7[1]), .pin3(_74193_2_pin7[0]), .pin4(_74193_1_pin13),
    .pin5(_74193_1_pin12), .pin6(_74193_2_pin7[2]), .pin7(_74193_2_pin7[3]), .pin8(1'b0),
    .pin9(_74193_2_pin9), .pin10(_74193_2_pin10), .pin11(in_3), .pin12(_74193_2_pin12),
    .pin13(_74193_2_pin13), .pin14(in_4), .pin15(_74193_2_pin15), .pin16(1'b1));
  _74173 _74173_2 (
    .pin1(1'b0), .pin2(1'b0), .pin3(_74193_2_pin15), .pin4(_74193_2_pin1), .pin5(_74193_2_pin10),
    .pin6(_74193_2_pin9), .pin7(in_5), .pin8(1'b0), .pin9(1'b0), .pin10(1'b0), .pin11(_74173_2_pin11),
    .pin12(_74173_2_pin12), .pin13(_74173_2_pin13), .pin14(_74173_2_pin14), .pin15(1'b0), .pin16(1'b1));
  _74219 _74219_2 (
    .pin1(in_8), .pin2(in_6), .pin3(in_7), .pin4(_74541_1_pin14), .pin5(_74173_2_pin14),
    .pin6(_74541_1_pin13), .pin7(_74173_2_pin13), .pin8(1'b0), .pin9(_74173_2_pin12), .pin10(_74541_1_pin12),
    .pin11(_74173_2_pin11), .pin12(_74541_1_pin11), .pin13(in_11), .pin14(in_10), .pin15(in_9), .pin16(1'b1));
  _74193 _74193_3 (
    .pin1(_74193_3_pin1), .pin2(_74193_3_pin7[1]), .pin3(_74193_3_pin7[0]), .pin4(_74193_2_pin13),
    .pin5(_74193_2_pin12), .pin6(_74193_3_pin7[2]), .pin7(_74193_3_pin7[3]), .pin8(1'b0),
    .pin9(_74193_3_pin9), .pin10(_74193_3_pin10), .pin11(in_3), .pin12(_74193_3_pin12),
    .pin13(_74193_3_pin13), .pin14(in_4), .pin15(_74193_3_pin15), .pin16(1'b1));
  _74173 _74173_3 (
    .pin1(1'b0), .pin2(1'b0), .pin3(_74193_3_pin15), .pin4(_74193_3_pin1), .pin5(_74193_3_pin10),
    .pin6(_74193_3_pin9), .pin7(in_5), .pin8(1'b0), .pin9(1'b0), .pin10(1'b0), .pin11(_74173_3_pin11),
    .pin12(_74173_3_pin12), .pin13(_74173_3_pin13), .pin14(_74173_3_pin14), .pin15(1'b0), .pin16(1'b1));
  _74219 _74219_3 (
    .pin1(in_8), .pin2(in_6), .pin3(in_7), .pin4(_74541_2_pin18), .pin5(_74173_3_pin14),
    .pin6(_74541_2_pin17), .pin7(_74173_3_pin13), .pin8(1'b0), .pin9(_74173_3_pin12), .pin10(_74541_2_pin16),
    .pin11(_74173_3_pin11), .pin12(_74541_2_pin15), .pin13(in_11), .pin14(in_10), .pin15(in_9), .pin16(1'b1));
  _74193 _74193_4 (
    .pin1(_74193_4_pin1), .pin2(_74193_4_pin7[1]), .pin3(_74193_4_pin7[0]), .pin4(_74193_3_pin13),
    .pin5(_74193_3_pin12), .pin6(_74193_4_pin7[2]), .pin7(_74193_4_pin7[3]), .pin8(1'b0),
    .pin9(_74193_4_pin9), .pin10(_74193_4_pin10), .pin11(in_3), .pin14(in_4), .pin15(_74193_4_pin15),
    .pin16(1'b1));  // open: pin12, pin13
  _74173 _74173_4 (
    .pin1(1'b0), .pin2(1'b0), .pin3(_74193_4_pin15), .pin4(_74193_4_pin1), .pin5(_74193_4_pin10),
    .pin6(_74193_4_pin9), .pin7(in_5), .pin8(1'b0), .pin9(1'b0), .pin10(1'b0), .pin11(_74173_4_pin11),
    .pin12(_74173_4_pin12), .pin13(_74173_4_pin13), .pin14(_74173_4_pin14), .pin15(1'b0), .pin16(1'b1));
  _74541 _74541_3 (
    .pin1(in_28), .pin2(_74193_4_pin7[3]), .pin3(_74193_4_pin7[2]), .pin4(_74193_4_pin7[1]),
    .pin5(_74193_4_pin7[0]), .pin6(_74193_3_pin7[3]), .pin7(_74193_3_pin7[2]), .pin8(_74193_3_pin7[1]),
    .pin9(_74193_3_pin7[0]), .pin10(1'b0), .pin11(_74541_2_pin18), .pin12(_74541_2_pin17),
    .pin13(_74541_2_pin16), .pin14(_74541_2_pin15), .pin15(_74541_2_pin14), .pin16(_74541_2_pin13),
    .pin17(_74541_2_pin12), .pin18(_74541_2_pin11), .pin19(in_28), .pin20(1'b1));
  _74541 _74541_4 (
    .pin1(in_28), .pin2(_74193_2_pin7[3]), .pin3(_74193_2_pin7[2]), .pin4(_74193_2_pin7[1]),
    .pin5(_74193_2_pin7[0]), .pin6(_74193_1_pin7[3]), .pin7(_74193_1_pin7[2]), .pin8(_74193_1_pin7[1]),
    .pin9(_74193_1_pin7[0]), .pin10(1'b0), .pin11(_74541_1_pin18), .pin12(_74541_1_pin17),
    .pin13(_74541_1_pin16), .pin14(_74541_1_pin15), .pin15(_74541_1_pin14), .pin16(_74541_1_pin13),
    .pin17(_74541_1_pin12), .pin18(_74541_1_pin11), .pin19(in_28), .pin20(1'b1));
  _74219 _74219_4 (
    .pin1(in_8), .pin2(in_6), .pin3(in_7), .pin4(_74541_2_pin14), .pin5(_74173_4_pin14),
    .pin6(_74541_2_pin13), .pin7(_74173_4_pin13), .pin8(1'b0), .pin9(_74173_4_pin12), .pin10(_74541_2_pin12),
    .pin11(_74173_4_pin11), .pin12(_74541_2_pin11), .pin13(in_11), .pin14(in_10), .pin15(in_9), .pin16(1'b1));

  // Notes on the sheet:
  //   Bit Counter
  //   Bit Slot Decoder
  //   Bit Slot
  //   ADDRESS
endmodule
