// Digital circuit adder_subtractor_alu_14gate.dig as structural Verilog
module adder_subtractor_alu_14gate (
  input  I1,
  input  A,
  input  B,
  input  I0,
  input  Cin,
  input  I2,
  input  I3,
  input  I1_2,
  input  A_2,
  input  B_2,
  input  I0_2,
  input  I7,
  input  A_3,
  input  B_3,
  input  C,
  input  in_21,
  input  I6,
  input  A_4,
  input  B_4,
  input  I1_3,
  input  A_5,
  input  B_5,
  input  I0_3,
  input  I3_2,
  input  C_2,
  input  I2_2,
  input  I1_4,
  input  A_6,
  input  B_6,
  input  I0_4,
  input  INV,
  input  L_A,
  input  Cin_2,
  input  I1_5,
  input  A_7,
  input  B_7,
  input  I0_5,
  input  nINV,
  input  nL_A,
  input  Cin_3,
  input  I1_6,
  input  A_8,
  input  B_8,
  input  I0_6,
  input  INV_2,
  input  nL_A_2,
  input  Cin_4,
  input  in_64,
  input  in_65,
  input  in_66,
  input  in_67,
  input  in_69,
  output Sum,
  output Carry,
  output out_14,
  output Sum_2,
  output Carry_2,
  output Sum_3,
  output Carry_3,
  output out_31,
  output Sum_4,
  output Cout,
  output Sum_5,
  output Cout_2,
  output Sum_6,
  output Cout_3,
  output Sum_7,
  output Cout_4,
  output out_68
);

  wire and_1_out, and_2_out, and_3_out, and_4_out, and_5_out, and_6_out, nand_1_out, nand_2_out, nand_3_out,
       nand_4_out, nand_5_out, nand_6_out, nand_7_out, nand_8_out, nand_9_out, nand_10_out, nand_11_out,
       nand_12_out, nand_13_out, nand_14_out, nand_15_out, nand_16_out, nand_17_out, nand_18_out,
       nand_19_out, nand_20_out, nand_21_out, nand_22_out, nand_23_out, nand_25_out, nand_26_out,
       nand_27_out, nand_28_out, nand_29_out, nand_30_out, nand_31_out, nand_32_out, nand_33_out,
       nand_34_out, nand_37_out, nand_38_out, nand_39_out, nand_40_out, nand_41_out, nand_42_out,
       nand_43_out, nand_44_out, nand_45_out, nand_46_out, nand_47_out, nand_48_out, nand_49_out,
       nand_50_out, nand_51_out, nand_52_out, nand_53_out, nand_54_out, nand_55_out, nand_57_out,
       nand_58_out, nand_59_out, nand_60_out, nand_61_out, nand_62_out, nand_63_out, nand_64_out,
       nand_65_out, nand_66_out, nand_67_out, nand_69_out, nand_70_out, nand_71_out, nand_72_out,
       nand_73_out, nand_76_out, nand_77_out, nand_78_out, nand_79_out, nand_81_out, nand_82_out,
       nand_84_out, nand_85_out, nand_88_out, nand_91_out, nand_92_out, or_1_out, or_3_out, or_4_out,
       or_5_out, or_6_out, or_7_out, xor_1_out;

  and and_1 (and_1_out, Cin_4, nL_A_2);
  nand nand_1 (nand_1_out, Cin_2, nand_52_out);
  nand nand_2 (nand_2_out, nand_1_out, nand_5_out);
  and and_2 (and_2_out, A_8, and_1_out);
  and and_3 (and_3_out, B_8, and_1_out);
  and and_4 (and_4_out, A_8, B_8);
  xor xor_1 (xor_1_out, A_8, B_8);
  nand nand_3 (nand_3_out, A, B);
  nand nand_4 (nand_4_out, Cin, Cin);
  nand nand_5 (nand_5_out, A_6, B_6);
  nand nand_6 (nand_6_out, A_4, B_4);
  nand nand_7 (nand_7_out, A_5, B_5);
  nand nand_8 (nand_8_out, Cin_2, Cin_2);
  or or_1 (or_1_out, and_2_out, and_3_out);
  nand nand_9 (nand_9_out, A, nand_3_out);
  nand nand_10 (nand_10_out, nand_3_out, B);
  nand nand_11 (nand_11_out, A_3, B_3);
  nand nand_12 (nand_12_out, nand_2_out, L_A);
  nand nand_13 (nand_13_out, A_6, nand_5_out);
  nand nand_14 (nand_14_out, nand_5_out, B_6);
  nand nand_15 (nand_15_out, A_2, B_2);
  nand nand_16 (nand_16_out, A_5, nand_7_out);
  nand nand_17 (nand_17_out, nand_7_out, B_5);
  nand nand_18 (nand_18_out, A_7, B_7);
  nand nand_19 (nand_19_out, Cin_3, nL_A);
  or or_2 (Cout_4, or_1_out, and_4_out);
  and and_5 (and_5_out, and_4_out, I1_6);
  and and_6 (and_6_out, xor_1_out, I0_6);
  or or_3 (or_3_out, INV_2, and_1_out);
  nand nand_20 (nand_20_out, B, nand_3_out);
  nand nand_21 (nand_21_out, nand_9_out, nand_10_out);
  nand nand_22 (nand_22_out, A_4, nand_6_out);
  nand nand_23 (nand_23_out, nand_6_out, B_4);
  nand nand_24 (Cout_2, nand_12_out, nand_12_out);
  nand nand_25 (nand_25_out, nand_5_out, nand_5_out);
  nand nand_26 (nand_26_out, nand_13_out, nand_14_out);
  or or_4 (or_4_out, and_5_out, and_6_out);
  nand nand_27 (nand_27_out, A_3, nand_11_out);
  nand nand_28 (nand_28_out, nand_11_out, B_3);
  nand nand_29 (nand_29_out, nand_7_out, nand_7_out);
  nand nand_30 (nand_30_out, nand_16_out, nand_17_out);
  nand nand_31 (nand_31_out, A_7, nand_18_out);
  nand nand_32 (nand_32_out, nand_18_out, B_7);
  nand nand_33 (nand_33_out, A_2, nand_15_out);
  nand nand_34 (nand_34_out, nand_15_out, B_2);
  nand nand_35 (Carry_3, nand_6_out, nand_6_out);
  nand nand_36 (Sum_3, nand_22_out, nand_23_out);
  xor xor_2 (Sum_7, or_4_out, or_3_out);
  nand nand_37 (nand_37_out, I1, nand_20_out);
  nand nand_38 (nand_38_out, nand_21_out, I0);
  nand nand_39 (nand_39_out, nand_4_out, I2);
  nand nand_40 (nand_40_out, B_3, nand_11_out);
  nand nand_41 (nand_41_out, nand_27_out, nand_28_out);
  nand nand_42 (nand_42_out, I1_4, nand_25_out);
  nand nand_43 (nand_43_out, nand_26_out, I0_4);
  nand nand_44 (nand_44_out, nand_15_out, nand_15_out);
  nand nand_45 (nand_45_out, nand_33_out, nand_34_out);
  nand nand_46 (nand_46_out, I1_3, nand_29_out);
  nand nand_47 (nand_47_out, nand_30_out, I0_3);
  nand nand_48 (nand_48_out, nand_18_out, nand_18_out);
  nand nand_49 (nand_49_out, nand_31_out, nand_32_out);
  nand nand_50 (nand_50_out, nand_37_out, nand_38_out);
  nand nand_51 (nand_51_out, nand_39_out, I3);
  nand nand_52 (nand_52_out, nand_42_out, nand_43_out);
  nand nand_53 (nand_53_out, nand_8_out, INV);
  nand nand_54 (nand_54_out, I7, nand_40_out);
  nand nand_55 (nand_55_out, nand_41_out, I6);
  nand nand_56 (out_31, nand_46_out, nand_47_out);
  nand nand_57 (nand_57_out, nand_50_out, nand_51_out);
  nand nand_58 (nand_58_out, I1_2, nand_44_out);
  nand nand_59 (nand_59_out, nand_45_out, I0_2);
  nand nand_60 (nand_60_out, I1_5, nand_48_out);
  nand nand_61 (nand_61_out, nand_49_out, I0_5);
  nand nand_62 (nand_62_out, nINV, nand_19_out);
  nand nand_63 (nand_63_out, nand_19_out, nand_19_out);
  nand nand_64 (nand_64_out, nand_54_out, nand_55_out);
  nand nand_65 (nand_65_out, nand_52_out, nand_53_out);
  nand nand_66 (nand_66_out, nand_50_out, nand_57_out);
  nand nand_67 (nand_67_out, nand_57_out, nand_51_out);
  nand nand_68 (out_14, nand_58_out, nand_59_out);
  nand nand_69 (nand_69_out, nand_60_out, nand_61_out);
  nand nand_70 (nand_70_out, nand_64_out, C);
  nand nand_71 (nand_71_out, out_31, C_2);
  nand nand_72 (nand_72_out, nand_52_out, nand_65_out);
  nand nand_73 (nand_73_out, nand_65_out, nand_53_out);
  nand nand_74 (Carry, nand_3_out, nand_57_out);
  nand nand_75 (Sum, nand_66_out, nand_67_out);
  nand nand_76 (nand_76_out, nand_64_out, nand_70_out);
  nand nand_77 (nand_77_out, nand_70_out, C);
  nand nand_78 (nand_78_out, out_31, nand_71_out);
  nand nand_79 (nand_79_out, nand_71_out, C_2);
  nand nand_80 (Sum_5, nand_72_out, nand_73_out);
  nand nand_81 (nand_81_out, nand_63_out, nand_69_out);
  nand nand_82 (nand_82_out, nand_69_out, nand_62_out);
  nand nand_83 (Cout_3, nand_18_out, nand_81_out);
  nand nand_84 (nand_84_out, nand_69_out, nand_82_out);
  nand nand_85 (nand_85_out, nand_82_out, nand_62_out);
  nand nand_86 (Carry_2, nand_11_out, nand_70_out);
  nand nand_87 (Sum_2, nand_76_out, nand_77_out);
  nand nand_88 (nand_88_out, nand_78_out, nand_79_out);
  nand nand_89 (Cout, nand_71_out, nand_7_out);
  nand nand_90 (Sum_6, nand_84_out, nand_85_out);
  nand nand_91 (nand_91_out, I3_2, out_31);
  nand nand_92 (nand_92_out, nand_88_out, I2_2);
  nand nand_93 (Sum_4, nand_91_out, nand_92_out);
  or or_5 (or_5_out, in_69, in_64);
  or or_6 (or_6_out, or_5_out, in_65);
  or or_7 (or_7_out, or_6_out, in_66);
  or or_8 (out_68, or_7_out, in_67);

  // Notes on the sheet:
  //   INV  ~L/A   I1    I0
  //   0       0       0      0      ZERO
  //   0       0       0      1      XOR
  //   0       0       1      0      AND
  //   0       0       1      1      OR
  //   0       1       0      0      Cin
  //   0       1       0      1      ADD
  //   0       1       1      0
  //   0       1       1      1
  //   1       0       0      0       ONE
  //   1       0       0      1       XNOR
  //   1       0       1      0       NAND
  //   1       0       1      1       NOR
  //   1       1       0      0
  //   1       1       0      1
  //   1       1       1      0
  //   1       1       1      1
  //   C  I1 I0
  //   0   0   0    F = 0
  //   0   0   1    F = A XOR B 
  //   0   1   0    F = A AND B
  //   0   1   1    F = A OR B
  //   1   0   0    F = 1
  //   1   0   1    F = A XNOR B
  //   1   1   0    F = A NAND B
  //   1   1   1    F = A NOR B
  //   Suppress Cin ~L/A = 0
  //   Carry Logic
  //   C
  //   12-Gate Arithmetic Logic Unit
  //   0, XOR, AND, OR
  //   Half Adder AND/XOR
  //   16-Gate Arithmetic Logic Unit  Zero, XOR, AND, OR
  //   A&C
  //   B&C
  //   A&B
  //   A ^ B
  //   Suppress Cout
  //   Zero, XOR, AND, OR
  //   8-Gate Logic Unit  Zero, XOR, AND, OR
  //   A&B | A&C | B&C
  //   2 Input Mux
  //   16 Gate ALU
  //   XOR/Inverter
  //   17-Gate Arithmetic Logic Unit
  //   I1:I0
  //   0 0   Zero
  //   0 1   XOR
  //   1 0  AND
  //   1  1  OR
  //   If  ~INV =0 the output Sum is inverted
  //   13 Gate ALU
  //   Half Adder / Invert
  //   XOR
  //   Zero Detection
endmodule
