// Digital circuit basic_gates_1.dig as structural Verilog
module basic_gates_1 (
  input  in_2,
  input  in_3,
  input  in_4,
  input  in_5,
  input  in_6,
  input  in_7,
  input  in_8,
  input  in_9,
  input  in_11,
  input  in_12,
  input  in_14,
  input  in_15,
  input  in_17,
  input  in_18,
  input  in_20,
  input  in_21,
  input  in_26,
  input  in_27,
  input  in_32,
  input  in_33,
  input  in_38,
  input  in_40,
  input  in_41,
  input  in_42,
  input  in_43,
  input  in_45,
  input  in_46,
  input  in_47,
  input  in_48,
  input  in_50,
  input  in_51,
  input  in_52,
  input  in_53,
  input  in_54,
  input  in_55,
  input  B,
  input  A,
  input  E5,
  input  E4,
  input  C,
  input  C_2,
  input  S0,
  input  D,
  input  A_2,
  input  B_2,
  input  S1,
  input  EN,
  input  S0_2,
  input  S1_2,
  input  EN_2,
  input  in_72,
  input  in_73,
  input  in_74,
  input  in_75,
  input  in_76,
  input  in_77,
  input  A_3,
  input  B_3,
  input  Cin,
  input  A_4,
  input  B_4,
  input  Cin_2,
  output out_1,
  output out_10,
  output out_13,
  output out_16,
  output out_19,
  output out_22,
  output out_23,
  output out_24,
  output out_25,
  output out_28,
  output out_29,
  output out_30,
  output out_31,
  output out_34,
  output out_35,
  output out_36,
  output out_37,
  output out_39,
  output out_44,
  output out_49,
  output out_56,
  output Carry,
  output Sum,
  output Carry_2,
  output Sum_2,
  output Carry_3,
  output Sum_3
);

  wire AL, and_1_out, and_3_out, and_4_out, and_5_out, and_6_out, and_7_out, AR0, AR1, AR2, AR3, nand_1_out,
       nand_2_out, nand_3_out, nand_4_out, nand_5_out, nand_6_out, nand_7_out, nand_8_out, nand_9_out,
       nand_10_out, nand_11_out, nand_12_out, nand_13_out, nand_14_out, nand_16_out, nand_17_out,
       nand_18_out, nand_19_out, nand_20_out, nand_21_out, nand_22_out, nand_23_out, nand_24_out,
       nand_25_out, nand_26_out, nand_27_out, nand_28_out, nand_29_out, nand_30_out, nand_31_out,
       nand_32_out, nand_33_out, nand_34_out, nand_35_out, nand_36_out, nand_37_out, nand_38_out,
       nand_39_out, nand_40_out, nand_41_out, nand_42_out, nand_43_out, nand_44_out, nand_45_out,
       nand_46_out, nand_47_out, nand_48_out, nand_49_out, nand_50_out, nand_51_out, nand_52_out,
       nand_53_out, nand_54_out, nand_55_out, nand_56_out, nand_57_out, nand_58_out, nand_59_out,
       nand_60_out, nand_61_out, nand_62_out, nand_63_out, nand_64_out, nand_65_out, nand_66_out,
       nand_67_out, nand_68_out, nand_69_out, nand_70_out, nand_71_out, nand_72_out, nand_73_out,
       nand_74_out, nand_75_out, nand_76_out, nand_77_out, nand_78_out, nand_79_out, nand_80_out,
       nand_81_out, nand_82_out, nand_83_out, nand_84_out, nand_85_out, nand_86_out, nand_87_out,
       nand_88_out, nand_89_out, nand_90_out, nand_91_out, nand_92_out, nand_93_out, nand_94_out,
       nand_95_out, nand_96_out, nand_97_out, nand_98_out, nand_99_out, nand_102_out, nand_105_out,
       nand_106_out, nand_107_out, nand_108_out, nand_109_out, nand_116_out, nand_117_out, nand_118_out,
       nand_119_out, nand_120_out, nand_121_out, nand_122_out, nand_123_out, nand_128_out, nand_129_out,
       nand_130_out, nand_131_out, nand_132_out, nand_133_out, nand_134_out, nand_135_out, nand_136_out,
       nand_137_out, nand_138_out, nand_139_out, nand_140_out, nand_141_out, nand_142_out, nand_143_out,
       nand_144_out, nand_145_out, nand_146_out, nand_147_out, nand_148_out, nand_149_out, nand_151_out,
       nand_152_out, nand_153_out, nand_154_out, nand_167_out, nand_168_out, nand_169_out, nJMP, nW,
       pullup_1_out, pullup_2_out, pullup_3_out, pullup_4_out, pullup_5_out, W, xor_1_out, xor_2_out;

  nand nand_1 (nand_1_out, S0, S0);
  nand nand_2 (nand_2_out, S1, S1);
  and and_1 (and_1_out, A_3, B_3);
  xor xor_1 (xor_1_out, A_3, B_3);
  nand nand_3 (nand_3_out, A_4, B_4);
  xor xor_2 (xor_2_out, A_4, B_4);
  nand nand_4 (nand_4_out, S0_2, S0_2);
  nand nand_5 (nand_5_out, S1_2, S1_2);
  and and_2 (Carry, in_76, in_77);
  xor xor_3 (Sum, in_76, in_77);
  nand nand_6 (nand_6_out, xor_2_out, Cin_2);
  xor xor_4 (Sum_3, xor_2_out, Cin_2);
  nand nand_7 (nand_7_out, D, S0);
  nand nand_8 (nand_8_out, C_2, nand_1_out);
  nand nand_9 (nand_9_out, B_2, S0);
  nand nand_10 (nand_10_out, A_2, nand_1_out);
  and and_3 (and_3_out, xor_1_out, Cin);
  xor xor_5 (Sum_2, xor_1_out, Cin);
  nand nand_11 (nand_11_out, nand_4_out, nand_5_out);
  nand nand_12 (nand_12_out, S0_2, nand_5_out);
  nand nand_13 (nand_13_out, nand_4_out, S1_2);
  nand nand_14 (nand_14_out, S0_2, S1_2);
  nand nand_15 (Carry_3, nand_3_out, nand_6_out);
  or or_1 (Carry_2, and_1_out, and_3_out);
  nand nand_16 (nand_16_out, nand_7_out, nand_8_out);
  nand nand_17 (nand_17_out, nand_9_out, nand_10_out);
  nand nand_18 (nand_18_out, nand_11_out, nand_11_out);
  nand nand_19 (nand_19_out, nand_12_out, nand_12_out);
  nand nand_20 (nand_20_out, nand_13_out, nand_13_out);
  nand nand_21 (nand_21_out, nand_14_out, nand_14_out);
  nand nand_22 (nand_22_out, S1, nand_16_out);
  nand nand_23 (nand_23_out, nand_17_out, nand_2_out);
  nand nand_24 (nand_24_out, nand_18_out, EN_2);
  nand nand_25 (nand_25_out, nand_19_out, EN_2);
  nand nand_26 (nand_26_out, nand_20_out, EN_2);
  nand nand_27 (nand_27_out, nand_21_out, EN_2);
  nand nand_28 (nand_28_out, C, C);
  nand nand_29 (nand_29_out, B, B);
  nand nand_30 (nand_30_out, A, A);
  nand nand_31 (nand_31_out, E5, E4);
  nand nand_32 (nand_32_out, nand_22_out, nand_23_out);
  LED led_1 (.in(nand_24_out));
  LED led_2 (.in(nand_25_out));
  LED led_3 (.in(nand_26_out));
  LED led_4 (.in(nand_27_out));
  nand nand_33 (nand_33_out, nand_32_out, EN);
  nand nand_34 (nand_34_out, nand_33_out, nand_33_out);
  LED led_5 (.in(nand_34_out));
  nand nand_35 (nand_35_out, nand_31_out, nand_28_out);
  nand nand_36 (nand_36_out, nand_29_out, nand_30_out);
  nand nand_37 (nand_37_out, nand_31_out, nand_28_out);
  nand nand_38 (nand_38_out, A, nand_29_out);
  nand nand_39 (nand_39_out, nand_31_out, nand_28_out);
  nand nand_40 (nand_40_out, nand_30_out, B);
  nand nand_41 (nand_41_out, nand_31_out, nand_28_out);
  nand nand_42 (nand_42_out, A, B);
  nand nand_43 (nand_43_out, nand_31_out, C);
  nand nand_44 (nand_44_out, nand_29_out, nand_30_out);
  nand nand_45 (nand_45_out, nand_31_out, C);
  nand nand_46 (nand_46_out, A, nand_29_out);
  nand nand_47 (nand_47_out, nand_31_out, C);
  nand nand_48 (nand_48_out, nand_30_out, B);
  nand nand_49 (nand_49_out, nand_31_out, C);
  nand nand_50 (nand_50_out, A, B);
  nand nand_51 (nand_51_out, nand_35_out, nand_35_out);
  nand nand_52 (nand_52_out, nand_36_out, nand_36_out);
  nand nand_53 (nand_53_out, nand_37_out, nand_37_out);
  nand nand_54 (nand_54_out, nand_38_out, nand_38_out);
  nand nand_55 (nand_55_out, nand_39_out, nand_39_out);
  nand nand_56 (nand_56_out, nand_40_out, nand_40_out);
  nand nand_57 (nand_57_out, nand_41_out, nand_41_out);
  nand nand_58 (nand_58_out, nand_42_out, nand_42_out);
  nand nand_59 (nand_59_out, nand_43_out, nand_43_out);
  nand nand_60 (nand_60_out, nand_44_out, nand_44_out);
  nand nand_61 (nand_61_out, nand_45_out, nand_45_out);
  nand nand_62 (nand_62_out, nand_46_out, nand_46_out);
  nand nand_63 (nand_63_out, nand_47_out, nand_47_out);
  nand nand_64 (nand_64_out, nand_48_out, nand_48_out);
  nand nand_65 (nand_65_out, nand_49_out, nand_49_out);
  nand nand_66 (nand_66_out, nand_50_out, nand_50_out);
  nand nand_67 (nand_67_out, nand_51_out, nand_52_out);
  nand nand_68 (nand_68_out, nand_53_out, nand_54_out);
  nand nand_69 (nand_69_out, nand_55_out, nand_56_out);
  nand nand_70 (nand_70_out, nand_57_out, nand_58_out);
  nand nand_71 (nand_71_out, nand_59_out, nand_60_out);
  nand nand_72 (nand_72_out, nand_61_out, nand_62_out);
  nand nand_73 (nand_73_out, nand_63_out, nand_64_out);
  nand nand_74 (nand_74_out, nand_65_out, nand_66_out);
  LED led_6 (.in(nand_67_out));
  LED led_7 (.in(nand_68_out));
  LED led_8 (.in(nand_69_out));
  LED led_9 (.in(nand_70_out));
  LED led_10 (.in(nand_71_out));
  LED led_11 (.in(nand_72_out));
  LED led_12 (.in(nand_73_out));
  LED led_13 (.in(nand_74_out));
  nand nand_75 (nand_75_out, in_72, in_72);
  nand nand_76 (nand_76_out, in_73, in_73);
  nand nand_77 (nand_77_out, in_74, in_74);
  nand nand_78 (nand_78_out, nand_75_out, nand_76_out);
  nand nand_79 (nand_79_out, in_72, nand_76_out);
  nand nand_80 (nand_80_out, nand_75_out, in_73);
  nand nand_81 (nand_81_out, in_72, in_73);
  nand nand_82 (nand_82_out, nand_75_out, nand_76_out);
  nand nand_83 (nand_83_out, in_72, nand_76_out);
  nand nand_84 (nand_84_out, nand_75_out, in_73);
  nand nand_85 (nand_85_out, in_72, in_73);
  nand nand_86 (nand_86_out, in_75, nand_78_out);
  nand nand_87 (nand_87_out, in_75, nand_79_out);
  nand nand_88 (nand_88_out, in_75, nand_80_out);
  nand nand_89 (nand_89_out, in_75, nand_81_out);
  nand nand_90 (nand_90_out, in_75, nand_82_out);
  nand nand_91 (nand_91_out, in_75, nand_83_out);
  nand nand_92 (nand_92_out, in_75, nand_84_out);
  nand nand_93 (nand_93_out, in_75, nand_85_out);
  nand nand_94 (nand_94_out, nand_86_out, nand_77_out);
  nand nand_95 (nand_95_out, nand_87_out, nand_77_out);
  nand nand_96 (nand_96_out, nand_88_out, nand_77_out);
  nand nand_97 (nand_97_out, nand_89_out, nand_77_out);
  nand nand_98 (nand_98_out, nand_90_out, in_74);
  nand nand_99 (nand_99_out, nand_91_out, in_74);
  nand nand_100 (nW, nand_92_out, in_74);
  nand nand_101 (nJMP, nand_93_out, in_74);
  nand nand_102 (nand_102_out, in_6, in_6);
  PullUp pullup_1 (.out(pullup_1_out));
  DiodeBackward diodebackward_1 (.in(nJMP), .out(pullup_1_out));
  DiodeBackward diodebackward_2 (.in(in_74), .out(pullup_1_out));
  nand nand_103 (AL, pullup_1_out, pullup_1_out);
  and and_4 (and_4_out, nand_102_out, in_8);
  and and_5 (and_5_out, in_6, in_8);
  PullUp pullup_2 (.out(pullup_2_out));
  DiodeBackward diodebackward_3 (.in(nand_94_out), .out(pullup_2_out));
  DiodeBackward diodebackward_4 (.in(nand_95_out), .out(pullup_2_out));
  DiodeBackward diodebackward_5 (.in(nand_96_out), .out(pullup_2_out));
  DiodeBackward diodebackward_6 (.in(nand_98_out), .out(pullup_2_out));
  nand nand_104 (AR3, pullup_2_out, pullup_2_out);
  nand nand_105 (nand_105_out, in_20, in_20);
  nand nand_106 (nand_106_out, in_21, in_21);
  nand nand_107 (nand_107_out, in_26, in_26);
  nand nand_108 (nand_108_out, in_27, in_27);
  nand nand_109 (nand_109_out, in_38, in_38);
  // NAnd nand_110 has open pins: In_1=in_32, In_2=in_32, out=open
  // NAnd nand_111 has open pins: In_1=in_33, In_2=in_33, out=open
  PullUp pullup_3 (.out(pullup_3_out));
  DiodeBackward diodebackward_7 (.in(nand_94_out), .out(pullup_3_out));
  DiodeBackward diodebackward_8 (.in(nand_96_out), .out(pullup_3_out));
  DiodeBackward diodebackward_9 (.in(nand_97_out), .out(pullup_3_out));
  DiodeBackward diodebackward_10 (.in(nand_98_out), .out(pullup_3_out));
  DiodeBackward diodebackward_11 (.in(nW), .out(pullup_3_out));
  nand nand_112 (AR2, pullup_3_out, pullup_3_out);
  PullUp pullup_4 (.out(pullup_4_out));
  DiodeBackward diodebackward_12 (.in(nand_96_out), .out(pullup_4_out));
  DiodeBackward diodebackward_13 (.in(nand_97_out), .out(pullup_4_out));
  DiodeBackward diodebackward_14 (.in(nand_99_out), .out(pullup_4_out));
  nand nand_113 (AR1, pullup_4_out, pullup_4_out);
  PullUp pullup_5 (.out(pullup_5_out));
  DiodeBackward diodebackward_15 (.in(nand_99_out), .out(pullup_5_out));
  DiodeBackward diodebackward_16 (.in(nW), .out(pullup_5_out));
  nand nand_114 (AR0, pullup_5_out, pullup_5_out);
  nand nand_115 (W, nW, nW);
  and and_6 (and_6_out, in_2, in_3);
  and and_7 (and_7_out, in_4, in_5);
  nand nand_116 (nand_116_out, and_4_out, in_7);
  nand nand_117 (nand_117_out, and_5_out, in_9);
  nand nand_118 (nand_118_out, and_4_out, in_11);
  nand nand_119 (nand_119_out, and_5_out, in_12);
  nand nand_120 (nand_120_out, and_4_out, in_14);
  nand nand_121 (nand_121_out, and_5_out, in_15);
  nand nand_122 (nand_122_out, and_4_out, in_17);
  nand nand_123 (nand_123_out, and_5_out, in_18);
  nand nand_124 (out_22, nand_105_out, nand_106_out);
  nand nand_125 (out_23, in_20, nand_106_out);
  nand nand_126 (out_24, nand_105_out, in_21);
  nand nand_127 (out_25, in_20, in_21);
  nand nand_128 (nand_128_out, nand_107_out, nand_108_out);
  nand nand_129 (nand_129_out, in_26, nand_108_out);
  nand nand_130 (nand_130_out, nand_107_out, in_27);
  nand nand_131 (nand_131_out, in_26, in_27);
  nand nand_132 (nand_132_out, nand_107_out, nand_108_out);
  nand nand_133 (nand_133_out, in_26, nand_108_out);
  nand nand_134 (nand_134_out, nand_107_out, in_27);
  nand nand_135 (nand_135_out, in_26, in_27);
  nand nand_136 (nand_136_out, 1'b0, 1'b0);
  nand nand_137 (nand_137_out, in_54, in_54);
  nand nand_138 (nand_138_out, in_55, in_55);
  nand nand_139 (nand_139_out, in_52, in_52);
  nand nand_140 (nand_140_out, in_53, in_53);
  nand nand_141 (nand_141_out, in_50, in_50);
  nand nand_142 (nand_142_out, in_51, in_51);
  nand nand_143 (nand_143_out, in_45, in_46);
  nand nand_144 (nand_144_out, in_47, in_48);
  nand nand_145 (nand_145_out, in_40, in_41);
  nand nand_146 (nand_146_out, in_42, in_43);
  LED led_14 (.in(nand_94_out));
  LED led_15 (.in(nand_95_out));
  LED led_16 (.in(nand_96_out));
  LED led_17 (.in(nand_97_out));
  LED led_18 (.in(nand_98_out));
  LED led_19 (.in(nand_99_out));
  LED led_20 (.in(nW));
  LED led_21 (.in(nJMP));
  nand nand_147 (nand_147_out, 1'b0, 1'b0);
  nand nand_148 (nand_148_out, nand_137_out, nand_138_out);
  nand nand_149 (nand_149_out, nand_139_out, nand_140_out);
  nand nand_150 (out_49, nand_141_out, nand_142_out);
  nand nand_151 (nand_151_out, nand_143_out, nand_143_out);
  nand nand_152 (nand_152_out, nand_144_out, nand_144_out);
  nand nand_153 (nand_153_out, nand_145_out, nand_145_out);
  nand nand_154 (nand_154_out, nand_146_out, nand_146_out);
  and and_8 (out_1, and_6_out, and_7_out);
  nand nand_155 (out_10, nand_116_out, nand_117_out);
  nand nand_156 (out_13, nand_118_out, nand_119_out);
  nand nand_157 (out_16, nand_120_out, nand_121_out);
  nand nand_158 (out_19, nand_122_out, nand_123_out);
  nand nand_159 (out_28, nand_109_out, nand_128_out);
  nand nand_160 (out_29, nand_109_out, nand_129_out);
  nand nand_161 (out_30, nand_109_out, nand_130_out);
  nand nand_162 (out_31, nand_109_out, nand_131_out);
  nand nand_163 (out_34, in_38, nand_132_out);
  nand nand_164 (out_35, in_38, nand_133_out);
  nand nand_165 (out_36, in_38, nand_134_out);
  nand nand_166 (out_37, in_38, nand_135_out);
  nand nand_167 (nand_167_out, nand_148_out, nand_148_out);
  nand nand_168 (nand_168_out, nand_149_out, nand_149_out);
  nand nand_169 (nand_169_out, nand_151_out, nand_152_out);
  nand nand_170 (out_39, nand_153_out, nand_154_out);
  nand nand_171 (out_44, nand_169_out, nand_169_out);
  Seven_Seg_Hex seven_seg_hex_1 (.d({3'b000, AL}), .dp(1'b0));
  nand nand_172 (out_56, nand_167_out, nand_168_out);
  Seven_Seg_Hex seven_seg_hex_2 (.d({AR3, AR2, AR1, AR0}), .dp(1'b0));

  // Other names for the same wires on the sheet: IR4 = in_72; IR5 = in_73; IR6 = in_74

  // Notes on the sheet:
  //   2 to 4 line decoder with enable ('139)
  //   4:1 Multiplexer with Enable
  //   1 of 8 decoder (74xx138)
  //   CONTROL UNIT
  //   3 to 8 Instruction decoder - 27 Gates
  //   S
  //   EN
  //   A
  //   B
  //   C
  //   74xx157 equiv
  //   half 74xx139 equiv
  //   Octal Inverter/Driver
  //   4 Input AND
  //   4 Input NAND
  //   4-input AND
  //   2 Input OR
  //   LOAD
  //   AND
  //   OR
  //   XOR
  //   ADD
  //   SUB
  //   STORE
  //   JMP
  //   4 Input OR
  //   INSTRUCTION
endmodule
