// Digital circuit basic_gates_3.dig as structural Verilog
module basic_gates_3 (
  input  in_1,
  input  in_2,
  input  in_3,
  input  in_4,
  input  in_5,
  input  in_6,
  input  in_7,
  input  in_8,
  input  in_9,
  input  in_10,
  input  DAT,
  input  CLK,
  input  in_13,
  input  DAT_2,
  input  in_15,
  input  DAT_3,
  input  in_17,
  input  DATA,
  input  CK,
  input  nLD,
  input  in_21,
  input  in_22,
  input  in_23,
  input  in_24,
  input  in_25,
  input  in_26,
  input  D3,
  input  D2,
  input  D1,
  input  D0,
  input  S1,
  input  S0,
  input  E1,
  input  E0,
  input  in_35,
  input  in_36,
  input  in_37,
  input  in_38,
  input  C,
  input  S0_2,
  input  D,
  input  A,
  input  B,
  input  S1_2,
  input  EN,
  input  in_46,
  input  in_47,
  input  in_48,
  input  in_49,
  input  in_50,
  input  in_51,
  input  in_52,
  input  in_53,
  input  in_54,
  input  C_2,
  input  S0_3,
  input  D_2,
  input  A_2,
  input  B_2,
  input  S1_3
);

  wire nand_1_out, nand_2_out, nand_3_out, nand_4_out, nand_5_out, nand_6_out, nand_7_out, nand_8_out,
       nand_9_out, nand_10_out, nand_11_out, nand_12_out, nand_13_out, nand_14_out, nand_15_out, nand_16_out,
       nand_17_out, nand_18_out, nand_19_out, nand_20_out, nand_21_out, nand_22_out, nand_23_out,
       nand_24_out, nand_25_out, nand_26_out, nand_27_out, nand_28_out, nand_29_out, nand_30_out,
       nand_31_out, nand_32_out, nand_33_out, nand_34_out, nand_35_out, nand_36_out, nand_37_out,
       nand_38_out, nand_39_out, nand_40_out, nand_41_out, nand_42_out, nand_43_out, nand_44_out,
       nand_45_out, nand_46_out, nand_47_out, nand_48_out, nand_49_out, nand_50_out, nand_51_out,
       nand_52_out, nand_53_out, nand_54_out, nand_55_out, nand_56_out, nand_57_out, nand_58_out,
       nand_59_out, nand_60_out, nand_61_out, nand_62_out, nand_63_out, nand_64_out, nand_65_out,
       nand_66_out, nand_67_out, nand_68_out, nand_69_out, nand_70_out, nand_71_out, nand_72_out,
       nand_73_out, nand_74_out, nand_75_out, nand_76_out, nand_77_out, nand_78_out, nand_79_out,
       nand_80_out, nand_81_out, nand_82_out, nand_83_out, nand_84_out, nand_85_out, nand_86_out,
       nand_87_out, nand_88_out, nand_89_out, nand_90_out, nand_91_out, nand_92_out, nand_93_out,
       nand_94_out, nand_95_out, nand_96_out, nand_97_out, nand_98_out, nand_99_out, nand_100_out,
       nand_101_out, nand_102_out, nand_103_out, nand_104_out, nand_105_out, nand_106_out, nand_107_out,
       nand_108_out, nand_109_out, nand_110_out, nand_111_out, nand_112_out, nand_113_out, nand_114_out,
       nand_115_out, nand_116_out, nand_117_out, nand_118_out, nand_119_out, nand_120_out, nand_121_out,
       nand_122_out, nand_123_out, nand_124_out, nand_125_out, nand_126_out, nand_127_out, nor_1_out,
       nor_2_out, xor_1_out, xor_2_out, xor_3_out, xor_4_out;

  nand nand_1 (nand_1_out, S0_3, S0_3);
  nand nand_2 (nand_2_out, S1_3, S1_3);
  nand nand_3 (nand_3_out, S0_2, S0_2);
  nand nand_4 (nand_4_out, S1_2, S1_2);
  nand nand_5 (nand_5_out, E1, E0);
  nand nand_6 (nand_6_out, S0, S0);
  nand nand_7 (nand_7_out, D_2, S0_3);
  nand nand_8 (nand_8_out, C_2, nand_1_out);
  nand nand_9 (nand_9_out, B_2, S0_3);
  nand nand_10 (nand_10_out, A_2, nand_1_out);
  nand nand_11 (nand_11_out, S1, S1);
  nand nand_12 (nand_12_out, D, S0_2);
  nand nand_13 (nand_13_out, C, nand_3_out);
  nand nand_14 (nand_14_out, B, S0_2);
  nand nand_15 (nand_15_out, A, nand_3_out);
  nand nand_16 (nand_16_out, nand_7_out, nand_8_out);
  nand nand_17 (nand_17_out, nand_9_out, nand_10_out);
  nand nand_18 (nand_18_out, D3, nand_5_out);
  nand nand_19 (nand_19_out, S1, S0);
  nand nand_20 (nand_20_out, D2, nand_5_out);
  nand nand_21 (nand_21_out, nand_6_out, S1);
  nand nand_22 (nand_22_out, D1, nand_5_out);
  nand nand_23 (nand_23_out, S0, nand_11_out);
  nand nand_24 (nand_24_out, D0, nand_5_out);
  nand nand_25 (nand_25_out, nand_6_out, nand_11_out);
  nand nand_26 (nand_26_out, nand_12_out, nand_13_out);
  nand nand_27 (nand_27_out, nand_14_out, nand_15_out);
  nand nand_28 (nand_28_out, S1_3, nand_16_out);
  nand nand_29 (nand_29_out, nand_17_out, nand_2_out);
  nand nand_30 (nand_30_out, nand_18_out, nand_18_out);
  nand nand_31 (nand_31_out, nand_19_out, nand_19_out);
  nand nand_32 (nand_32_out, nand_20_out, nand_20_out);
  nand nand_33 (nand_33_out, nand_21_out, nand_21_out);
  nand nand_34 (nand_34_out, nand_22_out, nand_22_out);
  nand nand_35 (nand_35_out, nand_23_out, nand_23_out);
  nand nand_36 (nand_36_out, nand_24_out, nand_24_out);
  nand nand_37 (nand_37_out, nand_25_out, nand_25_out);
  nand nand_38 (nand_38_out, S1_2, nand_26_out);
  nand nand_39 (nand_39_out, nand_27_out, nand_4_out);
  nand nand_40 (nand_40_out, nand_28_out, nand_29_out);
  nand nand_41 (nand_41_out, nand_30_out, nand_31_out);
  nand nand_42 (nand_42_out, nand_32_out, nand_33_out);
  nand nand_43 (nand_43_out, nand_34_out, nand_35_out);
  nand nand_44 (nand_44_out, nand_36_out, nand_37_out);
  nand nand_45 (nand_45_out, nand_38_out, nand_39_out);
  LED led_1 (.in(nand_40_out));
  nand nand_46 (nand_46_out, nand_45_out, EN);
  nand nand_47 (nand_47_out, nand_41_out, nand_42_out);
  nand nand_48 (nand_48_out, nand_43_out, nand_44_out);
  nand nand_49 (nand_49_out, nand_46_out, nand_46_out);
  nand nand_50 (nand_50_out, nand_47_out, nand_47_out);
  nand nand_51 (nand_51_out, nand_48_out, nand_48_out);
  LED led_2 (.in(nand_49_out));
  nand nand_52 (nand_52_out, nand_50_out, nand_51_out);
  LED led_3 (.in(nand_52_out));
  nand nand_53 (nand_53_out, in_46, in_47);
  nand nand_54 (nand_54_out, in_48, in_49);
  nand nand_55 (nand_55_out, in_35, in_36);
  nand nand_56 (nand_56_out, in_37, in_38);
  nand nand_57 (nand_57_out, in_21, in_22);
  nand nand_58 (nand_58_out, in_50, in_50);
  nand nand_59 (nand_59_out, in_23, in_24);
  nand nand_60 (nand_60_out, in_25, in_25);
  nand nand_61 (nand_61_out, in_26, in_26);
  nand nand_62 (nand_62_out, nand_53_out, nand_53_out);
  nand nand_63 (nand_63_out, nand_54_out, nand_54_out);
  nand nand_64 (nand_64_out, nand_55_out, nand_55_out);
  nand nand_65 (nand_65_out, nand_56_out, nand_56_out);
  nand nand_66 (nand_66_out, nand_57_out, nand_58_out);
  nand nand_67 (nand_67_out, nand_58_out, nand_59_out);
  nand nand_68 (nand_68_out, nand_60_out, nand_61_out);
  nand nand_69 (nand_69_out, nand_62_out, nand_63_out);
  nand nand_70 (nand_70_out, nand_64_out, nand_65_out);
  nand nand_71 (nand_71_out, nand_66_out, nand_67_out);
  LED led_4 (.in(nand_68_out));
  LED led_5 (.in(nand_69_out));
  LED led_6 (.in(nand_70_out));
  LED led_7 (.in(nand_71_out));
  nand nand_72 (nand_72_out, in_53, in_53);
  nand nand_73 (nand_73_out, in_54, in_54);
  nand nand_74 (nand_74_out, in_51, in_51);
  nand nand_75 (nand_75_out, in_52, in_52);
  nor nor_1 (nor_1_out, in_1, in_3, in_5, in_7);
  xor xor_1 (xor_1_out, in_1, in_2);
  xor xor_2 (xor_2_out, in_3, in_4);
  xor xor_3 (xor_3_out, in_5, in_6);
  xor xor_4 (xor_4_out, in_7, in_8);
  nand nand_76 (nand_76_out, nand_72_out, nand_73_out);
  nand nand_77 (nand_77_out, nand_74_out, nand_75_out);
  nand nand_78 (nand_78_out, nand_76_out, nand_76_out);
  nand nand_79 (nand_79_out, nand_77_out, nand_77_out);
  nor nor_2 (nor_2_out, xor_1_out, xor_2_out, xor_3_out, xor_4_out);
  nand nand_80 (nand_80_out, nand_78_out, nand_79_out);
  LED led_8 (.in(nor_1_out));
  LED led_9 (.in(nor_2_out));
  nand nand_81 (nand_81_out, nLD, nLD);
  LED led_10 (.in(nand_80_out));
  nand nand_82 (nand_82_out, nand_120_out, nLD);
  nand nand_83 (nand_83_out, nand_81_out, DATA);
  nand nand_84 (nand_84_out, nand_82_out, nand_83_out);
  nand nand_85 (nand_85_out, in_9, in_10);
  nand nand_86 (nand_86_out, in_9, nand_85_out);
  nand nand_87 (nand_87_out, nand_85_out, in_10);
  nand nand_88 (nand_88_out, CK, CK);
  nand nand_89 (nand_89_out, nand_84_out, nand_84_out);
  nand nand_90 (nand_90_out, in_17, in_17);
  nand nand_91 (nand_91_out, nand_123_out, nand_123_out);
  nand nand_92 (nand_92_out, DAT_2, DAT_2);
  nand nand_93 (nand_93_out, in_15, in_15);
  nand nand_94 (nand_94_out, nand_84_out, nand_88_out);
  nand nand_95 (nand_95_out, nand_88_out, nand_89_out);
  nand nand_96 (nand_96_out, nand_86_out, nand_87_out);
  nand nand_97 (nand_97_out, nand_125_out, DAT, in_13);
  nand nand_98 (nand_98_out, in_13, DAT, nand_124_out);
  nand nand_99 (nand_99_out, in_13, in_13);
  nand nand_100 (nand_100_out, DAT_2, in_15);
  nand nand_101 (nand_101_out, in_15, nand_92_out);
  nand nand_102 (nand_102_out, nand_123_out, nand_90_out);
  nand nand_103 (nand_103_out, nand_90_out, nand_91_out);
  LED led_11 (.in(nand_96_out));
  nand nand_104 (nand_104_out, nand_94_out, nand_105_out);
  nand nand_105 (nand_105_out, nand_104_out, nand_95_out);
  nand nand_106 (nand_106_out, nand_97_out, nand_107_out);
  nand nand_107 (nand_107_out, nand_106_out, nand_98_out);
  nand nand_108 (nand_108_out, nand_100_out, nand_109_out);
  nand nand_109 (nand_109_out, nand_108_out, nand_101_out);
  nand nand_110 (nand_110_out, nand_102_out, nand_111_out);
  nand nand_111 (nand_111_out, nand_110_out, nand_103_out);
  nand nand_112 (nand_112_out, nand_104_out, CK);
  nand nand_113 (nand_113_out, CK, nand_105_out);
  nand nand_114 (nand_114_out, nand_106_out, nand_99_out);
  nand nand_115 (nand_115_out, nand_99_out, nand_107_out);
  nand nand_116 (nand_116_out, nand_108_out, nand_93_out);
  nand nand_117 (nand_117_out, nand_93_out, nand_109_out);
  nand nand_118 (nand_118_out, nand_110_out, in_17);
  nand nand_119 (nand_119_out, in_17, nand_111_out);
  nand nand_120 (nand_120_out, nand_112_out, nand_121_out);
  nand nand_121 (nand_121_out, nand_120_out, nand_113_out);
  nand nand_122 (nand_122_out, nand_118_out, nand_123_out);
  nand nand_123 (nand_123_out, nand_122_out, nand_119_out);
  nand nand_124 (nand_124_out, nand_114_out, nand_125_out);
  nand nand_125 (nand_125_out, nand_124_out, nand_115_out);
  nand nand_126 (nand_126_out, nand_116_out, nand_127_out);
  nand nand_127 (nand_127_out, nand_126_out, nand_117_out);
  LED Q (.in(nand_120_out));
  LED nQ (.in(nand_121_out));
  LED Q_2 (.in(nand_124_out));
  LED nQ_2 (.in(nand_125_out));
  LED Q_3 (.in(nand_126_out));
  LED nQ_3 (.in(nand_127_out));
  LED Q_4 (.in(nand_122_out));
  LED nQ_4 (.in(nand_123_out));

  // Notes on the sheet:
  //   4:1 Multiplexer
  //   4:1 Multiplexer (MK 2)
  //   4 Input AND-OR
  //   2-Input OR
  //   4-Input Nand
  //   4-bit Comparator A=B and Zero Detect A=0
  //   4 Input OR
  //   4002
  //   A=0
  //   A=B
  //   2 Input XOR
  //   1-bit register
  //   Master-Slave JK Flipflop
  //   D-Type Flipflop
  //   Toggle -Type Flipflop
endmodule
