// Digital circuit control_unit_1.dig as structural Verilog
module control_unit_1 (
  input  in_1,
  input  in_2,
  input  in_3
);

  wire AL, AR0, AR1, AR2, AR3, nand_1_out, nand_2_out, nand_3_out, nand_4_out, nand_5_out, nand_6_out,
       nand_7_out, nand_8_out, nand_9_out, nand_10_out, nand_11_out, nand_12_out, nand_13_out, nand_14_out,
       nand_15_out, nand_16_out, nand_17_out, nand_18_out, nand_19_out, nand_20_out, nand_21_out,
       nand_22_out, nand_23_out, nand_24_out, nand_25_out, nand_34_out, nand_35_out, nJMP, nW, pullup_1_out,
       pullup_2_out, pullup_3_out, pullup_4_out, pullup_5_out, W;

  nand nand_1 (nand_1_out, in_1, in_1);
  nand nand_2 (nand_2_out, in_2, in_2);
  nand nand_3 (nand_3_out, in_3, in_3);
  nand nand_4 (nand_4_out, nand_1_out, nand_2_out);
  nand nand_5 (nand_5_out, in_1, nand_2_out);
  nand nand_6 (nand_6_out, nand_1_out, in_2);
  nand nand_7 (nand_7_out, in_1, in_2);
  nand nand_8 (nand_8_out, nand_1_out, nand_2_out);
  nand nand_9 (nand_9_out, in_1, nand_2_out);
  nand nand_10 (nand_10_out, nand_1_out, in_2);
  nand nand_11 (nand_11_out, in_1, in_2);
  nand nand_12 (nand_12_out, nand_4_out, nand_4_out);
  nand nand_13 (nand_13_out, nand_5_out, nand_5_out);
  nand nand_14 (nand_14_out, nand_6_out, nand_6_out);
  nand nand_15 (nand_15_out, nand_7_out, nand_7_out);
  nand nand_16 (nand_16_out, nand_8_out, nand_8_out);
  nand nand_17 (nand_17_out, nand_9_out, nand_9_out);
  nand nand_18 (nand_18_out, nand_10_out, nand_10_out);
  nand nand_19 (nand_19_out, nand_11_out, nand_11_out);
  nand nand_20 (nand_20_out, nand_12_out, nand_3_out);
  nand nand_21 (nand_21_out, nand_13_out, nand_3_out);
  nand nand_22 (nand_22_out, nand_14_out, nand_3_out);
  nand nand_23 (nand_23_out, nand_15_out, nand_3_out);
  nand nand_24 (nand_24_out, nand_16_out, in_3);
  nand nand_25 (nand_25_out, nand_17_out, in_3);
  nand nand_26 (nW, nand_18_out, in_3);
  nand nand_27 (nJMP, nand_19_out, in_3);
  PullUp pullup_1 (.out(pullup_1_out));
  DiodeBackward diodebackward_1 (.in(nJMP), .out(pullup_1_out));
  DiodeBackward diodebackward_2 (.in(in_3), .out(pullup_1_out));
  nand nand_28 (AL, pullup_1_out, pullup_1_out);
  PullUp pullup_2 (.out(pullup_2_out));
  DiodeBackward diodebackward_3 (.in(nand_20_out), .out(pullup_2_out));
  DiodeBackward diodebackward_4 (.in(nand_21_out), .out(pullup_2_out));
  DiodeBackward diodebackward_5 (.in(nand_22_out), .out(pullup_2_out));
  DiodeBackward diodebackward_6 (.in(nand_24_out), .out(pullup_2_out));
  nand nand_29 (AR3, pullup_2_out, pullup_2_out);
  PullUp pullup_3 (.out(pullup_3_out));
  DiodeBackward diodebackward_7 (.in(nand_20_out), .out(pullup_3_out));
  DiodeBackward diodebackward_8 (.in(nand_22_out), .out(pullup_3_out));
  DiodeBackward diodebackward_9 (.in(nand_23_out), .out(pullup_3_out));
  DiodeBackward diodebackward_10 (.in(nand_24_out), .out(pullup_3_out));
  DiodeBackward diodebackward_11 (.in(nW), .out(pullup_3_out));
  nand nand_30 (AR2, pullup_3_out, pullup_3_out);
  PullUp pullup_4 (.out(pullup_4_out));
  DiodeBackward diodebackward_12 (.in(nand_22_out), .out(pullup_4_out));
  DiodeBackward diodebackward_13 (.in(nand_23_out), .out(pullup_4_out));
  DiodeBackward diodebackward_14 (.in(nand_25_out), .out(pullup_4_out));
  nand nand_31 (AR1, pullup_4_out, pullup_4_out);
  PullUp pullup_5 (.out(pullup_5_out));
  DiodeBackward diodebackward_15 (.in(nand_25_out), .out(pullup_5_out));
  DiodeBackward diodebackward_16 (.in(nW), .out(pullup_5_out));
  nand nand_32 (AR0, pullup_5_out, pullup_5_out);
  nand nand_33 (W, nW, nW);
  nand nand_34 (nand_34_out, 1'b0, 1'b0);
  LED led_1 (.in(nand_20_out));
  LED led_2 (.in(nand_21_out));
  LED led_3 (.in(nand_22_out));
  LED led_4 (.in(nand_23_out));
  LED led_5 (.in(nand_24_out));
  LED led_6 (.in(nand_25_out));
  LED led_7 (.in(nW));
  LED led_8 (.in(nJMP));
  nand nand_35 (nand_35_out, 1'b0, 1'b0);

  // Other names for the same wires on the sheet: IR5 = in_1; IR6 = in_2; IR7 = in_3

  // Notes on the sheet:
  //   CONTROL UNIT
  //   3 to 8 Instruction decoder - 27 Gates
  //   Octal Inverter/Driver
  //   LOAD
  //   AND
  //   OR
  //   XOR
  //   ADD
  //   SUB
  //   STORE
  //   JMP
endmodule
