// Digital circuit full_adder.dig as structural Verilog
module full_adder (
  input  A,
  input  B,
  input  C,
  input  in_8,
  input  in_9,
  input  in_10,
  input  in_11,
  output Sum,
  output Carry,
  output A_xor_B,
  output out_7
);

  wire nand_1_out, nand_2_out, nand_3_out, nand_4_out, nand_5_out, nand_8_out, nand_9_out, nand_10_out;

  nand nand_1 (nand_1_out, A, B);
  nand nand_2 (nand_2_out, A, nand_1_out);
  nand nand_3 (nand_3_out, nand_1_out, B);
  nand nand_4 (nand_4_out, in_8, in_9);
  nand nand_5 (nand_5_out, in_10, in_11);
  nand nand_6 (A_xor_B, nand_2_out, nand_3_out);
  nand nand_7 (out_7, nand_4_out, nand_5_out);
  nand nand_8 (nand_8_out, A_xor_B, C);
  nand nand_9 (nand_9_out, A_xor_B, nand_8_out);
  nand nand_10 (nand_10_out, nand_8_out, C);
  nand nand_11 (Sum, nand_9_out, nand_10_out);
  nand nand_12 (Carry, nand_8_out, nand_1_out);

  // Notes on the sheet:
  //   Half Adder
endmodule
