// Digital circuit half_adder.dig as structural Verilog
module half_adder (
  input  B,
  input  A,
  output Fout,
  output Cout
);

  wire nand_1_out, nand_2_out, nand_3_out, not_1_out, not_2_out;

  not not_1 (not_1_out, B);
  not not_2 (not_2_out, A);
  nand nand_1 (nand_1_out, A, not_1_out);
  nand nand_2 (nand_2_out, not_2_out, B);
  nand nand_3 (nand_3_out, A, B);
  nand nand_4 (Fout, nand_1_out, nand_2_out);
  not not_3 (Cout, nand_3_out);
endmodule
