// Digital circuit min_calc_1.dig as structural Verilog
module min_calc_1 (
  input  in_1,
  input  in_2,
  input  in_3,
  input  clk,
  input  in_7,
  input  in_8,
  input  in_9,
  input  in_10,
  output SUM,
  output Cout
);

  wire and_1_out, button_1_out, button_2_out, button_3_out, button_4_out, button_5_out, button_6_out,
       button_7_out, button_8_out, button_9_out, button_10_out, d_ff_1_nq, d_ff_2_nq, d_ff_3_nq, d_ff_4_nq,
       d_ff_5_nq, d_ff_6_nq, IC1_pin11, IC1_pin12, IC1_pin13, IC1_pin14, IC1_pin15, IC2_pin7, IC2_pin9,
       IC2_pin10, IC2_pin11, IC2_pin12, IC2_pin13, IC2_pin14, IC2_pin15, IC5_pin6, IC5_pin8, IC6_pin2,
       IC6_pin3, IC6_pin4, IC6_pin5, IC6_pin6, IC6_pin7, IC6_pin8, IC6_pin9, IC7_pin7, IC7_pin9, IC11_pin2,
       IC11_pin9, IC11_pin10, IC11_pin13, IC13_pin13, IC13_pin15, IC16_2_nq, IC16_nq, IC17_nq, IC17_q,
       nand_1_out, nand_2_out, nand_3_out, nand_4_out, nand_5_out, nand_6_out, nand_7_out, nand_8_out,
       nand_9_out, nand_10_out, nand_11_out, nand_12_out, nand_13_out, nand_14_out, nand_15_out, nand_17_out,
       nand_18_out, nand_19_out, nand_20_out, nand_21_out, or_2_out, xor_1_out, xor_3_out, xor_4_out;
  wire [3:0] d_ff_1_q, IC5_pin1, IC5_pin9, IC13_pin10;

  LED led_1 (.in(d_ff_1_q[3]));
  D_FF IC16 (.D(IC16_nq), .C(button_1_out), .Q(d_ff_1_q[3]), .nQ(IC16_nq));
  LED led_2 (.in(d_ff_1_q[2]));
  D_FF d_ff_1 (.D(d_ff_1_nq), .C(button_2_out), .Q(d_ff_1_q[2]), .nQ(d_ff_1_nq));
  Button button_1 (.out(button_1_out));
  LED led_3 (.in(d_ff_1_q[1]));
  D_FF d_ff_2 (.D(d_ff_2_nq), .C(button_3_out), .Q(d_ff_1_q[1]), .nQ(d_ff_2_nq));
  Button button_2 (.out(button_2_out));
  LED led_4 (.in(d_ff_1_q[0]));
  D_FF d_ff_3 (.D(d_ff_3_nq), .C(button_4_out), .Q(d_ff_1_q[0]), .nQ(d_ff_3_nq));
  Button button_3 (.out(button_3_out));
  _74166 IC13 (
    .pin1(1'b0), .pin2(d_ff_1_q[3]), .pin3(d_ff_1_q[2]), .pin4(d_ff_1_q[1]), .pin5(d_ff_1_q[0]), .pin6(1'b0),
    .pin7(clk), .pin8(1'b0), .pin9(1'b1), .pin10(IC13_pin10[3]), .pin11(IC13_pin10[2]),
    .pin12(IC13_pin10[1]), .pin13(IC13_pin13), .pin14(IC13_pin10[0]), .pin15(IC13_pin15), .pin16(1'b1));
  LED led_5 (.in(IC13_pin10[3]));
  D_FF d_ff_4 (.D(d_ff_4_nq), .C(button_5_out), .Q(IC13_pin10[3]), .nQ(d_ff_4_nq));
  Button button_4 (.out(button_4_out));
  LED led_6 (.in(IC13_pin10[2]));
  D_FF d_ff_5 (.D(d_ff_5_nq), .C(button_6_out), .Q(IC13_pin10[2]), .nQ(d_ff_5_nq));
  Button button_5 (.out(button_5_out));
  LED led_7 (.in(IC13_pin10[1]));
  D_FF d_ff_6 (.D(d_ff_6_nq), .C(button_7_out), .Q(IC13_pin10[1]), .nQ(d_ff_6_nq));
  Button button_6 (.out(button_6_out));
  LED led_8 (.in(IC13_pin10[0]));
  D_FF IC16_2 (.D(IC16_2_nq), .C(button_8_out), .Q(IC13_pin10[0]), .nQ(IC16_2_nq));
  Button button_7 (.out(button_7_out));
  nand nand_1 (nand_1_out, in_8, in_8);
  nand nand_2 (nand_2_out, nand_1_out, in_7);
  nand nand_3 (nand_3_out, in_8, in_7);
  and and_1 (and_1_out, nand_4_out, in_10);
  Seven_Seg_Hex seven_seg_hex_1 (.d(d_ff_1_q), .dp(1'b0));
  Button button_8 (.out(button_8_out));
  nand nand_4 (nand_4_out, nand_3_out, nand_3_out);
  Seven_Seg_Hex seven_seg_hex_2 (.d(IC13_pin10), .dp(1'b0));
  Button button_9 (.out(button_9_out));
  or or_1 (IC13_pin15, IC11_pin2, IC2_pin15);
  // PolarityAwareLED polarityawareled_1: pin names not known; wires that end beside it: 1'b1, IC13_pin15
  xor xor_1 (xor_1_out, IC13_pin15, button_9_out);
  // Probe Bin on IC13_pin13
  // Probe CLK on clk
  // Probe PC+ on nand_5_out
  nand nand_5 (nand_5_out, IC2_pin7, IC2_pin7);
  _7474 IC11 (
    .pin1(1'b1), .pin2(IC11_pin2), .pin3(xor_1_out), .pin4(1'b1), .pin6(IC11_pin2), .pin7(1'b0),
    .pin9(IC11_pin9), .pin10(IC11_pin10), .pin11(clk), .pin12(Cout), .pin13(IC11_pin13), .pin14(1'b1));  // open: pin5, pin8
  // Probe ~ADD/SUB on and_1_out
  _74161 IC1 (
    .pin1(1'b1), .pin2(clk), .pin3(in_1), .pin4(in_2), .pin5(in_3), .pin6(1'b1), .pin7(1'b1), .pin8(1'b0),
    .pin9(1'b1), .pin10(1'b1), .pin11(IC1_pin11), .pin12(IC1_pin12), .pin13(IC1_pin13), .pin14(IC1_pin14),
    .pin15(IC1_pin15), .pin16(1'b1));
  nand nand_6 (nand_6_out, and_1_out, IC2_pin15);
  LED led_9 (.in(IC11_pin10));
  xor xor_2 (IC11_pin10, and_1_out, nand_6_out);
  LED led_10 (.in(IC13_pin13));
  LED led_11 (.in(and_1_out));
  nand nand_7 (nand_7_out, IC1_pin12, IC1_pin13, IC1_pin14);
  LED led_12 (.in(IC6_pin9));
  _74138 IC2 (
    .pin1(IC1_pin14), .pin2(IC1_pin13), .pin3(IC1_pin12), .pin4(1'b0), .pin5(1'b0), .pin6(1'b1),
    .pin7(IC2_pin7), .pin8(1'b0), .pin9(IC2_pin9), .pin10(IC2_pin10), .pin11(IC2_pin11), .pin12(IC2_pin12),
    .pin13(IC2_pin13), .pin14(IC2_pin14), .pin15(IC2_pin15), .pin16(1'b1));
  LED led_13 (.in(IC11_pin9));
  xor xor_3 (xor_3_out, IC13_pin13, and_1_out);
  nand nand_8 (nand_8_out, clk, nand_7_out);
  // Probe Cin on IC11_pin9
  xor xor_4 (xor_4_out, IC6_pin9, xor_3_out);
  nand nand_9 (nand_9_out, xor_3_out, IC6_pin9);
  nand nand_10 (nand_10_out, IC6_pin9, IC6_pin9);
  nand nand_11 (nand_11_out, IC13_pin13, IC13_pin13);
  LED led_14 (.in(nand_8_out));
  // Probe 8PULSE on nand_8_out
  xor xor_5 (SUM, xor_4_out, IC11_pin9);
  nand nand_12 (nand_12_out, xor_4_out, IC11_pin9);
  nand nand_13 (nand_13_out, nand_11_out, nand_10_out);
  nand nand_14 (nand_14_out, nand_9_out, nand_9_out);
  LED led_15 (.in(IC2_pin15));
  LED led_16 (.in(IC2_pin14));
  LED led_17 (.in(IC2_pin13));
  LED led_18 (.in(IC2_pin12));
  LED led_19 (.in(IC2_pin11));
  LED led_20 (.in(IC2_pin10));
  LED led_21 (.in(IC2_pin9));
  LED led_22 (.in(IC2_pin7));
  nand nand_15 (nand_15_out, IC2_pin14, IC2_pin14);
  nand nand_16 (Cout, nand_12_out, nand_9_out);
  // Probe LD on nand_15_out
  _74153 IC7 (
    .pin1(nand_2_out), .pin2(in_9), .pin3(nand_10_out), .pin4(xor_4_out), .pin5(nand_13_out),
    .pin6(nand_14_out), .pin7(IC7_pin7), .pin8(1'b0), .pin9(IC7_pin9), .pin10(SUM), .pin11(SUM), .pin12(SUM),
    .pin13(SUM), .pin14(in_10), .pin15(nand_3_out), .pin16(1'b1));
  D_FF IC17 (.D(IC17_nq), .C(button_10_out), .Q(IC17_q), .nQ(IC17_nq));
  Button button_10 (.out(button_10_out));
  // PolarityAwareLED polarityawareled_2: pin names not known; wires that end beside it: 1'b1, nand_2_out
  nand nand_17 (nand_17_out, IC17_q, IC17_q);
  LED led_23 (.in(IC7_pin9));
  LED led_24 (.in(IC7_pin7));
  // PolarityAwareLED polarityawareled_3: pin names not known; wires that end beside it: 1'b1, nand_3_out
  or or_2 (or_2_out, IC7_pin9, IC7_pin7);
  _7425 IC5 (
    .pin1(IC5_pin1[3]), .pin2(IC5_pin1[2]), .pin4(IC5_pin1[1]), .pin5(IC5_pin1[0]), .pin6(IC5_pin6),
    .pin7(1'b0), .pin8(IC5_pin8), .pin9(IC5_pin9[3]), .pin10(IC5_pin9[2]), .pin12(IC5_pin9[1]),
    .pin13(IC5_pin9[0]), .pin14(1'b1));  // open: pin3, pin11
  nand nand_18 (nand_18_out, or_2_out, nand_17_out);
  nand nand_19 (nand_19_out, IC17_q, IC6_pin9);
  LED led_25 (.in(or_2_out));
  // Probe RESULT on or_2_out
  nand nand_20 (nand_20_out, IC5_pin8, IC5_pin6);
  nand nand_21 (nand_21_out, nand_18_out, nand_19_out);
  Reset reset_1 (.out(IC11_pin13));
  LED led_26 (.in(nand_20_out));
  // Probe Zero on nand_20_out
  _74574 IC6 (
    .pin1(1'b0), .pin2(IC6_pin2), .pin3(IC6_pin3), .pin4(IC6_pin4), .pin5(IC6_pin5), .pin6(IC6_pin6),
    .pin7(IC6_pin7), .pin8(IC6_pin8), .pin9(IC6_pin9), .pin10(1'b0), .pin11(nand_15_out),
    .pin12(IC5_pin1[0]), .pin13(IC5_pin1[1]), .pin14(IC5_pin1[2]), .pin15(IC5_pin1[3]), .pin16(IC5_pin9[0]),
    .pin17(IC5_pin9[1]), .pin18(IC5_pin9[2]), .pin19(IC5_pin9[3]), .pin20(1'b1));
  _74164 IC12 (
    .pin1(1'b1), .pin2(nand_21_out), .pin3(IC6_pin2), .pin4(IC6_pin3), .pin5(IC6_pin4), .pin6(IC6_pin5),
    .pin7(1'b0), .pin8(clk), .pin9(IC11_pin13), .pin10(IC6_pin6), .pin11(IC6_pin7), .pin12(IC6_pin8),
    .pin13(IC6_pin9), .pin14(1'b1));
  LED led_27 (.in(IC5_pin9[2]));
  LED led_28 (.in(IC5_pin9[3]));
  LED led_29 (.in(IC5_pin9[0]));
  LED led_30 (.in(IC5_pin9[1]));
  LED led_31 (.in(IC5_pin1[2]));
  LED led_32 (.in(IC5_pin1[3]));
  LED led_33 (.in(IC5_pin1[0]));
  LED led_34 (.in(IC5_pin1[1]));
  Seven_Seg_Hex seven_seg_hex_3 (.d(IC5_pin9), .dp(1'b0));
  Seven_Seg_Hex seven_seg_hex_4 (.d(IC5_pin1), .dp(1'b0));

  // Notes on the sheet:
  //   clk: Hz: 8
  //   ALU SECTION
  //   Enter B
  //   Input Register
  //   B Register
  //   INSTRUCTION  DECODE
  //   INSTRUCTION
  //   Deposit
  //   IC14
  //   LOGIC
  //   ARITHMETIC
  //   ~ADD/SUB
  //   SET CARRY LOGIC
  //   IC3A
  //   Carry FF
  //   Bit Counter
  //   B
  //   A
  //   Bit Slot Decoder
  //   Full Adder using XOR and NAND gates
  //   Cin
  //   IC8
  //   IC3C
  //   IC9 (XOR) IC10 (NAND)
  //   Bit Slot
  //   IC3B
  //   IC4
  //   Hold
  //   Zero Detect
  //   IC3D
  //   Shift/Hold Logic
  //   ALU Result Register
  //   Output Display
  //   Output Register
endmodule
