// Digital circuit min_calculator_7.dig as structural Verilog
module min_calculator_7 (
  input  in_1,
  input  in_2,
  input  in_3,
  input  in_4,
  input  CLK,
  input  in_6,
  input  in_7,
  input  in_8,
  input  in_9,
  output SUM,
  output Cout
);

  wire button_1_out, button_2_out, button_3_out, button_4_out, button_5_out, button_6_out, button_7_out,
       button_8_out, button_9_out, button_10_out, button_11_out, button_12_out, button_13_out, button_14_out,
       button_15_out, button_16_out, button_17_out, d_ff_1_nq, d_ff_2_nq, d_ff_3_nq, d_ff_4_nq, d_ff_5_nq,
       d_ff_6_nq, d_ff_7_nq, d_ff_8_nq, d_ff_9_nq, d_ff_10_nq, d_ff_11_nq, d_ff_12_nq, d_ff_13_nq, IC2_pin3,
       IC2_pin6, IC2_pin8, IC2_pin10, IC3_pin4, IC3_pin5, IC3_pin9, IC5_pin7, IC5_pin13, IC5_pin15,
       IC6_pin13, IC7_pin18, IC11_pin9, IC11_pin10, IC11_pin13, IC14_pin6, IC14_pin8, IC16_nq, IC17_2_nq,
       IC17_nq, monoflop_1_q, nand_1_out, nand_2_out, nand_3_out, nand_4_out, nand_5_out, nand_6_out,
       nand_8_out, nand_9_out, nand_10_out, xor_2_out, xor_3_out;
  wire [3:0] IC5_pin5, IC5_pin14, IC6_pin10, IC7_pin7, IC7_pin16, IC14_pin5, IC14_pin13, IC16_q;

  LED led_1 (.in(IC5_pin5[3]));
  D_FF IC17 (.D(IC17_nq), .C(button_1_out), .Q(IC5_pin5[3]), .nQ(IC17_nq));
  Button button_1 (.out(button_1_out));
  LED led_2 (.in(IC5_pin5[2]));
  D_FF d_ff_1 (.D(d_ff_1_nq), .C(button_2_out), .Q(IC5_pin5[2]), .nQ(d_ff_1_nq));
  Button button_2 (.out(button_2_out));
  LED led_3 (.in(IC5_pin5[1]));
  D_FF d_ff_2 (.D(d_ff_2_nq), .C(button_3_out), .Q(IC5_pin5[1]), .nQ(d_ff_2_nq));
  Button button_3 (.out(button_3_out));
  _74166 IC5 (
    .pin1(1'b0), .pin2(IC5_pin5[3]), .pin3(IC5_pin5[2]), .pin4(IC5_pin5[1]), .pin5(IC5_pin5[0]), .pin6(1'b0),
    .pin7(IC5_pin7), .pin8(1'b0), .pin9(1'b1), .pin10(IC5_pin14[3]), .pin11(IC5_pin14[2]),
    .pin12(IC5_pin14[1]), .pin13(IC5_pin13), .pin14(IC5_pin14[0]), .pin15(IC5_pin15), .pin16(1'b1));
  LED led_4 (.in(IC5_pin5[0]));
  D_FF d_ff_3 (.D(d_ff_3_nq), .C(button_4_out), .Q(IC5_pin5[0]), .nQ(d_ff_3_nq));
  Button button_4 (.out(button_4_out));
  LED led_5 (.in(IC5_pin14[3]));
  D_FF d_ff_4 (.D(d_ff_4_nq), .C(button_5_out), .Q(IC5_pin14[3]), .nQ(d_ff_4_nq));
  Button button_5 (.out(button_5_out));
  LED led_6 (.in(IC5_pin14[2]));
  D_FF d_ff_5 (.D(d_ff_5_nq), .C(button_6_out), .Q(IC5_pin14[2]), .nQ(d_ff_5_nq));
  Button button_6 (.out(button_6_out));
  LED led_7 (.in(IC5_pin14[1]));
  D_FF d_ff_6 (.D(d_ff_6_nq), .C(button_7_out), .Q(IC5_pin14[1]), .nQ(d_ff_6_nq));
  Button button_7 (.out(button_7_out));
  LED led_8 (.in(IC5_pin14[0]));
  D_FF IC17_2 (.D(IC17_2_nq), .C(button_8_out), .Q(IC5_pin14[0]), .nQ(IC17_2_nq));
  Button button_8 (.out(button_8_out));
  Seven_Seg_Hex seven_seg_hex_1 (.d(IC5_pin5), .dp(1'b0));
  _74299 IC7 (
    .pin1(in_9), .pin2(in_6), .pin3(in_7), .pin4(IC7_pin16[2]), .pin5(IC7_pin16[0]), .pin6(IC7_pin7[2]),
    .pin7(IC7_pin7[0]), .pin9(1'b1), .pin10(1'b0), .pin11(in_8), .pin12(IC5_pin7), .pin13(IC7_pin7[1]),
    .pin14(IC7_pin7[3]), .pin15(IC7_pin16[1]), .pin16(IC7_pin16[3]), .pin18(IC7_pin18), .pin19(1'b1),
    .pin20(1'b1));  // open: pin8, pin17
  Seven_Seg_Hex seven_seg_hex_2 (.d(IC5_pin14), .dp(1'b0));
  LED led_9 (.in(IC16_q[3]));
  D_FF IC16 (.D(IC16_nq), .C(button_9_out), .Q(IC16_q[3]), .nQ(IC16_nq));
  LED led_10 (.in(IC16_q[2]));
  D_FF d_ff_7 (.D(d_ff_7_nq), .C(button_10_out), .Q(IC16_q[2]), .nQ(d_ff_7_nq));
  Button button_9 (.out(button_9_out));
  LED led_11 (.in(IC16_q[1]));
  D_FF d_ff_8 (.D(d_ff_8_nq), .C(button_11_out), .Q(IC16_q[1]), .nQ(d_ff_8_nq));
  Button button_10 (.out(button_10_out));
  LED led_12 (.in(IC16_q[0]));
  D_FF d_ff_9 (.D(d_ff_9_nq), .C(button_12_out), .Q(IC16_q[0]), .nQ(d_ff_9_nq));
  Button button_11 (.out(button_11_out));
  LED led_13 (.in(IC7_pin16[3]));
  LED led_14 (.in(IC7_pin16[2]));
  _74166 IC6 (
    .pin1(1'b0), .pin2(IC16_q[3]), .pin3(IC16_q[2]), .pin4(IC16_q[1]), .pin5(IC16_q[0]), .pin6(1'b0),
    .pin7(IC5_pin7), .pin8(1'b0), .pin9(1'b1), .pin10(IC6_pin10[3]), .pin11(IC6_pin10[2]),
    .pin12(IC6_pin10[1]), .pin13(IC6_pin13), .pin14(IC6_pin10[0]), .pin15(IC5_pin15), .pin16(1'b1));
  LED led_15 (.in(IC6_pin10[3]));
  D_FF d_ff_10 (.D(d_ff_10_nq), .C(button_13_out), .Q(IC6_pin10[3]), .nQ(d_ff_10_nq));
  Button button_12 (.out(button_12_out));
  LED led_16 (.in(IC7_pin16[1]));
  LED led_17 (.in(IC7_pin16[0]));
  LED led_18 (.in(IC6_pin10[2]));
  D_FF d_ff_11 (.D(d_ff_11_nq), .C(button_14_out), .Q(IC6_pin10[2]), .nQ(d_ff_11_nq));
  Button button_13 (.out(button_13_out));
  LED led_19 (.in(IC7_pin7[3]));
  LED led_20 (.in(IC7_pin7[2]));
  LED led_21 (.in(IC6_pin10[1]));
  D_FF d_ff_12 (.D(d_ff_12_nq), .C(button_15_out), .Q(IC6_pin10[1]), .nQ(d_ff_12_nq));
  Button button_14 (.out(button_14_out));
  LED led_22 (.in(IC7_pin7[1]));
  LED led_23 (.in(IC7_pin7[0]));
  LED led_24 (.in(IC6_pin10[0]));
  D_FF d_ff_13 (.D(d_ff_13_nq), .C(button_16_out), .Q(IC6_pin10[0]), .nQ(d_ff_13_nq));
  Button button_15 (.out(button_15_out));
  Seven_Seg_Hex seven_seg_hex_3 (.d(IC7_pin16), .dp(1'b0));
  Seven_Seg_Hex seven_seg_hex_4 (.d(IC16_q), .dp(1'b0));
  Button button_16 (.out(button_16_out));
  Seven_Seg_Hex seven_seg_hex_5 (.d(IC7_pin7), .dp(1'b0));
  Button button_17 (.out(button_17_out));
  Seven_Seg_Hex seven_seg_hex_6 (.d(IC6_pin10), .dp(1'b0));
  Monoflop #(.timerDelay(2)) monoflop_1 (.C(button_17_out), .R(1'b0), .Q(monoflop_1_q));  // open: nQ
  // Probe LD on IC5_pin15
  Monoflop monoflop_2 (.C(IC2_pin8), .R(1'b0), .nQ(IC5_pin15));  // open: Q
  _7474 IC11 (
    .pin1(1'b0), .pin2(1'b0), .pin3(1'b0), .pin4(1'b0), .pin7(1'b0), .pin9(IC11_pin9), .pin10(IC11_pin10),
    .pin11(IC5_pin7), .pin12(Cout), .pin13(IC11_pin13), .pin14(1'b1));  // open: pin5, pin6, pin8
  _7474 IC2 (
    .pin1(1'b1), .pin2(monoflop_1_q), .pin3(IC2_pin3), .pin4(1'b1), .pin6(IC2_pin6), .pin7(1'b0),
    .pin8(IC2_pin8), .pin10(IC2_pin10), .pin11(1'b1), .pin12(IC2_pin8), .pin13(IC2_pin6), .pin14(1'b1));  // open: pin5, pin9
  LED led_25 (.in(in_4));
  Reset reset_1 (.out(IC11_pin13));
  xor xor_1 (IC11_pin10, nand_1_out, in_4);
  nand nand_1 (nand_1_out, in_4, IC5_pin15);
  _7400 IC3 (
    .pin1(CLK), .pin2(CLK), .pin3(IC2_pin3), .pin4(IC3_pin4), .pin5(IC3_pin5), .pin6(IC2_pin10), .pin7(1'b0),
    .pin8(IC5_pin7), .pin9(IC3_pin9), .pin10(IC3_pin9), .pin11(IC3_pin9), .pin12(IC2_pin8), .pin13(CLK),
    .pin14(1'b1));
  // Probe SS on IC2_pin8
  nand nand_2 (nand_2_out, IC2_pin10, IC2_pin10);
  LED led_26 (.in(IC11_pin9));
  LED led_27 (.in(IC6_pin13));
  LED led_28 (.in(IC5_pin13));
  _74163 IC1 (
    .pin1(IC2_pin8), .pin2(CLK), .pin3(1'b0), .pin4(1'b0), .pin5(1'b0), .pin6(1'b0), .pin7(IC2_pin8),
    .pin8(1'b0), .pin9(1'b1), .pin10(1'b1), .pin11(IC3_pin5), .pin14(IC3_pin4), .pin16(1'b1));  // open: pin12, pin13, pin15
  // Probe Cin on IC11_pin9
  // Probe Bin on IC6_pin13
  xor xor_2 (xor_2_out, IC6_pin13, in_4);
  xor xor_3 (xor_3_out, xor_2_out, IC5_pin13);
  nand nand_3 (nand_3_out, IC5_pin13, xor_2_out);
  nand nand_4 (nand_4_out, IC5_pin13, IC5_pin13);
  nand nand_5 (nand_5_out, IC6_pin13, IC6_pin13);
  xor xor_4 (SUM, xor_3_out, IC11_pin9);
  nand nand_6 (nand_6_out, xor_3_out, IC11_pin9);
  nand nand_7 (Cout, nand_6_out, nand_3_out);
  nand nand_8 (nand_8_out, nand_4_out, nand_5_out);
  nand nand_9 (nand_9_out, nand_3_out, nand_3_out);
  _74151 IC13 (
    .pin1(nand_4_out), .pin2(xor_3_out), .pin3(nand_8_out), .pin4(nand_9_out), .pin5(IC7_pin18), .pin7(in_1),
    .pin8(1'b0), .pin9(in_2), .pin10(in_3), .pin11(in_4), .pin12(SUM), .pin13(SUM), .pin14(SUM), .pin15(SUM),
    .pin16(1'b1));  // open: pin6
  LED led_29 (.in(Cout));
  LED led_30 (.in(SUM));
  _7425 IC14 (
    .pin1(IC14_pin5[0]), .pin2(IC14_pin5[1]), .pin4(IC14_pin5[2]), .pin5(IC14_pin5[3]), .pin6(IC14_pin6),
    .pin7(1'b0), .pin8(IC14_pin8), .pin9(IC14_pin13[0]), .pin10(IC14_pin13[1]), .pin12(IC14_pin13[2]),
    .pin13(IC14_pin13[3]), .pin14(1'b1));  // open: pin3, pin11
  _74595 IC8 (
    .pin1(IC14_pin5[2]), .pin2(IC14_pin5[1]), .pin3(IC14_pin5[0]), .pin4(IC14_pin13[3]),
    .pin5(IC14_pin13[2]), .pin6(IC14_pin13[1]), .pin7(IC14_pin13[0]), .pin8(1'b0), .pin9(IC7_pin18),
    .pin10(1'b1), .pin11(nand_2_out), .pin12(IC5_pin7), .pin13(1'b0), .pin15(IC14_pin5[3]), .pin16(1'b1));  // open: pin14
  nand nand_10 (nand_10_out, IC14_pin8, IC14_pin6);
  LED led_31 (.in(nand_10_out));
  // Probe Zero on nand_10_out
  // Probe Dout on IC7_pin18
  // Probe SCK on IC5_pin7
  // Probe LATCH on nand_2_out
  Seven_Seg_Hex seven_seg_hex_7 (.d(IC14_pin5), .dp(1'b0));
  Seven_Seg_Hex seven_seg_hex_8 (.d(IC14_pin13), .dp(1'b0));

  // Notes on the sheet:
  //   CLK: Hz: 2
  //   8-bit Serial ALU
  //   SCK
  //   A Register
  //   S1     S0       MODE
  //   0          0       HOLD
  //   0          1       RIGHT
  //   1          0       LEFT
  //   1          1       LOAD
  //   ALU Result Register
  //   A in
  //   B Register
  //   B in
  //   LOAD
  //   INSTRUCTION
  //   SPI Sequencer
  //   TRIG
  //   Carry FF
  //   SET CARRY LOGIC
  //   ~ADD/SUB
  //   IC15B
  //   Full Adder using XOR and NAND gates
  //   Cin
  //   Ain
  //   Bin
  //   A
  //   B
  //   NotB
  //   IC9 (XOR)
  //   IC10 (NAND)
  //   IC12
  //   AxorB
  //   NOT
  //   XOR
  //   OR
  //   AND
  //   Dout
  //   Cout
  //   SUM
  //   Zero Detect
  //   Slave Register
  //   IC15A
endmodule
