// Digital circuit minimal_calculator.dig as structural Verilog
module minimal_calculator (
  input  in_1,
  input  in_2,
  input  in_3,
  input  clk,
  input  in_7,
  input  in_8,
  input  in_9,
  input  in_10,
  output SUM,
  output Cout
);

  wire _7425_1_pin6, _7425_1_pin8, _74153_1_pin7, _74153_1_pin9, button_1_out, button_2_out, button_3_out,
       button_4_out, button_5_out, button_6_out, button_7_out, button_8_out, button_9_out, button_10_out,
       button_11_out, d_ff_1_nq, d_ff_2_nq, d_ff_3_nq, d_ff_4_nq, d_ff_5_nq, d_ff_6_nq, d_ff_7_nq, IC1_pin11,
       IC1_pin12, IC1_pin13, IC1_pin14, IC1_pin15, IC2_pin7, IC2_pin9, IC2_pin10, IC2_pin11, IC2_pin12,
       IC2_pin13, IC2_pin14, IC2_pin15, IC11_pin9, IC11_pin10, IC11_pin13, IC13_pin2, IC13_pin3, IC13_pin4,
       IC13_pin5, IC13_pin6, IC13_pin7, IC13_pin8, IC13_pin9, IC16_2_pin13, IC16_2_pin15, IC16_3_nq, IC16_nq,
       IC17_nq, IC17_q, nand_1_out, nand_2_out, nand_3_out, nand_4_out, nand_5_out, nand_6_out, nand_7_out,
       nand_8_out, nand_9_out, nand_10_out, nand_11_out, nand_12_out, nand_13_out, nand_14_out, nand_15_out,
       nand_17_out, nand_18_out, nand_19_out, nand_20_out, nand_21_out, not_1_out, not_2_out, or_2_out,
       rs_ff_as_1_q, xor_2_out, xor_3_out;
  wire [3:0] _7425_1_pin1, _7425_1_pin9, IC16_2_pin10, IC16_q;

  // Probe CLK on clk
  nand nand_1 (nand_1_out, IC2_pin7, IC2_pin7);
  LED led_1 (.in(IC16_q[3]));
  D_FF IC16 (.D(IC16_nq), .C(button_1_out), .Q(IC16_q[3]), .nQ(IC16_nq));
  Button button_1 (.out(button_1_out));
  Button button_2 (.out(button_2_out));
  _7474 IC11 (
    .pin1(1'b0), .pin2(1'b0), .pin3(1'b0), .pin4(1'b0), .pin7(1'b0), .pin9(IC11_pin9), .pin10(IC11_pin10),
    .pin11(clk), .pin12(Cout), .pin13(IC11_pin13), .pin14(1'b1));  // open: pin5, pin6, pin8
  LED led_2 (.in(IC16_q[2]));
  D_FF d_ff_1 (.D(d_ff_1_nq), .C(button_3_out), .Q(IC16_q[2]), .nQ(d_ff_1_nq));
  Button button_3 (.out(button_3_out));
  _74161 IC1 (
    .pin1(1'b1), .pin2(clk), .pin3(in_1), .pin4(in_2), .pin5(in_3), .pin6(1'b1), .pin7(1'b1), .pin8(1'b0),
    .pin9(1'b1), .pin10(1'b1), .pin11(IC1_pin11), .pin12(IC1_pin12), .pin13(IC1_pin13), .pin14(IC1_pin14),
    .pin15(IC1_pin15), .pin16(1'b1));
  RS_FF_AS rs_ff_as_1 (.S(button_2_out), .R(IC1_pin15), .Q(rs_ff_as_1_q));  // open: nQ
  nand nand_2 (nand_2_out, nand_15_out, IC2_pin15);
  LED led_3 (.in(IC16_q[1]));
  D_FF d_ff_2 (.D(d_ff_2_nq), .C(button_4_out), .Q(IC16_q[1]), .nQ(d_ff_2_nq));
  Button button_4 (.out(button_4_out));
  LED led_4 (.in(IC11_pin10));
  xor xor_1 (IC11_pin10, nand_15_out, nand_2_out);
  _74166 IC16_2 (
    .pin1(1'b0), .pin2(IC16_q[3]), .pin3(IC16_q[2]), .pin4(IC16_q[1]), .pin5(IC16_q[0]), .pin6(1'b0),
    .pin7(clk), .pin8(1'b0), .pin9(1'b1), .pin10(IC16_2_pin10[3]), .pin11(IC16_2_pin10[2]),
    .pin12(IC16_2_pin10[1]), .pin13(IC16_2_pin13), .pin14(IC16_2_pin10[0]), .pin15(IC16_2_pin15), .pin16(1'b1));
  LED led_5 (.in(IC16_q[0]));
  D_FF d_ff_3 (.D(d_ff_3_nq), .C(button_5_out), .Q(IC16_q[0]), .nQ(d_ff_3_nq));
  Button button_5 (.out(button_5_out));
  LED led_6 (.in(IC16_2_pin10[3]));
  D_FF d_ff_4 (.D(d_ff_4_nq), .C(button_6_out), .Q(IC16_2_pin10[3]), .nQ(d_ff_4_nq));
  Button button_6 (.out(button_6_out));
  LED led_7 (.in(IC16_2_pin13));
  LED led_8 (.in(IC16_2_pin10[2]));
  D_FF d_ff_5 (.D(d_ff_5_nq), .C(button_7_out), .Q(IC16_2_pin10[2]), .nQ(d_ff_5_nq));
  Button button_7 (.out(button_7_out));
  nand nand_3 (nand_3_out, IC1_pin12, IC1_pin13, IC1_pin14);
  LED led_9 (.in(IC13_pin9));
  // Probe Bin on IC16_2_pin13
  LED led_10 (.in(IC16_2_pin10[1]));
  D_FF d_ff_6 (.D(d_ff_6_nq), .C(button_8_out), .Q(IC16_2_pin10[1]), .nQ(d_ff_6_nq));
  Button button_8 (.out(button_8_out));
  _74138 IC2 (
    .pin1(IC1_pin14), .pin2(IC1_pin13), .pin3(IC1_pin12), .pin4(1'b0), .pin5(1'b0), .pin6(1'b1),
    .pin7(IC2_pin7), .pin8(1'b0), .pin9(IC2_pin9), .pin10(IC2_pin10), .pin11(IC2_pin11), .pin12(IC2_pin12),
    .pin13(IC2_pin13), .pin14(IC2_pin14), .pin15(IC2_pin15), .pin16(1'b1));
  LED led_11 (.in(IC11_pin9));
  xor xor_2 (xor_2_out, IC16_2_pin13, nand_15_out);
  LED led_12 (.in(IC16_2_pin10[0]));
  D_FF IC16_3 (.D(IC16_3_nq), .C(button_9_out), .Q(IC16_2_pin10[0]), .nQ(IC16_3_nq));
  Button button_9 (.out(button_9_out));
  nand nand_4 (nand_4_out, clk, nand_3_out);
  // Probe Cin on IC11_pin9
  Seven_Seg_Hex seven_seg_hex_1 (.d(IC16_q), .dp(1'b0));
  xor xor_3 (xor_3_out, IC13_pin9, xor_2_out);
  nand nand_5 (nand_5_out, xor_2_out, IC13_pin9);
  nand nand_6 (nand_6_out, IC13_pin9, IC13_pin9);
  nand nand_7 (nand_7_out, IC16_2_pin13, IC16_2_pin13);
  Seven_Seg_Hex seven_seg_hex_2 (.d(IC16_2_pin10), .dp(1'b0));
  LED led_13 (.in(nand_4_out));
  or or_1 (IC16_2_pin15, d_ff_7_nq, IC2_pin15);
  D_FF d_ff_7 (.D(d_ff_7_nq), .C(button_10_out), .nQ(d_ff_7_nq));  // open: Q
  Button button_10 (.out(button_10_out));
  Button button_11 (.out(button_11_out));
  LED led_14 (.in(IC16_2_pin15));
  // Probe 8PULSE on nand_4_out
  D_FF IC17 (.D(IC17_nq), .C(button_11_out), .Q(IC17_q), .nQ(IC17_nq));
  xor xor_4 (SUM, xor_3_out, IC11_pin9);
  nand nand_8 (nand_8_out, xor_3_out, IC11_pin9);
  LED led_15 (.in(IC2_pin15));
  LED led_16 (.in(IC2_pin14));
  LED led_17 (.in(IC2_pin13));
  LED led_18 (.in(IC2_pin12));
  LED led_19 (.in(IC2_pin11));
  LED led_20 (.in(IC2_pin10));
  LED led_21 (.in(IC2_pin9));
  LED led_22 (.in(IC2_pin7));
  nand nand_9 (nand_9_out, IC2_pin14, IC2_pin14);
  nand nand_10 (nand_10_out, nand_7_out, nand_6_out);
  nand nand_11 (nand_11_out, nand_5_out, nand_5_out);
  nand nand_12 (nand_12_out, in_8, in_8);
  nand nand_13 (nand_13_out, nand_12_out, in_7);
  nand nand_14 (nand_14_out, in_8, in_7);
  nand nand_15 (nand_15_out, nand_14_out, in_10);
  nand nand_16 (Cout, nand_8_out, nand_5_out);
  nand nand_17 (nand_17_out, IC17_q, IC17_q);
  _74153 _74153_1 (
    .pin1(nand_13_out), .pin2(in_9), .pin3(nand_6_out), .pin4(xor_3_out), .pin5(nand_10_out),
    .pin6(nand_11_out), .pin7(_74153_1_pin7), .pin8(1'b0), .pin9(_74153_1_pin9), .pin10(SUM), .pin11(SUM),
    .pin12(SUM), .pin13(SUM), .pin14(in_10), .pin15(nand_14_out), .pin16(1'b1));
  not not_1 (not_1_out, nand_13_out);
  _7425 _7425_1 (
    .pin1(_7425_1_pin1[3]), .pin2(_7425_1_pin1[2]), .pin4(_7425_1_pin1[1]), .pin5(_7425_1_pin1[0]),
    .pin6(_7425_1_pin6), .pin7(1'b0), .pin8(_7425_1_pin8), .pin9(_7425_1_pin9[3]), .pin10(_7425_1_pin9[2]),
    .pin12(_7425_1_pin9[1]), .pin13(_7425_1_pin9[0]), .pin14(1'b1));  // open: pin3, pin11
  nand nand_18 (nand_18_out, SUM, nand_17_out);
  nand nand_19 (nand_19_out, IC17_q, IC13_pin9);
  LED led_23 (.in(nand_15_out));
  LED led_24 (.in(not_1_out));
  nand nand_20 (nand_20_out, _7425_1_pin8, _7425_1_pin6);
  nand nand_21 (nand_21_out, nand_18_out, nand_19_out);
  Reset reset_1 (.out(IC11_pin13));
  not not_2 (not_2_out, nand_14_out);
  LED led_25 (.in(_74153_1_pin9));
  LED led_26 (.in(_74153_1_pin7));
  LED led_27 (.in(nand_20_out));
  LED led_28 (.in(not_2_out));
  or or_2 (or_2_out, _74153_1_pin9, _74153_1_pin7);
  // Probe Zero on nand_20_out
  LED led_29 (.in(or_2_out));
  _74574 IC13 (
    .pin1(1'b0), .pin2(IC13_pin2), .pin3(IC13_pin3), .pin4(IC13_pin4), .pin5(IC13_pin5), .pin6(IC13_pin6),
    .pin7(IC13_pin7), .pin8(IC13_pin8), .pin9(IC13_pin9), .pin10(1'b0), .pin11(nand_9_out),
    .pin12(_7425_1_pin1[0]), .pin13(_7425_1_pin1[1]), .pin14(_7425_1_pin1[2]), .pin15(_7425_1_pin1[3]),
    .pin16(_7425_1_pin9[0]), .pin17(_7425_1_pin9[1]), .pin18(_7425_1_pin9[2]), .pin19(_7425_1_pin9[3]),
    .pin20(1'b1));
  _74164 IC12 (
    .pin1(1'b1), .pin2(nand_21_out), .pin3(IC13_pin2), .pin4(IC13_pin3), .pin5(IC13_pin4), .pin6(IC13_pin5),
    .pin7(1'b0), .pin8(clk), .pin9(IC11_pin13), .pin10(IC13_pin6), .pin11(IC13_pin7), .pin12(IC13_pin8),
    .pin13(IC13_pin9), .pin14(1'b1));
  LED led_30 (.in(_7425_1_pin9[2]));
  LED led_31 (.in(_7425_1_pin9[3]));
  LED led_32 (.in(_7425_1_pin9[0]));
  LED led_33 (.in(_7425_1_pin9[1]));
  LED led_34 (.in(_7425_1_pin1[2]));
  LED led_35 (.in(_7425_1_pin1[3]));
  LED led_36 (.in(_7425_1_pin1[0]));
  LED led_37 (.in(_7425_1_pin1[1]));
  Seven_Seg_Hex seven_seg_hex_3 (.d(_7425_1_pin9), .dp(1'b0));
  Seven_Seg_Hex seven_seg_hex_4 (.d(_7425_1_pin1), .dp(1'b0));

  // Notes on the sheet:
  //   clk: Hz: 2
  //   CALCULATOR SECTION
  //   Enter B
  //   Carry FF
  //   SET CARRY LOGIC
  //   Bit Counter
  //   Full Adder using XOR and NAND gates
  //   B Register
  //   B
  //   A
  //   Bit Slot Decoder
  //   Cin
  //   IC18
  //   Deposit
  //   Hold
  //   IC9 (XOR) IC10 (NAND)
  //   INST DECODE
  //   Bit Slot
  //   Zero Detect
  //   ~ADD/SUB
  //   LOGIC
  //   Shift/Hold Logic
  //   ALU Result Register
  //   ARITHMETIC
  //   Output Display
endmodule
