// Digital circuit mux_74153.dig as structural Verilog
module mux_74153 (
  input  I3,
  input  I2,
  input  I1,
  input  I0,
  input  B,
  input  A,
  input  Cin,
  input  I1_2,
  input  A_2,
  input  B_2,
  input  C,
  input  I0_2,
  output Sum,
  output Cout,
  output Sum_Diff,
  output Carry,
  output Borrow
);

  wire nand_1_out, nand_2_out, nand_3_out, nand_4_out, nand_5_out, nand_6_out, nand_7_out, nand_8_out,
       nand_9_out, nand_10_out, nand_11_out, nand_12_out, nand_13_out, nand_14_out, nand_15_out, nand_16_out,
       nand_17_out, nand_18_out, nand_19_out, nand_20_out, nand_21_out, nand_22_out, nand_23_out,
       nand_25_out, nand_26_out;

  nand nand_1 (nand_1_out, A_2, B_2);
  nand nand_2 (nand_2_out, B, B);
  nand nand_3 (nand_3_out, A, A);
  nand nand_4 (nand_4_out, A_2, nand_1_out);
  nand nand_5 (nand_5_out, nand_1_out, B_2);
  nand nand_6 (nand_6_out, I3, A);
  nand nand_7 (nand_7_out, I2, nand_3_out);
  nand nand_8 (nand_8_out, I1, A);
  nand nand_9 (nand_9_out, I0, nand_3_out);
  nand nand_10 (nand_10_out, B_2, nand_1_out);
  nand nand_11 (nand_11_out, nand_4_out, nand_5_out);
  nand nand_12 (nand_12_out, nand_6_out, nand_7_out);
  nand nand_13 (nand_13_out, nand_8_out, nand_9_out);
  nand nand_14 (nand_14_out, B, nand_12_out);
  nand nand_15 (nand_15_out, nand_13_out, nand_2_out);
  nand nand_16 (nand_16_out, I1_2, nand_10_out);
  nand nand_17 (nand_17_out, nand_11_out, I0_2);
  nand nand_18 (nand_18_out, nand_14_out, nand_15_out);
  nand nand_19 (nand_19_out, nand_16_out, nand_17_out);
  nand nand_20 (nand_20_out, nand_19_out, C);
  nand nand_21 (nand_21_out, nand_18_out, Cin);
  nand nand_22 (nand_22_out, nand_19_out, nand_20_out);
  nand nand_23 (nand_23_out, nand_20_out, C);
  nand nand_24 (Cout, nand_21_out, nand_18_out);
  nand nand_25 (nand_25_out, nand_18_out, nand_21_out);
  nand nand_26 (nand_26_out, nand_21_out, Cin);
  nand nand_27 (Sum, nand_25_out, nand_26_out);
  nand nand_28 (Carry, nand_1_out, nand_20_out);
  nand nand_29 (Sum_Diff, nand_22_out, nand_23_out);
  nand nand_30 (Borrow, nand_5_out, nand_23_out);

  // Notes on the sheet:
  //   Instruction I3 I2 I1 I0
  //   0000   F = 0
  //   0001   F = A NOR B
  //   0010   F = A AND ~B
  //   0011  F = ~B
  //   0100  F = ~A AND B
  //   0101  F = ~A
  //   0110  F = A XOR B
  //   0111  F = A NAND B
  //   1000  F = A AND B
  //   1001  F = A XNOR B
  //   1010  F = A
  //   1011  F = A OR ~B
  //   1100  F = B
  //   1101 F = ~A OR B
  //   1110   F = A OR B
  //   1111  F = 1
  //   C  I1 I0
  //   0   0   0    F = 0
  //   0   0   1    F = A XOR B 
  //   0   1   0    F = A AND B
  //   0   1   1    F = A OR B
  //   1   0   0    F = 1
  //   1   0   1    F = A XNOR B
  //   1   1   0    F = A NAND B
  //   1   1   1    F = A NOR B
  //   Half Adder AND/XOR
  //   LOGIC UNIT (74HC153 4:1 MUX)
  //   2 Input Mux
  //   13 Gate ALU
  //   Half Adder / Invert
endmodule
