// Digital circuit mux_flipflop.dig as structural Verilog
module mux_flipflop (
  input  Data,
  input  CLK,
  output Q,
  output nQ
);

  wire nand_1_out, nand_2_out, nand_3_out, nand_4_out, nand_5_out, nand_6_out, nand_7_out;

  nand nand_1 (nand_1_out, CLK, CLK);
  nand nand_2 (nand_2_out, Data, nand_1_out);
  nand nand_3 (nand_3_out, nand_2_out, nand_1_out);
  nand nand_4 (nand_4_out, nand_2_out, nand_5_out);
  nand nand_5 (nand_5_out, nand_4_out, nand_3_out);
  nand nand_6 (nand_6_out, nand_4_out, CLK);
  nand nand_7 (nand_7_out, nand_6_out, CLK);
  nand nand_8 (Q, nand_6_out, nQ);
  nand nand_9 (nQ, Q, nand_7_out);

  // Notes on the sheet:
  //   CLK: Hz: 2147483647
  //   Master Slave arrangement using gated D-type latches
  //   Master
  //   Slave
endmodule
