// Digital circuit steering_logic.dig as structural Verilog
module steering_logic (
  input  SEL,
  input  OE,
  input  SEL_2,
  input  OE_2,
  output S0,
  output S1,
  output S2,
  output S3
);

  wire nand_1_out, nand_2_out, not_1_out, not_2_out, not_3_out;

  not not_1 (not_1_out, SEL_2);
  and and_1 (S2, ~OE_2, ~SEL_2);  // And
  and and_2 (S3, ~OE_2, ~not_1_out);  // And
  not not_2 (not_2_out, SEL);
  not not_3 (not_3_out, OE);
  nand nand_1 (nand_1_out, not_3_out, not_2_out);
  nand nand_2 (nand_2_out, not_3_out, SEL);
  not not_4 (S0, nand_1_out);
  not not_5 (S1, nand_2_out);
endmodule
