// Digital circuit testbed15.dig as structural Verilog
module testbed15 (
  input  clk,
  input  I0,
  input  I1,
  input  nADD,
  output SUM,
  output Cout,
  output Fout,
  output Cb_2,
  output SUM_2,
  output Cout_2
);

  wire _74151_1_pin5, _74151_2_pin5, _74163_1_pin15, Aout, Bout, button_1_out, button_2_out, button_3_out,
       button_4_out, button_5_out, button_6_out, button_7_out, button_8_out, button_9_out, button_10_out,
       button_11_out, button_12_out, button_13_out, button_14_out, button_15_out, button_16_out,
       button_17_out, D0, D1, D2, D3, D4, D5, D6, D7, D8, D9, D10, D11, D12, D13, D14, D15, d_ff_1_nq,
       d_ff_2_nq, d_ff_3_nq, d_ff_4_nq, d_ff_5_nq, d_ff_6_nq, d_ff_7_nq, d_ff_8_nq, d_ff_9_nq, d_ff_10_nq,
       d_ff_11_nq, d_ff_12_nq, d_ff_13_nq, IC13_pin9, IC14_pin9, IC16_2_nq, IC16_nq, IC17_2_nq, IC17_nq,
       nand_1_out, nand_2_out, nand_3_out, nand_5_out, nand_6_out, nand_7_out, nand_8_out, nand_9_out,
       nand_11_out, pullup_1_out, RCLK, RES, xor_1_out, xor_2_out, xor_3_out;
  wire [3:0] _74163_1_pin11, _74164_1_pin3, _74164_1_pin10, _74164_2_pin3, IC13_pin4, IC13_pin15, IC14_pin4,
       IC14_pin15;
  wire [3:1] _74164_2_pin10;

  LED led_1 (.in(D15));
  _74164 _74164_1 (
    .pin1(1'b1), .pin2(Fout), .pin3(_74164_1_pin3[3]), .pin4(_74164_1_pin3[2]), .pin5(_74164_1_pin3[1]),
    .pin6(_74164_1_pin3[0]), .pin7(1'b0), .pin8(clk), .pin9(RES), .pin10(_74164_1_pin10[3]),
    .pin11(_74164_1_pin10[2]), .pin12(_74164_1_pin10[1]), .pin13(_74164_1_pin10[0]), .pin14(1'b1));
  LED led_2 (.in(D14));
  D_FF IC17 (.D(IC17_nq), .C(button_1_out), .Q(D15), .nQ(IC17_nq));
  Button button_1 (.out(button_1_out));
  LED led_3 (.in(D13));
  D_FF d_ff_1 (.D(d_ff_1_nq), .C(button_2_out), .Q(D14), .nQ(d_ff_1_nq));
  Button button_2 (.out(button_2_out));
  LED led_4 (.in(D12));
  D_FF d_ff_2 (.D(d_ff_2_nq), .C(button_3_out), .Q(D13), .nQ(d_ff_2_nq));
  Button button_3 (.out(button_3_out));
  Seven_Seg_Hex seven_seg_hex_1 (.d(_74164_1_pin3), .dp(1'b0));
  LED led_5 (.in(D11));
  D_FF d_ff_3 (.D(d_ff_3_nq), .C(button_4_out), .Q(D12), .nQ(d_ff_3_nq));
  Button button_4 (.out(button_4_out));
  Seven_Seg_Hex seven_seg_hex_2 (.d(_74164_1_pin10), .dp(1'b0));
  LED led_6 (.in(D10));
  D_FF d_ff_4 (.D(d_ff_4_nq), .C(button_5_out), .Q(D11), .nQ(d_ff_4_nq));
  Button button_5 (.out(button_5_out));
  Seven_Seg_Hex seven_seg_hex_3 (.d(_74164_2_pin3), .dp(1'b0));
  _74151 _74151_1 (
    .pin1(D11), .pin2(D10), .pin3(D9), .pin4(D8), .pin5(_74151_1_pin5), .pin7(1'b0), .pin8(1'b0),
    .pin9(_74163_1_pin11[2]), .pin10(_74163_1_pin11[1]), .pin11(_74163_1_pin11[0]), .pin12(D15), .pin13(D14),
    .pin14(D13), .pin15(D12), .pin16(1'b1));  // open: pin6
  LED led_7 (.in(D9));
  D_FF d_ff_5 (.D(d_ff_5_nq), .C(button_6_out), .Q(D10), .nQ(d_ff_5_nq));
  Button button_6 (.out(button_6_out));
  LED led_8 (.in(D8));
  D_FF d_ff_6 (.D(d_ff_6_nq), .C(button_7_out), .Q(D9), .nQ(d_ff_6_nq));
  Button button_7 (.out(button_7_out));
  Seven_Seg_Hex seven_seg_hex_4 (.d({_74164_2_pin10, Aout}), .dp(1'b0));
  _74164 _74164_2 (
    .pin1(1'b1), .pin2(_74164_1_pin10[0]), .pin3(_74164_2_pin3[3]), .pin4(_74164_2_pin3[2]),
    .pin5(_74164_2_pin3[1]), .pin6(_74164_2_pin3[0]), .pin7(1'b0), .pin8(clk), .pin9(RES),
    .pin10(_74164_2_pin10[3]), .pin11(_74164_2_pin10[2]), .pin12(_74164_2_pin10[1]), .pin13(Aout),
    .pin14(1'b1));
  D_FF IC17_2 (.D(IC17_2_nq), .C(button_8_out), .Q(D8), .nQ(IC17_2_nq));
  Button button_8 (.out(button_8_out));
  Seven_Seg_Hex seven_seg_hex_5 (.d({D15, D14, D13, D12}), .dp(1'b0));
  Seven_Seg_Hex seven_seg_hex_6 (.d({D11, D10, D9, D8}), .dp(1'b0));
  LED led_9 (.in(D7));
  D_FF IC16 (.D(IC16_nq), .C(button_9_out), .Q(D7), .nQ(IC16_nq));
  Button button_9 (.out(button_9_out));
  LED led_10 (.in(D6));
  D_FF d_ff_7 (.D(d_ff_7_nq), .C(button_10_out), .Q(D6), .nQ(d_ff_7_nq));
  Button button_10 (.out(button_10_out));
  LED led_11 (.in(D5));
  D_FF d_ff_8 (.D(d_ff_8_nq), .C(button_11_out), .Q(D5), .nQ(d_ff_8_nq));
  Button button_11 (.out(button_11_out));
  LED led_12 (.in(D4));
  D_FF d_ff_9 (.D(d_ff_9_nq), .C(button_12_out), .Q(D4), .nQ(d_ff_9_nq));
  Button button_12 (.out(button_12_out));
  LED led_13 (.in(D3));
  D_FF d_ff_10 (.D(d_ff_10_nq), .C(button_13_out), .Q(D3), .nQ(d_ff_10_nq));
  Button button_13 (.out(button_13_out));
  LED led_14 (.in(D2));
  D_FF d_ff_11 (.D(d_ff_11_nq), .C(button_14_out), .Q(D2), .nQ(d_ff_11_nq));
  Button button_14 (.out(button_14_out));
  _74163 _74163_1 (
    .pin1(RES), .pin2(clk), .pin3(1'b0), .pin4(1'b0), .pin5(1'b0), .pin6(1'b0), .pin7(1'b1), .pin8(1'b0),
    .pin9(1'b1), .pin10(1'b1), .pin11(_74163_1_pin11[3]), .pin12(_74163_1_pin11[2]),
    .pin13(_74163_1_pin11[1]), .pin14(_74163_1_pin11[0]), .pin15(_74163_1_pin15), .pin16(1'b1));
  _74151 _74151_2 (
    .pin1(D3), .pin2(D2), .pin3(D1), .pin4(D0), .pin5(_74151_2_pin5), .pin7(1'b0), .pin8(1'b0),
    .pin9(_74163_1_pin11[2]), .pin10(_74163_1_pin11[1]), .pin11(_74163_1_pin11[0]), .pin12(D7), .pin13(D6),
    .pin14(D5), .pin15(D4), .pin16(1'b1));  // open: pin6
  LED led_15 (.in(D1));
  D_FF d_ff_12 (.D(d_ff_12_nq), .C(button_15_out), .Q(D1), .nQ(d_ff_12_nq));
  Button button_15 (.out(button_15_out));
  LED led_16 (.in(D0));
  D_FF IC16_2 (.D(IC16_2_nq), .C(button_16_out), .Q(D0), .nQ(IC16_2_nq));
  Button button_16 (.out(button_16_out));
  not not_1 (RCLK, _74163_1_pin15);
  LED led_17 (.in(_74163_1_pin15));
  Seven_Seg_Hex seven_seg_hex_7 (.d({D7, D6, D5, D4}), .dp(1'b0));
  Seven_Seg_Hex seven_seg_hex_8 (.d({D3, D2, D1, D0}), .dp(1'b0));
  Seven_Seg_Hex seven_seg_hex_9 (.d(_74163_1_pin11), .dp(1'b0));
  nand nand_1 (nand_1_out, _74163_1_pin11[3], _74163_1_pin11[3]);
  nand nand_2 (nand_2_out, nand_1_out, _74151_2_pin5);
  nand nand_3 (nand_3_out, _74151_1_pin5, _74163_1_pin11[3]);
  LED led_18 (.in(RES));
  D_FF d_ff_13 (.D(d_ff_13_nq), .C(button_17_out), .Q(RES), .nQ(d_ff_13_nq));
  Button button_17 (.out(button_17_out));
  nand nand_4 (Bout, nand_2_out, nand_3_out);
  LED led_19 (.in(IC13_pin15[3]));
  _74595 IC13 (
    .pin1(IC13_pin15[2]), .pin2(IC13_pin15[1]), .pin3(IC13_pin15[0]), .pin4(IC13_pin4[3]),
    .pin5(IC13_pin4[2]), .pin6(IC13_pin4[1]), .pin7(IC13_pin4[0]), .pin8(1'b0), .pin9(IC13_pin9),
    .pin10(RES), .pin11(clk), .pin12(RCLK), .pin13(1'b0), .pin14(Fout), .pin15(IC13_pin15[3]), .pin16(1'b1));
  LED led_20 (.in(IC13_pin15[1]));
  LED led_21 (.in(IC13_pin15[2]));
  LED led_22 (.in(Bout));
  LED led_23 (.in(IC13_pin4[3]));
  LED led_24 (.in(IC13_pin15[0]));
  LED led_25 (.in(Aout));
  LED led_26 (.in(IC13_pin4[1]));
  LED led_27 (.in(IC13_pin4[2]));
  LED led_28 (.in(IC13_pin4[0]));
  LED led_29 (.in(IC14_pin15[3]));
  xor xor_1 (xor_1_out, Aout, Bout);
  _74595 IC14 (
    .pin1(IC14_pin15[2]), .pin2(IC14_pin15[1]), .pin3(IC14_pin15[0]), .pin4(IC14_pin4[3]),
    .pin5(IC14_pin4[2]), .pin6(IC14_pin4[1]), .pin7(IC14_pin4[0]), .pin8(1'b0), .pin9(IC14_pin9),
    .pin10(RES), .pin11(clk), .pin12(RCLK), .pin13(1'b0), .pin14(IC13_pin9), .pin15(IC14_pin15[3]),
    .pin16(1'b1));
  LED led_30 (.in(IC14_pin15[1]));
  LED led_31 (.in(IC14_pin15[2]));
  LED led_32 (.in(IC14_pin4[3]));
  LED led_33 (.in(IC14_pin15[0]));
  nand nand_5 (nand_5_out, SUM, I0);
  nand nand_6 (nand_6_out, I1, Cout);
  nand nand_7 (nand_7_out, I1, I1);
  xor xor_2 (xor_2_out, xor_1_out, nADD);
  xor xor_3 (xor_3_out, nADD, Aout);
  LED led_34 (.in(IC14_pin4[1]));
  LED led_35 (.in(IC14_pin4[2]));
  xor xor_4 (SUM, xor_1_out, Cb_2);
  nand nand_8 (nand_8_out, Cb_2, xor_2_out);
  nand nand_9 (nand_9_out, Bout, xor_3_out);
  LED led_36 (.in(Aout));
  LED led_37 (.in(IC14_pin9));
  LED led_38 (.in(IC14_pin4[0]));
  nand nand_10 (Fout, nand_5_out, nand_6_out);
  nand nand_11 (nand_11_out, nand_7_out, Cout);
  Seven_Seg_Hex seven_seg_hex_10 (.d(IC13_pin15), .dp(1'b0));
  nand nand_12 (Cout, nand_8_out, nand_9_out);
  Seven_Seg_Hex seven_seg_hex_11 (.d(IC13_pin4), .dp(1'b0));
  PullUp pullup_1 (.out(pullup_1_out));
  D_FF_AS d_ff_as_1 (.Set(~RES), .D(nand_11_out), .C(clk), .Clr(~pullup_1_out), .nQ(Cb_2));  // open: Q
  Seven_Seg_Hex seven_seg_hex_12 (.d(IC14_pin15), .dp(1'b0));
  Seven_Seg_Hex seven_seg_hex_13 (.d(IC14_pin4), .dp(1'b0));

  assign Cout_2 = Cout;
  assign SUM_2 = SUM;

  // Notes on the sheet:
  //   clk: Hz: 16
  //   16 bit Shift Register
  //   ENTER H
  //   ACCUMULATOR
  //   ENTER L
  //   4-bit Counter
  //   High/Low Select
  //   # Clock
  //   RESET
  //   Output Display Registers
  //   Full Adder/Subtractor
  //   Bit Serial ALU
  //   1
  //   Output MUX
  //   Carry Suppress
  //   4
  //   3
  //   A
  //   2
  //   Carry FF
endmodule
