// Digital circuit testbed20.dig as structural Verilog
module testbed20 (
  input  clk,
  input  I0,
  input  I1,
  input  INV_A,
  input  INV_B,
  input  SC,
  output GCLK,
  output Fout
);

  wire _74165_1_pin9, Aout, Bout, button_1_out, button_2_out, button_3_out, button_4_out, button_5_out,
       button_6_out, button_7_out, button_8_out, button_9_out, button_10_out, button_11_out, button_12_out,
       button_13_out, button_14_out, button_15_out, button_16_out, button_17_out, button_18_out, Cin, CLR,
       Cout, D0, D1, D2, D3, D4, D5, D6, D7, D8, D9, D10, D11, D12, D13, D14, D15, d_ff_1_nq, d_ff_2_nq,
       d_ff_3_nq, d_ff_4_nq, d_ff_5_nq, d_ff_6_nq, d_ff_7_nq, d_ff_8_nq, d_ff_9_nq, d_ff_10_nq, d_ff_11_nq,
       d_ff_12_nq, IC16_2_nq, IC16_nq, IC17_2_nq, IC17_nq, LD, monoflop_1_nq, monoflop_2_q, nand_1_out,
       nand_2_out, nand_5_out, nand_6_out, nand_7_out, nand_8_out, nand_9_out, nand_10_out, nand_11_out,
       nand_14_out, pullup_1_out, RCLK, RES, RST, S0, S1, S2, S3, T0, T7, T8, T15, U17_pin9, U17_pin10,
       U17_pin11, U17_pin12, U17_pin13, U17_pin14, U17_pin15, U19_pin9, U19_pin10, U19_pin11, U19_pin12,
       U19_pin13, U19_pin14, xor_1_out, xor_2_out, xor_3_out, xor_4_out;
  wire [3:0] _74161_1_pin11, _74164_1_pin6, _74164_1_pin13, _74164_2_pin6;
  wire [3:1] _74164_2_pin10;

  LED led_1 (.in(D15));
  LED led_2 (.in(D14));
  D_FF IC17 (.D(IC17_nq), .C(button_1_out), .Q(D15), .nQ(IC17_nq));
  Button button_1 (.out(button_1_out));
  LED led_3 (.in(D13));
  D_FF d_ff_1 (.D(d_ff_1_nq), .C(button_2_out), .Q(D14), .nQ(d_ff_1_nq));
  Button button_2 (.out(button_2_out));
  LED led_4 (.in(D12));
  D_FF d_ff_2 (.D(d_ff_2_nq), .C(button_3_out), .Q(D13), .nQ(d_ff_2_nq));
  Button button_3 (.out(button_3_out));
  LED led_5 (.in(D11));
  D_FF d_ff_3 (.D(d_ff_3_nq), .C(button_4_out), .Q(D12), .nQ(d_ff_3_nq));
  Button button_4 (.out(button_4_out));
  _74161 _74161_1 (
    .pin1(RST), .pin2(clk), .pin3(1'b0), .pin4(1'b0), .pin5(1'b0), .pin6(1'b0), .pin7(1'b1), .pin8(1'b0),
    .pin9(1'b1), .pin10(1'b1), .pin11(_74161_1_pin11[3]), .pin12(_74161_1_pin11[2]),
    .pin13(_74161_1_pin11[1]), .pin14(_74161_1_pin11[0]), .pin15(RCLK), .pin16(1'b1));
  _74165 _74165_1 (
    .pin1(LD), .pin2(GCLK), .pin3(D11), .pin4(D10), .pin5(D9), .pin6(D8), .pin8(1'b0), .pin9(_74165_1_pin9),
    .pin10(1'b0), .pin11(D15), .pin12(D14), .pin13(D13), .pin14(D12), .pin15(1'b0), .pin16(1'b1));  // open: pin7
  LED led_6 (.in(D10));
  D_FF d_ff_4 (.D(d_ff_4_nq), .C(button_5_out), .Q(D11), .nQ(d_ff_4_nq));
  Button button_5 (.out(button_5_out));
  LED led_7 (.in(D9));
  D_FF d_ff_5 (.D(d_ff_5_nq), .C(button_6_out), .Q(D10), .nQ(d_ff_5_nq));
  Button button_6 (.out(button_6_out));
  LED led_8 (.in(D8));
  D_FF d_ff_6 (.D(d_ff_6_nq), .C(button_7_out), .Q(D9), .nQ(d_ff_6_nq));
  Button button_7 (.out(button_7_out));
  D_FF IC17_2 (.D(IC17_2_nq), .C(button_8_out), .Q(D8), .nQ(IC17_2_nq));
  Button button_8 (.out(button_8_out));
  nand nand_1 (nand_1_out, _74161_1_pin11[0], _74161_1_pin11[1], _74161_1_pin11[2], _74161_1_pin11[3]);
  Seven_Seg_Hex seven_seg_hex_1 (.d({D15, D14, D13, D12}), .dp(1'b0));
  Seven_Seg_Hex seven_seg_hex_2 (.d(_74161_1_pin11), .dp(1'b0));
  _74165 _74165_2 (
    .pin1(LD), .pin2(GCLK), .pin3(D3), .pin4(D2), .pin5(D1), .pin6(D0), .pin8(1'b0), .pin9(Bout),
    .pin10(_74165_1_pin9), .pin11(D7), .pin12(D6), .pin13(D5), .pin14(D4), .pin15(1'b0), .pin16(1'b1));  // open: pin7
  Seven_Seg_Hex seven_seg_hex_3 (.d({D11, D10, D9, D8}), .dp(1'b0));
  nand nand_2 (nand_2_out, clk, clk);
  Monoflop monoflop_1 (.C(nand_1_out), .R(1'b0), .nQ(monoflop_1_nq));  // open: Q
  LED led_9 (.in(D7));
  D_FF IC16 (.D(IC16_nq), .C(button_9_out), .Q(D7), .nQ(IC16_nq));
  Button button_9 (.out(button_9_out));
  nand nand_3 (GCLK, nand_2_out, RST);
  nand nand_4 (RST, RES, nand_5_out);
  nand nand_5 (nand_5_out, RST, T0);
  LED led_10 (.in(D6));
  D_FF d_ff_7 (.D(d_ff_7_nq), .C(button_10_out), .Q(D6), .nQ(d_ff_7_nq));
  Button button_10 (.out(button_10_out));
  LED led_11 (.in(D5));
  D_FF d_ff_8 (.D(d_ff_8_nq), .C(button_11_out), .Q(D5), .nQ(d_ff_8_nq));
  Button button_11 (.out(button_11_out));
  LED led_12 (.in(D4));
  D_FF d_ff_9 (.D(d_ff_9_nq), .C(button_12_out), .Q(D4), .nQ(d_ff_9_nq));
  Button button_12 (.out(button_12_out));
  LED led_13 (.in(D3));
  D_FF d_ff_10 (.D(d_ff_10_nq), .C(button_13_out), .Q(D3), .nQ(d_ff_10_nq));
  Button button_13 (.out(button_13_out));
  LED led_14 (.in(D2));
  D_FF d_ff_11 (.D(d_ff_11_nq), .C(button_14_out), .Q(D2), .nQ(d_ff_11_nq));
  Button button_14 (.out(button_14_out));
  LED led_15 (.in(D1));
  D_FF d_ff_12 (.D(d_ff_12_nq), .C(button_15_out), .Q(D1), .nQ(d_ff_12_nq));
  Button button_15 (.out(button_15_out));
  _74164 _74164_1 (
    .pin1(1'b1), .pin2(Fout), .pin3(_74164_1_pin6[3]), .pin4(_74164_1_pin6[2]), .pin5(_74164_1_pin6[1]),
    .pin6(_74164_1_pin6[0]), .pin7(1'b0), .pin8(GCLK), .pin9(CLR), .pin10(_74164_1_pin13[3]),
    .pin11(_74164_1_pin13[2]), .pin12(_74164_1_pin13[1]), .pin13(_74164_1_pin13[0]), .pin14(1'b1));
  LED led_16 (.in(D0));
  D_FF IC16_2 (.D(IC16_2_nq), .C(button_16_out), .Q(D0), .nQ(IC16_2_nq));
  Button button_16 (.out(button_16_out));
  Seven_Seg_Hex seven_seg_hex_4 (.d({D7, D6, D5, D4}), .dp(1'b0));
  Seven_Seg_Hex seven_seg_hex_5 (.d(_74164_1_pin6), .dp(1'b0));
  Seven_Seg_Hex seven_seg_hex_6 (.d({D3, D2, D1, D0}), .dp(1'b0));
  xor xor_1 (xor_1_out, Aout, INV_A);
  xor xor_2 (xor_2_out, INV_B, Bout);
  Seven_Seg_Hex seven_seg_hex_7 (.d(_74164_1_pin13), .dp(1'b0));
  xor xor_3 (xor_3_out, xor_1_out, xor_2_out);
  Seven_Seg_Hex seven_seg_hex_8 (.d(_74164_2_pin6), .dp(1'b0));
  Monoflop monoflop_2 (.C(button_17_out), .R(1'b0), .Q(monoflop_2_q), .nQ(LD));
  Button button_17 (.out(button_17_out));
  Seven_Seg_Hex seven_seg_hex_9 (.d({_74164_2_pin10, Aout}), .dp(1'b0));
  _74164 _74164_2 (
    .pin1(1'b1), .pin2(_74164_1_pin13[0]), .pin3(_74164_2_pin6[3]), .pin4(_74164_2_pin6[2]),
    .pin5(_74164_2_pin6[1]), .pin6(_74164_2_pin6[0]), .pin7(1'b0), .pin8(GCLK), .pin9(CLR),
    .pin10(_74164_2_pin10[3]), .pin11(_74164_2_pin10[2]), .pin12(_74164_2_pin10[1]), .pin13(Aout),
    .pin14(1'b1));
  Monoflop monoflop_3 (.C(monoflop_2_q), .R(1'b0), .nQ(RES));  // open: Q
  xor xor_4 (xor_4_out, xor_3_out, Cin);
  nand nand_6 (nand_6_out, xor_3_out, Cin);
  nand nand_7 (nand_7_out, xor_1_out, xor_2_out);
  nand nand_8 (nand_8_out, nand_6_out, nand_7_out);
  Monoflop monoflop_4 (.C(button_18_out), .R(1'b0), .nQ(CLR));  // open: Q
  Button button_18 (.out(button_18_out));
  nand nand_9 (nand_9_out, xor_4_out, I0);
  nand nand_10 (nand_10_out, I1, nand_8_out);
  nand nand_11 (nand_11_out, nand_8_out, SC);
  nand nand_12 (Fout, nand_9_out, nand_10_out);
  nand nand_13 (Cout, nand_11_out, nand_11_out);
  _74163 _74163_1 (
    .pin1(RST), .pin2(clk), .pin3(1'b0), .pin4(1'b0), .pin5(1'b0), .pin6(1'b0), .pin7(1'b1), .pin8(1'b0),
    .pin9(1'b1), .pin10(1'b1), .pin11(S3), .pin12(S2), .pin13(S1), .pin14(S0), .pin16(1'b1));  // open: pin15
  PullUp pullup_1 (.out(pullup_1_out));
  D_FF_AS d_ff_as_1 (.Set(~pullup_1_out), .D(Cout), .C(GCLK), .Clr(~pullup_1_out), .Q(Cin));  // open: nQ
  Seven_Seg_Hex seven_seg_hex_10 (.d({S3, S2, S1, S0}), .dp(1'b0));
  _74138 U17 (
    .pin1(S0), .pin2(S1), .pin3(S2), .pin4(S3), .pin5(1'b0), .pin6(1'b1), .pin7(T7), .pin8(1'b0),
    .pin9(U17_pin9), .pin10(U17_pin10), .pin11(U17_pin11), .pin12(U17_pin12), .pin13(U17_pin13),
    .pin14(U17_pin14), .pin15(U17_pin15), .pin16(1'b1));
  _74138 U19 (
    .pin1(S0), .pin2(S1), .pin3(S2), .pin4(1'b0), .pin5(1'b0), .pin6(S3), .pin7(T15), .pin8(1'b0),
    .pin9(U19_pin9), .pin10(U19_pin10), .pin11(U19_pin11), .pin12(U19_pin12), .pin13(U19_pin13),
    .pin14(U19_pin14), .pin15(T8), .pin16(1'b1));
  LED led_17 (.in(U17_pin15));
  LED led_18 (.in(U17_pin14));
  LED led_19 (.in(U17_pin13));
  LED led_20 (.in(U17_pin12));
  LED led_21 (.in(U17_pin11));
  LED led_22 (.in(U17_pin10));
  LED led_23 (.in(U17_pin9));
  LED led_24 (.in(T7));
  LED led_25 (.in(T8));
  LED led_26 (.in(U19_pin14));
  LED led_27 (.in(U19_pin13));
  LED led_28 (.in(U19_pin12));
  LED led_29 (.in(U19_pin11));
  LED led_30 (.in(U19_pin10));
  LED led_31 (.in(U19_pin9));
  LED led_32 (.in(T15));
  nand nand_14 (nand_14_out, U17_pin15, U17_pin15);
  Monoflop monoflop_5 (.C(nand_14_out), .R(1'b0), .nQ(T0));  // open: Q

  // Notes on the sheet:
  //   clk: Hz: 4
  //   ENTER H
  //   16 bit Shift Register B
  //   # Clock
  //   ENTER L
  //   16 bit Shift Register A
  //   ACCUMULATOR
  //   Four Chip Bit serial ALU
  //   LOAD
  //   RUN
  //   CLR ACC
  //   Suppress Carry
  //   Carry FF
endmodule
