// Digital circuit timing_gen.dig as structural Verilog
module timing_gen (
  input  CLK,
  input  Din,
  input  RnW,
  input  in_4,
  input  in_5,
  input  in_6,
  input  nEN,
  input  in_9,
  input  in_10,
  input  in_11,
  input  in_12,
  input  in_13,
  input  in_14,
  input  D,
  input  CLK_2,
  output out_7
);

  wire _7400_1_pin3, _7400_1_pin6, _7400_1_pin10, _74139_1_pin4, _74139_1_pin5, _74139_1_pin6, _74139_1_pin7,
       _74139_1_pin9, _74139_1_pin10, _74139_1_pin11, _74139_1_pin12, _74163_1_pin15, _74164_1_pin13,
       _74164_2_pin13, _74164_3_pin13, _74164_4_pin13, _74164_5_pin13, _74164_6_pin13, _74164_7_pin13, Aout,
       nand_1_out, nand_2_out, nand_3_out, nand_4_out, nand_5_out, nand_6_out, nand_7_out, nand_8_out,
       nand_9_out, nand_10_out, nand_11_out, nand_12_out, nand_13_out, nand_14_out, nand_15_out, nand_16_out,
       nand_17_out, nand_18_out, nEN0, nEN1, nEN2, nEN3, RES, S0, S1, S2, S3, S4, S5, S6, S7, U17_pin7,
       U17_pin9, U17_pin10, U17_pin11, U17_pin12, U17_pin13, U17_pin14, U17_pin15, U19_pin7, U19_pin9,
       U19_pin10, U19_pin11, U19_pin12, U19_pin13, U19_pin14, U19_pin15, U20_pin7, U20_pin9, U20_pin10,
       U20_pin11, U20_pin12, U20_pin13, U20_pin14, U20_pin15, U22_pin7, U22_pin9, U22_pin10, U22_pin11,
       U22_pin12, U22_pin13, U22_pin14, U22_pin15, U23_pin7, U23_pin9, U23_pin10, U23_pin11, U23_pin12,
       U23_pin13, U23_pin14, U23_pin15, U25_pin7, U25_pin9, U25_pin10, U25_pin11, U25_pin12, U25_pin13,
       U25_pin14, U25_pin15, U26_pin7, U26_pin9, U26_pin10, U26_pin11, U26_pin12, U26_pin13, U26_pin14,
       U26_pin15, U28_pin9, U28_pin10, U28_pin11, U28_pin12, U28_pin13, U28_pin14, U28_pin15, U29_pin7,
       U29_pin9, U29_pin10, U29_pin11;

  _7400 _7400_1 (
    .pin1(in_5), .pin2(in_5), .pin3(_7400_1_pin3), .pin4(_7400_1_pin3), .pin5(in_4), .pin6(_7400_1_pin6),
    .pin7(1'b0), .pin8(out_7), .pin9(_7400_1_pin6), .pin10(_7400_1_pin10), .pin11(_7400_1_pin10),
    .pin12(in_5), .pin13(in_6), .pin14(1'b1));
  nand nand_1 (nand_1_out, RnW, RnW);
  _74163 _74163_1 (
    .pin1(RES), .pin2(CLK), .pin3(1'b0), .pin4(1'b0), .pin5(1'b0), .pin6(1'b0), .pin7(1'b1), .pin8(1'b0),
    .pin9(1'b1), .pin10(1'b1), .pin11(S3), .pin12(S2), .pin13(S1), .pin14(S0), .pin15(_74163_1_pin15),
    .pin16(1'b1));
  _74163 _74163_2 (
    .pin1(RES), .pin2(CLK), .pin3(1'b0), .pin4(1'b0), .pin5(1'b0), .pin6(1'b0), .pin7(1'b1), .pin8(1'b0),
    .pin9(1'b1), .pin10(_74163_1_pin15), .pin11(S7), .pin12(S6), .pin13(S5), .pin14(S4), .pin16(1'b1));  // open: pin15
  _74138 U29 (
    .pin1(S4), .pin2(S5), .pin3(S6), .pin4(S7), .pin5(nEN), .pin6(1'b1), .pin7(U29_pin7), .pin8(1'b0),
    .pin9(U29_pin9), .pin10(U29_pin10), .pin11(U29_pin11), .pin12(nEN3), .pin13(nEN2), .pin14(nEN1),
    .pin15(nEN0), .pin16(1'b1));
  nand nand_2 (nand_2_out, Aout, RnW);
  nand nand_3 (nand_3_out, nand_1_out, Din);
  _74139 _74139_1 (
    .pin1(in_9), .pin2(in_10), .pin3(in_11), .pin4(_74139_1_pin4), .pin5(_74139_1_pin5),
    .pin6(_74139_1_pin6), .pin7(_74139_1_pin7), .pin8(1'b0), .pin9(_74139_1_pin9), .pin10(_74139_1_pin10),
    .pin11(_74139_1_pin11), .pin12(_74139_1_pin12), .pin13(in_14), .pin14(in_13), .pin15(in_12), .pin16(1'b1));
  nand nand_4 (nand_4_out, nand_2_out, nand_3_out);
  _74164 _74164_1 (
    .pin1(1'b1), .pin2(nand_4_out), .pin7(1'b0), .pin8(CLK), .pin9(RES), .pin13(_74164_1_pin13), .pin14(1'b1));  // open: pin3, pin4, pin5, pin6, pin10, pin11, pin12
  Seven_Seg_Hex seven_seg_hex_1 (.d({S7, S6, S5, S4}), .dp(1'b0));
  _74153 _74153_1 (
    .pin1(1'b0), .pin2(1'b0), .pin3(1'b0), .pin4(1'b0), .pin5(1'b0), .pin6(1'b0), .pin8(1'b0), .pin10(1'b1),
    .pin11(1'b1), .pin12(1'b1), .pin13(1'b1), .pin14(1'b1), .pin15(1'b1), .pin16(1'b1));  // open: pin7, pin9
  Seven_Seg_Hex seven_seg_hex_2 (.d({S3, S2, S1, S0}), .dp(1'b0));
  _74164 _74164_2 (
    .pin1(1'b1), .pin2(_74164_1_pin13), .pin7(1'b0), .pin8(CLK), .pin9(RES), .pin13(_74164_2_pin13),
    .pin14(1'b1));  // open: pin3, pin4, pin5, pin6, pin10, pin11, pin12
  _74164 _74164_3 (
    .pin1(1'b1), .pin2(_74164_2_pin13), .pin7(1'b0), .pin8(CLK), .pin9(RES), .pin13(_74164_3_pin13),
    .pin14(1'b1));  // open: pin3, pin4, pin5, pin6, pin10, pin11, pin12
  _74164 _74164_4 (
    .pin1(1'b1), .pin2(_74164_3_pin13), .pin7(1'b0), .pin8(CLK), .pin9(RES), .pin13(_74164_4_pin13),
    .pin14(1'b1));  // open: pin3, pin4, pin5, pin6, pin10, pin11, pin12
  _74138 U17 (
    .pin1(S0), .pin2(S1), .pin3(S2), .pin4(S3), .pin5(nEN0), .pin6(1'b1), .pin7(U17_pin7), .pin8(1'b0),
    .pin9(U17_pin9), .pin10(U17_pin10), .pin11(U17_pin11), .pin12(U17_pin12), .pin13(U17_pin13),
    .pin14(U17_pin14), .pin15(U17_pin15), .pin16(1'b1));
  _74138 U19 (
    .pin1(S0), .pin2(S1), .pin3(S2), .pin4(1'b0), .pin5(nEN0), .pin6(S3), .pin7(U19_pin7), .pin8(1'b0),
    .pin9(U19_pin9), .pin10(U19_pin10), .pin11(U19_pin11), .pin12(U19_pin12), .pin13(U19_pin13),
    .pin14(U19_pin14), .pin15(U19_pin15), .pin16(1'b1));
  _74138 U20 (
    .pin1(S0), .pin2(S1), .pin3(S2), .pin4(S3), .pin5(nEN1), .pin6(1'b1), .pin7(U20_pin7), .pin8(1'b0),
    .pin9(U20_pin9), .pin10(U20_pin10), .pin11(U20_pin11), .pin12(U20_pin12), .pin13(U20_pin13),
    .pin14(U20_pin14), .pin15(U20_pin15), .pin16(1'b1));
  _74138 U22 (
    .pin1(S0), .pin2(S1), .pin3(S2), .pin4(1'b0), .pin5(nEN1), .pin6(S3), .pin7(U22_pin7), .pin8(1'b0),
    .pin9(U22_pin9), .pin10(U22_pin10), .pin11(U22_pin11), .pin12(U22_pin12), .pin13(U22_pin13),
    .pin14(U22_pin14), .pin15(U22_pin15), .pin16(1'b1));
  _74138 U23 (
    .pin1(S0), .pin2(S1), .pin3(S2), .pin4(S3), .pin5(nEN2), .pin6(1'b1), .pin7(U23_pin7), .pin8(1'b0),
    .pin9(U23_pin9), .pin10(U23_pin10), .pin11(U23_pin11), .pin12(U23_pin12), .pin13(U23_pin13),
    .pin14(U23_pin14), .pin15(U23_pin15), .pin16(1'b1));
  _74138 U25 (
    .pin1(S0), .pin2(S1), .pin3(S2), .pin4(1'b0), .pin5(nEN2), .pin6(S3), .pin7(U25_pin7), .pin8(1'b0),
    .pin9(U25_pin9), .pin10(U25_pin10), .pin11(U25_pin11), .pin12(U25_pin12), .pin13(U25_pin13),
    .pin14(U25_pin14), .pin15(U25_pin15), .pin16(1'b1));
  _74138 U26 (
    .pin1(S0), .pin2(S1), .pin3(S2), .pin4(S3), .pin5(nEN3), .pin6(1'b1), .pin7(U26_pin7), .pin8(1'b0),
    .pin9(U26_pin9), .pin10(U26_pin10), .pin11(U26_pin11), .pin12(U26_pin12), .pin13(U26_pin13),
    .pin14(U26_pin14), .pin15(U26_pin15), .pin16(1'b1));
  _74138 U28 (
    .pin1(S0), .pin2(S1), .pin3(S2), .pin4(1'b0), .pin5(nEN3), .pin6(S3), .pin7(RES), .pin8(1'b0),
    .pin9(U28_pin9), .pin10(U28_pin10), .pin11(U28_pin11), .pin12(U28_pin12), .pin13(U28_pin13),
    .pin14(U28_pin14), .pin15(U28_pin15), .pin16(1'b1));
  _74164 _74164_5 (
    .pin1(1'b1), .pin2(_74164_4_pin13), .pin7(1'b0), .pin8(CLK), .pin9(RES), .pin13(_74164_5_pin13),
    .pin14(1'b1));  // open: pin3, pin4, pin5, pin6, pin10, pin11, pin12
  LED led_1 (.in(U17_pin15));
  LED led_2 (.in(U17_pin14));
  LED led_3 (.in(U17_pin13));
  LED led_4 (.in(U17_pin12));
  LED led_5 (.in(U17_pin11));
  LED led_6 (.in(U17_pin10));
  LED led_7 (.in(U17_pin9));
  LED led_8 (.in(U17_pin7));
  LED led_9 (.in(U19_pin15));
  LED led_10 (.in(U19_pin14));
  LED led_11 (.in(U19_pin13));
  LED led_12 (.in(U19_pin12));
  LED led_13 (.in(U19_pin11));
  LED led_14 (.in(U19_pin10));
  LED led_15 (.in(U19_pin9));
  LED led_16 (.in(U19_pin7));
  _74164 _74164_6 (
    .pin1(1'b1), .pin2(_74164_5_pin13), .pin7(1'b0), .pin8(CLK), .pin9(RES), .pin13(_74164_6_pin13),
    .pin14(1'b1));  // open: pin3, pin4, pin5, pin6, pin10, pin11, pin12
  nand nand_5 (nand_5_out, U17_pin15, nand_6_out);
  nand nand_6 (nand_6_out, nand_5_out, U17_pin13);
  nand nand_7 (nand_7_out, U19_pin15, nand_8_out);
  nand nand_8 (nand_8_out, nand_7_out, U19_pin14);
  nand nand_9 (nand_9_out, D, CLK_2);
  nand nand_10 (nand_10_out, nand_9_out, CLK_2);
  _74164 _74164_7 (
    .pin1(1'b1), .pin2(_74164_6_pin13), .pin7(1'b0), .pin8(CLK), .pin9(RES), .pin13(_74164_7_pin13),
    .pin14(1'b1));  // open: pin3, pin4, pin5, pin6, pin10, pin11, pin12
  // Probe hi on nand_5_out
  nand nand_11 (nand_11_out, nand_6_out, nand_8_out);
  nand nand_12 (nand_12_out, nand_9_out, nand_13_out);
  nand nand_13 (nand_13_out, nand_12_out, nand_10_out);
  nand nand_14 (nand_14_out, CLK_2, CLK_2);
  _74164 _74164_8 (
    .pin1(1'b1), .pin2(_74164_7_pin13), .pin7(1'b0), .pin8(CLK), .pin9(RES), .pin13(Aout), .pin14(1'b1));  // open: pin3, pin4, pin5, pin6, pin10, pin11, pin12
  // Probe Fn on nand_11_out
  nand nand_15 (nand_15_out, nand_12_out, nand_14_out);
  nand nand_16 (nand_16_out, nand_15_out, nand_14_out);
  nand nand_17 (nand_17_out, nand_15_out, nand_18_out);
  nand nand_18 (nand_18_out, nand_17_out, nand_16_out);

  // Notes on the sheet:
  //   CLK: Hz: 4
  //   7400
  //   Recirculating 64-bit shift register
  //   8-bit Counter
  //   # Clock
  //   Chain additional stages
  //   State
  //   Decoder
endmodule
